// Logisim project NC16.circ as structural Verilog: 6 circuits, main circuit main
module main (
);

  wire alu_1_carry_flag, alu_1_sign_flag, alu_1_zero_flag, and_1_out, button_1_out, clock_1_out, not_1_out;
  wire [4:0] instruction_control_1_cpu_control_bus_2;
  wire [15:0] alu_1_alu_out, decoder_1_out0, demultiplexer_1_out0, demultiplexer_1_out1, dipswitch_1_sw16,
       instruction_control_1_mem_data_out, instruction_control_1_operand, instruction_control_1_pc_data_out,
       multiplexer_1_out, multiplexer_2_out, multiplexer_3_out, registers_1_a_out, registers_1_b_out,
       registers_1_bp_out, registers_1_c_out, registers_1_d_out, registers_1_e_out, registers_1_flag_output,
       registers_1_memaddr_out, registers_1_memval_out, registers_1_output_out, registers_1_sp_out;
  wire [18:0] instruction_control_1_cpu_control_bus;

  LedBar #(.matrixcols(16)) Output_port_LED (
    .led0(registers_1_output_out[15]), .led1(registers_1_output_out[14]), .led2(registers_1_output_out[13]),
    .led3(registers_1_output_out[12]), .led4(registers_1_output_out[11]), .led5(registers_1_output_out[10]),
    .led6(registers_1_output_out[9]), .led7(registers_1_output_out[8]), .led8(registers_1_output_out[7]),
    .led9(registers_1_output_out[6]), .led10(registers_1_output_out[5]), .led11(registers_1_output_out[4]),
    .led12(registers_1_output_out[3]), .led13(registers_1_output_out[2]), .led14(registers_1_output_out[1]),
    .led15(registers_1_output_out[0]));
  DipSwitch #(.number(16)) dipswitch_1 (
    .sw1(dipswitch_1_sw16[15]), .sw2(dipswitch_1_sw16[14]), .sw3(dipswitch_1_sw16[13]),
    .sw4(dipswitch_1_sw16[12]), .sw5(dipswitch_1_sw16[11]), .sw6(dipswitch_1_sw16[10]),
    .sw7(dipswitch_1_sw16[9]), .sw8(dipswitch_1_sw16[8]), .sw9(dipswitch_1_sw16[7]),
    .sw10(dipswitch_1_sw16[6]), .sw11(dipswitch_1_sw16[5]), .sw12(dipswitch_1_sw16[4]),
    .sw13(dipswitch_1_sw16[3]), .sw14(dipswitch_1_sw16[2]), .sw15(dipswitch_1_sw16[1]),
    .sw16(dipswitch_1_sw16[0]));
  Button button_1 (.out(button_1_out));
  Clock clock_1 (.out(clock_1_out));
  and and_1 (and_1_out, clock_1_out, not_1_out);
  Decoder #(.select(4)) decoder_1 (
    .out0(decoder_1_out0[0]), .out1(decoder_1_out0[1]), .out2(decoder_1_out0[2]), .out3(decoder_1_out0[3]),
    .out4(decoder_1_out0[4]), .out5(decoder_1_out0[5]), .out6(decoder_1_out0[6]), .out7(decoder_1_out0[7]),
    .out8(decoder_1_out0[8]), .out9(decoder_1_out0[9]), .out10(decoder_1_out0[10]),
    .out11(decoder_1_out0[11]), .out12(decoder_1_out0[12]), .out13(decoder_1_out0[13]),
    .out14(decoder_1_out0[14]), .out15(decoder_1_out0[15]), .sel(instruction_control_1_cpu_control_bus[5:2]));  // open: en
  registers registers_1 (
    .reg_data_in(multiplexer_2_out), .CLK(and_1_out), .RESET(button_1_out),
    .write_reg_select(decoder_1_out0), .carry_flag(alu_1_carry_flag), .zero_flag(alu_1_zero_flag),
    .sign_flag(alu_1_sign_flag), .flag_write_sw(instruction_control_1_cpu_control_bus[18]),
    .memval_out(registers_1_memval_out), .memaddr_out(registers_1_memaddr_out), .a_out(registers_1_a_out),
    .b_out(registers_1_b_out), .c_out(registers_1_c_out), .d_out(registers_1_d_out),
    .e_out(registers_1_e_out), .bp_out(registers_1_bp_out), .sp_out(registers_1_sp_out),
    .output_out(registers_1_output_out), .flag_output(registers_1_flag_output));
  Instruction_Control instruction_control_1 (
    .mem_data_in(registers_1_memval_out), .mem_addr_in(registers_1_memaddr_out), .CLK(and_1_out),
    .pc_data_in(multiplexer_2_out), .pc_write_enable(decoder_1_out0[7]),
    .carry_flag(registers_1_flag_output[0]), .zero_flag(registers_1_flag_output[1]),
    .sign_flag(registers_1_flag_output[2]), .RESET(button_1_out),
    .mem_data_out(instruction_control_1_mem_data_out), .operand(instruction_control_1_operand),
    .pc_data_out(instruction_control_1_pc_data_out),
    .CPU_Control_BUS({instruction_control_1_cpu_control_bus[18:17], instruction_control_1_cpu_control_bus_2, instruction_control_1_cpu_control_bus[11:0]}));
  Multiplexer #(.select(4), .width(16)) multiplexer_1 (
    .in0(registers_1_a_out), .in1(registers_1_b_out), .in2(registers_1_c_out), .in3(registers_1_d_out),
    .in4(registers_1_e_out), .in5(registers_1_bp_out), .in6(registers_1_sp_out),
    .in7(instruction_control_1_operand), .in8(dipswitch_1_sw16), .in9(instruction_control_1_mem_data_out),
    .in10(instruction_control_1_pc_data_out), .in11(registers_1_memval_out), .in12(registers_1_flag_output),
    .out(multiplexer_1_out), .sel(instruction_control_1_cpu_control_bus_2[4:1]));  // open: in13, in14, in15
  Demultiplexer #(.width(16)) demultiplexer_1 (
    .out0(demultiplexer_1_out0), .out1(demultiplexer_1_out1), .in(multiplexer_1_out),
    .sel(instruction_control_1_cpu_control_bus_2[0]));
  not not_1 (not_1_out, instruction_control_1_cpu_control_bus[17]);
  Multiplexer #(.width(16)) multiplexer_2 (
    .in0(demultiplexer_1_out0), .in1(alu_1_alu_out), .out(multiplexer_2_out),
    .sel(instruction_control_1_cpu_control_bus_2[0]));
  Multiplexer #(.select(3), .width(16)) multiplexer_3 (
    .in0(registers_1_a_out), .in1(registers_1_b_out), .in2(registers_1_c_out), .in3(registers_1_d_out),
    .in4(registers_1_e_out), .in5(registers_1_bp_out), .in6(registers_1_sp_out),
    .in7(instruction_control_1_operand), .out(multiplexer_3_out),
    .sel(instruction_control_1_cpu_control_bus[11:9]));
  ALU alu_1 (
    .in1_data_in(demultiplexer_1_out1), .in2_data_in(multiplexer_3_out),
    .ALU_function_select(instruction_control_1_cpu_control_bus[8:6]), .ALU_Out(alu_1_alu_out),
    .sign_flag(alu_1_sign_flag), .zero_flag(alu_1_zero_flag), .carry_flag(alu_1_carry_flag));
endmodule

module right_shifter (
  input  [15:0] Input_bus_1,
  input  [15:0] Input_bus_2,
  output carry_out,
  output [15:0] Output_bus_1
);

  wire and_1_out, and_2_out, and_3_out, and_4_out, and_5_out, and_6_out, and_7_out, and_8_out, and_9_out,
       and_10_out, and_11_out, and_12_out, and_13_out, and_14_out, and_15_out, or_1_out, or_2_out;
  wire [14:0] PLA_1_out;
  wire [15:0] multiplexer_1_out, multiplexer_17_out, multiplexer_33_out, multiplexer_49_out,
       multiplexer_65_out, multiplexer_81_out, multiplexer_97_out, multiplexer_113_out, multiplexer_129_out,
       multiplexer_145_out, multiplexer_161_out, multiplexer_177_out, multiplexer_193_out,
       multiplexer_225_out;

  PLA #(.in_width(16), .out_width(15), .\table ("0000000000000001 000000000000001 # 1\n0000000000000010 000000000000011 # 2\n0000000000000011 000000000000111 # 3\n0000000000000100 000000000001111 # 4\n0000000000000101 000000000011111 # 5\n0000000000000110 000000000111111 # 6\n0000000000000111 000000001111111 # 7\n0000000000001000 000000011111111 # 8\n0000000000001001 000000111111111 # 9\n0000000000001010 000001111111111 # 10\n0000000000001011 000011111111111 # 11\n0000000000001100 000111111111111 # 12\n0000000000001101 001111111111111 # 13\n0000000000001110 011111111111111 # 14\n0000000000001111 111111111111111 # 15")) PLA_1 (
    .in(Input_bus_1), .out(PLA_1_out));
  and and_1 (and_1_out, Input_bus_2[0], PLA_1_out[0]);
  Multiplexer multiplexer_1 (
    .in0(Input_bus_2[0]), .in1(Input_bus_2[1]), .out(multiplexer_1_out[0]), .sel(PLA_1_out[0]));
  Multiplexer multiplexer_2 (
    .in0(Input_bus_2[1]), .in1(Input_bus_2[2]), .out(multiplexer_1_out[1]), .sel(PLA_1_out[0]));
  Multiplexer multiplexer_3 (
    .in0(Input_bus_2[2]), .in1(Input_bus_2[3]), .out(multiplexer_1_out[2]), .sel(PLA_1_out[0]));
  Multiplexer multiplexer_4 (
    .in0(Input_bus_2[3]), .in1(Input_bus_2[4]), .out(multiplexer_1_out[3]), .sel(PLA_1_out[0]));
  Multiplexer multiplexer_5 (
    .in0(Input_bus_2[4]), .in1(Input_bus_2[5]), .out(multiplexer_1_out[4]), .sel(PLA_1_out[0]));
  Multiplexer multiplexer_6 (
    .in0(Input_bus_2[5]), .in1(Input_bus_2[6]), .out(multiplexer_1_out[5]), .sel(PLA_1_out[0]));
  Multiplexer multiplexer_7 (
    .in0(Input_bus_2[6]), .in1(Input_bus_2[7]), .out(multiplexer_1_out[6]), .sel(PLA_1_out[0]));
  Multiplexer multiplexer_8 (
    .in0(Input_bus_2[7]), .in1(Input_bus_2[8]), .out(multiplexer_1_out[7]), .sel(PLA_1_out[0]));
  Multiplexer multiplexer_9 (
    .in0(Input_bus_2[8]), .in1(Input_bus_2[9]), .out(multiplexer_1_out[8]), .sel(PLA_1_out[0]));
  Multiplexer multiplexer_10 (
    .in0(Input_bus_2[9]), .in1(Input_bus_2[10]), .out(multiplexer_1_out[9]), .sel(PLA_1_out[0]));
  Multiplexer multiplexer_11 (
    .in0(Input_bus_2[10]), .in1(Input_bus_2[11]), .out(multiplexer_1_out[10]), .sel(PLA_1_out[0]));
  Multiplexer multiplexer_12 (
    .in0(Input_bus_2[11]), .in1(Input_bus_2[12]), .out(multiplexer_1_out[11]), .sel(PLA_1_out[0]));
  Multiplexer multiplexer_13 (
    .in0(Input_bus_2[12]), .in1(Input_bus_2[13]), .out(multiplexer_1_out[12]), .sel(PLA_1_out[0]));
  Multiplexer multiplexer_14 (
    .in0(Input_bus_2[13]), .in1(Input_bus_2[14]), .out(multiplexer_1_out[13]), .sel(PLA_1_out[0]));
  Multiplexer multiplexer_15 (
    .in0(Input_bus_2[14]), .in1(Input_bus_2[15]), .out(multiplexer_1_out[14]), .sel(PLA_1_out[0]));
  Multiplexer multiplexer_16 (.in0(Input_bus_2[15]), .in1(1'b0), .out(multiplexer_1_out[15]), .sel(PLA_1_out[0]));
  and and_2 (and_2_out, multiplexer_225_out[0], PLA_1_out[8]);
  Multiplexer multiplexer_17 (
    .in0(multiplexer_225_out[0]), .in1(multiplexer_225_out[1]), .out(multiplexer_17_out[0]),
    .sel(PLA_1_out[8]));
  Multiplexer multiplexer_18 (
    .in0(multiplexer_225_out[1]), .in1(multiplexer_225_out[2]), .out(multiplexer_17_out[1]),
    .sel(PLA_1_out[8]));
  Multiplexer multiplexer_19 (
    .in0(multiplexer_225_out[2]), .in1(multiplexer_225_out[3]), .out(multiplexer_17_out[2]),
    .sel(PLA_1_out[8]));
  Multiplexer multiplexer_20 (
    .in0(multiplexer_225_out[3]), .in1(multiplexer_225_out[4]), .out(multiplexer_17_out[3]),
    .sel(PLA_1_out[8]));
  Multiplexer multiplexer_21 (
    .in0(multiplexer_225_out[4]), .in1(multiplexer_225_out[5]), .out(multiplexer_17_out[4]),
    .sel(PLA_1_out[8]));
  Multiplexer multiplexer_22 (
    .in0(multiplexer_225_out[5]), .in1(multiplexer_225_out[6]), .out(multiplexer_17_out[5]),
    .sel(PLA_1_out[8]));
  Multiplexer multiplexer_23 (
    .in0(multiplexer_225_out[6]), .in1(multiplexer_225_out[7]), .out(multiplexer_17_out[6]),
    .sel(PLA_1_out[8]));
  Multiplexer multiplexer_24 (
    .in0(multiplexer_225_out[7]), .in1(multiplexer_225_out[8]), .out(multiplexer_17_out[7]),
    .sel(PLA_1_out[8]));
  Multiplexer multiplexer_25 (
    .in0(multiplexer_225_out[8]), .in1(multiplexer_225_out[9]), .out(multiplexer_17_out[8]),
    .sel(PLA_1_out[8]));
  Multiplexer multiplexer_26 (
    .in0(multiplexer_225_out[9]), .in1(multiplexer_225_out[10]), .out(multiplexer_17_out[9]),
    .sel(PLA_1_out[8]));
  Multiplexer multiplexer_27 (
    .in0(multiplexer_225_out[10]), .in1(multiplexer_225_out[11]), .out(multiplexer_17_out[10]),
    .sel(PLA_1_out[8]));
  Multiplexer multiplexer_28 (
    .in0(multiplexer_225_out[11]), .in1(multiplexer_225_out[12]), .out(multiplexer_17_out[11]),
    .sel(PLA_1_out[8]));
  Multiplexer multiplexer_29 (
    .in0(multiplexer_225_out[12]), .in1(multiplexer_225_out[13]), .out(multiplexer_17_out[12]),
    .sel(PLA_1_out[8]));
  Multiplexer multiplexer_30 (
    .in0(multiplexer_225_out[13]), .in1(multiplexer_225_out[14]), .out(multiplexer_17_out[13]),
    .sel(PLA_1_out[8]));
  Multiplexer multiplexer_31 (
    .in0(multiplexer_225_out[14]), .in1(multiplexer_225_out[15]), .out(multiplexer_17_out[14]),
    .sel(PLA_1_out[8]));
  Multiplexer multiplexer_32 (
    .in0(multiplexer_225_out[15]), .in1(1'b0), .out(multiplexer_17_out[15]), .sel(PLA_1_out[8]));
  and and_3 (and_3_out, multiplexer_1_out[0], PLA_1_out[1]);
  and and_4 (and_4_out, multiplexer_17_out[0], PLA_1_out[9]);
  Multiplexer multiplexer_33 (
    .in0(multiplexer_1_out[0]), .in1(multiplexer_1_out[1]), .out(multiplexer_33_out[0]), .sel(PLA_1_out[1]));
  Multiplexer multiplexer_34 (
    .in0(multiplexer_1_out[1]), .in1(multiplexer_1_out[2]), .out(multiplexer_33_out[1]), .sel(PLA_1_out[1]));
  Multiplexer multiplexer_35 (
    .in0(multiplexer_1_out[2]), .in1(multiplexer_1_out[3]), .out(multiplexer_33_out[2]), .sel(PLA_1_out[1]));
  Multiplexer multiplexer_36 (
    .in0(multiplexer_1_out[3]), .in1(multiplexer_1_out[4]), .out(multiplexer_33_out[3]), .sel(PLA_1_out[1]));
  Multiplexer multiplexer_37 (
    .in0(multiplexer_1_out[4]), .in1(multiplexer_1_out[5]), .out(multiplexer_33_out[4]), .sel(PLA_1_out[1]));
  Multiplexer multiplexer_38 (
    .in0(multiplexer_1_out[5]), .in1(multiplexer_1_out[6]), .out(multiplexer_33_out[5]), .sel(PLA_1_out[1]));
  Multiplexer multiplexer_39 (
    .in0(multiplexer_1_out[6]), .in1(multiplexer_1_out[7]), .out(multiplexer_33_out[6]), .sel(PLA_1_out[1]));
  Multiplexer multiplexer_40 (
    .in0(multiplexer_1_out[7]), .in1(multiplexer_1_out[8]), .out(multiplexer_33_out[7]), .sel(PLA_1_out[1]));
  Multiplexer multiplexer_41 (
    .in0(multiplexer_1_out[8]), .in1(multiplexer_1_out[9]), .out(multiplexer_33_out[8]), .sel(PLA_1_out[1]));
  Multiplexer multiplexer_42 (
    .in0(multiplexer_1_out[9]), .in1(multiplexer_1_out[10]), .out(multiplexer_33_out[9]), .sel(PLA_1_out[1]));
  Multiplexer multiplexer_43 (
    .in0(multiplexer_1_out[10]), .in1(multiplexer_1_out[11]), .out(multiplexer_33_out[10]), .sel(PLA_1_out[1]));
  Multiplexer multiplexer_44 (
    .in0(multiplexer_1_out[11]), .in1(multiplexer_1_out[12]), .out(multiplexer_33_out[11]), .sel(PLA_1_out[1]));
  Multiplexer multiplexer_45 (
    .in0(multiplexer_1_out[12]), .in1(multiplexer_1_out[13]), .out(multiplexer_33_out[12]), .sel(PLA_1_out[1]));
  Multiplexer multiplexer_46 (
    .in0(multiplexer_1_out[13]), .in1(multiplexer_1_out[14]), .out(multiplexer_33_out[13]), .sel(PLA_1_out[1]));
  Multiplexer multiplexer_47 (
    .in0(multiplexer_1_out[14]), .in1(multiplexer_1_out[15]), .out(multiplexer_33_out[14]), .sel(PLA_1_out[1]));
  Multiplexer multiplexer_48 (
    .in0(multiplexer_1_out[15]), .in1(1'b0), .out(multiplexer_33_out[15]), .sel(PLA_1_out[1]));
  Multiplexer multiplexer_49 (
    .in0(multiplexer_17_out[0]), .in1(multiplexer_17_out[1]), .out(multiplexer_49_out[0]), .sel(PLA_1_out[9]));
  Multiplexer multiplexer_50 (
    .in0(multiplexer_17_out[1]), .in1(multiplexer_17_out[2]), .out(multiplexer_49_out[1]), .sel(PLA_1_out[9]));
  Multiplexer multiplexer_51 (
    .in0(multiplexer_17_out[2]), .in1(multiplexer_17_out[3]), .out(multiplexer_49_out[2]), .sel(PLA_1_out[9]));
  Multiplexer multiplexer_52 (
    .in0(multiplexer_17_out[3]), .in1(multiplexer_17_out[4]), .out(multiplexer_49_out[3]), .sel(PLA_1_out[9]));
  Multiplexer multiplexer_53 (
    .in0(multiplexer_17_out[4]), .in1(multiplexer_17_out[5]), .out(multiplexer_49_out[4]), .sel(PLA_1_out[9]));
  Multiplexer multiplexer_54 (
    .in0(multiplexer_17_out[5]), .in1(multiplexer_17_out[6]), .out(multiplexer_49_out[5]), .sel(PLA_1_out[9]));
  Multiplexer multiplexer_55 (
    .in0(multiplexer_17_out[6]), .in1(multiplexer_17_out[7]), .out(multiplexer_49_out[6]), .sel(PLA_1_out[9]));
  Multiplexer multiplexer_56 (
    .in0(multiplexer_17_out[7]), .in1(multiplexer_17_out[8]), .out(multiplexer_49_out[7]), .sel(PLA_1_out[9]));
  Multiplexer multiplexer_57 (
    .in0(multiplexer_17_out[8]), .in1(multiplexer_17_out[9]), .out(multiplexer_49_out[8]), .sel(PLA_1_out[9]));
  Multiplexer multiplexer_58 (
    .in0(multiplexer_17_out[9]), .in1(multiplexer_17_out[10]), .out(multiplexer_49_out[9]), .sel(PLA_1_out[9]));
  Multiplexer multiplexer_59 (
    .in0(multiplexer_17_out[10]), .in1(multiplexer_17_out[11]), .out(multiplexer_49_out[10]),
    .sel(PLA_1_out[9]));
  Multiplexer multiplexer_60 (
    .in0(multiplexer_17_out[11]), .in1(multiplexer_17_out[12]), .out(multiplexer_49_out[11]),
    .sel(PLA_1_out[9]));
  Multiplexer multiplexer_61 (
    .in0(multiplexer_17_out[12]), .in1(multiplexer_17_out[13]), .out(multiplexer_49_out[12]),
    .sel(PLA_1_out[9]));
  Multiplexer multiplexer_62 (
    .in0(multiplexer_17_out[13]), .in1(multiplexer_17_out[14]), .out(multiplexer_49_out[13]),
    .sel(PLA_1_out[9]));
  Multiplexer multiplexer_63 (
    .in0(multiplexer_17_out[14]), .in1(multiplexer_17_out[15]), .out(multiplexer_49_out[14]),
    .sel(PLA_1_out[9]));
  Multiplexer multiplexer_64 (
    .in0(multiplexer_17_out[15]), .in1(1'b0), .out(multiplexer_49_out[15]), .sel(PLA_1_out[9]));
  and and_5 (and_5_out, multiplexer_33_out[0], PLA_1_out[2]);
  Multiplexer multiplexer_65 (
    .in0(multiplexer_33_out[0]), .in1(multiplexer_33_out[1]), .out(multiplexer_65_out[0]), .sel(PLA_1_out[2]));
  Multiplexer multiplexer_66 (
    .in0(multiplexer_33_out[1]), .in1(multiplexer_33_out[2]), .out(multiplexer_65_out[1]), .sel(PLA_1_out[2]));
  Multiplexer multiplexer_67 (
    .in0(multiplexer_33_out[2]), .in1(multiplexer_33_out[3]), .out(multiplexer_65_out[2]), .sel(PLA_1_out[2]));
  Multiplexer multiplexer_68 (
    .in0(multiplexer_33_out[3]), .in1(multiplexer_33_out[4]), .out(multiplexer_65_out[3]), .sel(PLA_1_out[2]));
  Multiplexer multiplexer_69 (
    .in0(multiplexer_33_out[4]), .in1(multiplexer_33_out[5]), .out(multiplexer_65_out[4]), .sel(PLA_1_out[2]));
  Multiplexer multiplexer_70 (
    .in0(multiplexer_33_out[5]), .in1(multiplexer_33_out[6]), .out(multiplexer_65_out[5]), .sel(PLA_1_out[2]));
  Multiplexer multiplexer_71 (
    .in0(multiplexer_33_out[6]), .in1(multiplexer_33_out[7]), .out(multiplexer_65_out[6]), .sel(PLA_1_out[2]));
  Multiplexer multiplexer_72 (
    .in0(multiplexer_33_out[7]), .in1(multiplexer_33_out[8]), .out(multiplexer_65_out[7]), .sel(PLA_1_out[2]));
  Multiplexer multiplexer_73 (
    .in0(multiplexer_33_out[8]), .in1(multiplexer_33_out[9]), .out(multiplexer_65_out[8]), .sel(PLA_1_out[2]));
  Multiplexer multiplexer_74 (
    .in0(multiplexer_33_out[9]), .in1(multiplexer_33_out[10]), .out(multiplexer_65_out[9]), .sel(PLA_1_out[2]));
  Multiplexer multiplexer_75 (
    .in0(multiplexer_33_out[10]), .in1(multiplexer_33_out[11]), .out(multiplexer_65_out[10]),
    .sel(PLA_1_out[2]));
  Multiplexer multiplexer_76 (
    .in0(multiplexer_33_out[11]), .in1(multiplexer_33_out[12]), .out(multiplexer_65_out[11]),
    .sel(PLA_1_out[2]));
  Multiplexer multiplexer_77 (
    .in0(multiplexer_33_out[12]), .in1(multiplexer_33_out[13]), .out(multiplexer_65_out[12]),
    .sel(PLA_1_out[2]));
  Multiplexer multiplexer_78 (
    .in0(multiplexer_33_out[13]), .in1(multiplexer_33_out[14]), .out(multiplexer_65_out[13]),
    .sel(PLA_1_out[2]));
  Multiplexer multiplexer_79 (
    .in0(multiplexer_33_out[14]), .in1(multiplexer_33_out[15]), .out(multiplexer_65_out[14]),
    .sel(PLA_1_out[2]));
  Multiplexer multiplexer_80 (
    .in0(multiplexer_33_out[15]), .in1(1'b0), .out(multiplexer_65_out[15]), .sel(PLA_1_out[2]));
  and and_6 (and_6_out, multiplexer_49_out[0], PLA_1_out[10]);
  Multiplexer multiplexer_81 (
    .in0(multiplexer_49_out[0]), .in1(multiplexer_49_out[1]), .out(multiplexer_81_out[0]), .sel(PLA_1_out[10]));
  Multiplexer multiplexer_82 (
    .in0(multiplexer_49_out[1]), .in1(multiplexer_49_out[2]), .out(multiplexer_81_out[1]), .sel(PLA_1_out[10]));
  Multiplexer multiplexer_83 (
    .in0(multiplexer_49_out[2]), .in1(multiplexer_49_out[3]), .out(multiplexer_81_out[2]), .sel(PLA_1_out[10]));
  Multiplexer multiplexer_84 (
    .in0(multiplexer_49_out[3]), .in1(multiplexer_49_out[4]), .out(multiplexer_81_out[3]), .sel(PLA_1_out[10]));
  Multiplexer multiplexer_85 (
    .in0(multiplexer_49_out[4]), .in1(multiplexer_49_out[5]), .out(multiplexer_81_out[4]), .sel(PLA_1_out[10]));
  Multiplexer multiplexer_86 (
    .in0(multiplexer_49_out[5]), .in1(multiplexer_49_out[6]), .out(multiplexer_81_out[5]), .sel(PLA_1_out[10]));
  Multiplexer multiplexer_87 (
    .in0(multiplexer_49_out[6]), .in1(multiplexer_49_out[7]), .out(multiplexer_81_out[6]), .sel(PLA_1_out[10]));
  Multiplexer multiplexer_88 (
    .in0(multiplexer_49_out[7]), .in1(multiplexer_49_out[8]), .out(multiplexer_81_out[7]), .sel(PLA_1_out[10]));
  Multiplexer multiplexer_89 (
    .in0(multiplexer_49_out[8]), .in1(multiplexer_49_out[9]), .out(multiplexer_81_out[8]), .sel(PLA_1_out[10]));
  Multiplexer multiplexer_90 (
    .in0(multiplexer_49_out[9]), .in1(multiplexer_49_out[10]), .out(multiplexer_81_out[9]),
    .sel(PLA_1_out[10]));
  Multiplexer multiplexer_91 (
    .in0(multiplexer_49_out[10]), .in1(multiplexer_49_out[11]), .out(multiplexer_81_out[10]),
    .sel(PLA_1_out[10]));
  Multiplexer multiplexer_92 (
    .in0(multiplexer_49_out[11]), .in1(multiplexer_49_out[12]), .out(multiplexer_81_out[11]),
    .sel(PLA_1_out[10]));
  Multiplexer multiplexer_93 (
    .in0(multiplexer_49_out[12]), .in1(multiplexer_49_out[13]), .out(multiplexer_81_out[12]),
    .sel(PLA_1_out[10]));
  Multiplexer multiplexer_94 (
    .in0(multiplexer_49_out[13]), .in1(multiplexer_49_out[14]), .out(multiplexer_81_out[13]),
    .sel(PLA_1_out[10]));
  Multiplexer multiplexer_95 (
    .in0(multiplexer_49_out[14]), .in1(multiplexer_49_out[15]), .out(multiplexer_81_out[14]),
    .sel(PLA_1_out[10]));
  Multiplexer multiplexer_96 (
    .in0(multiplexer_49_out[15]), .in1(1'b0), .out(multiplexer_81_out[15]), .sel(PLA_1_out[10]));
  and and_7 (and_7_out, multiplexer_65_out[0], PLA_1_out[3]);
  Multiplexer multiplexer_97 (
    .in0(multiplexer_65_out[0]), .in1(multiplexer_65_out[1]), .out(multiplexer_97_out[0]), .sel(PLA_1_out[3]));
  Multiplexer multiplexer_98 (
    .in0(multiplexer_65_out[1]), .in1(multiplexer_65_out[2]), .out(multiplexer_97_out[1]), .sel(PLA_1_out[3]));
  Multiplexer multiplexer_99 (
    .in0(multiplexer_65_out[2]), .in1(multiplexer_65_out[3]), .out(multiplexer_97_out[2]), .sel(PLA_1_out[3]));
  Multiplexer multiplexer_100 (
    .in0(multiplexer_65_out[3]), .in1(multiplexer_65_out[4]), .out(multiplexer_97_out[3]), .sel(PLA_1_out[3]));
  Multiplexer multiplexer_101 (
    .in0(multiplexer_65_out[4]), .in1(multiplexer_65_out[5]), .out(multiplexer_97_out[4]), .sel(PLA_1_out[3]));
  Multiplexer multiplexer_102 (
    .in0(multiplexer_65_out[5]), .in1(multiplexer_65_out[6]), .out(multiplexer_97_out[5]), .sel(PLA_1_out[3]));
  Multiplexer multiplexer_103 (
    .in0(multiplexer_65_out[6]), .in1(multiplexer_65_out[7]), .out(multiplexer_97_out[6]), .sel(PLA_1_out[3]));
  Multiplexer multiplexer_104 (
    .in0(multiplexer_65_out[7]), .in1(multiplexer_65_out[8]), .out(multiplexer_97_out[7]), .sel(PLA_1_out[3]));
  Multiplexer multiplexer_105 (
    .in0(multiplexer_65_out[8]), .in1(multiplexer_65_out[9]), .out(multiplexer_97_out[8]), .sel(PLA_1_out[3]));
  Multiplexer multiplexer_106 (
    .in0(multiplexer_65_out[9]), .in1(multiplexer_65_out[10]), .out(multiplexer_97_out[9]), .sel(PLA_1_out[3]));
  Multiplexer multiplexer_107 (
    .in0(multiplexer_65_out[10]), .in1(multiplexer_65_out[11]), .out(multiplexer_97_out[10]),
    .sel(PLA_1_out[3]));
  Multiplexer multiplexer_108 (
    .in0(multiplexer_65_out[11]), .in1(multiplexer_65_out[12]), .out(multiplexer_97_out[11]),
    .sel(PLA_1_out[3]));
  Multiplexer multiplexer_109 (
    .in0(multiplexer_65_out[12]), .in1(multiplexer_65_out[13]), .out(multiplexer_97_out[12]),
    .sel(PLA_1_out[3]));
  Multiplexer multiplexer_110 (
    .in0(multiplexer_65_out[13]), .in1(multiplexer_65_out[14]), .out(multiplexer_97_out[13]),
    .sel(PLA_1_out[3]));
  Multiplexer multiplexer_111 (
    .in0(multiplexer_65_out[14]), .in1(multiplexer_65_out[15]), .out(multiplexer_97_out[14]),
    .sel(PLA_1_out[3]));
  Multiplexer multiplexer_112 (
    .in0(multiplexer_65_out[15]), .in1(1'b0), .out(multiplexer_97_out[15]), .sel(PLA_1_out[3]));
  and and_8 (and_8_out, multiplexer_81_out[0], PLA_1_out[11]);
  Multiplexer multiplexer_113 (
    .in0(multiplexer_81_out[0]), .in1(multiplexer_81_out[1]), .out(multiplexer_113_out[0]),
    .sel(PLA_1_out[11]));
  Multiplexer multiplexer_114 (
    .in0(multiplexer_81_out[1]), .in1(multiplexer_81_out[2]), .out(multiplexer_113_out[1]),
    .sel(PLA_1_out[11]));
  Multiplexer multiplexer_115 (
    .in0(multiplexer_81_out[2]), .in1(multiplexer_81_out[3]), .out(multiplexer_113_out[2]),
    .sel(PLA_1_out[11]));
  Multiplexer multiplexer_116 (
    .in0(multiplexer_81_out[3]), .in1(multiplexer_81_out[4]), .out(multiplexer_113_out[3]),
    .sel(PLA_1_out[11]));
  Multiplexer multiplexer_117 (
    .in0(multiplexer_81_out[4]), .in1(multiplexer_81_out[5]), .out(multiplexer_113_out[4]),
    .sel(PLA_1_out[11]));
  Multiplexer multiplexer_118 (
    .in0(multiplexer_81_out[5]), .in1(multiplexer_81_out[6]), .out(multiplexer_113_out[5]),
    .sel(PLA_1_out[11]));
  Multiplexer multiplexer_119 (
    .in0(multiplexer_81_out[6]), .in1(multiplexer_81_out[7]), .out(multiplexer_113_out[6]),
    .sel(PLA_1_out[11]));
  Multiplexer multiplexer_120 (
    .in0(multiplexer_81_out[7]), .in1(multiplexer_81_out[8]), .out(multiplexer_113_out[7]),
    .sel(PLA_1_out[11]));
  Multiplexer multiplexer_121 (
    .in0(multiplexer_81_out[8]), .in1(multiplexer_81_out[9]), .out(multiplexer_113_out[8]),
    .sel(PLA_1_out[11]));
  Multiplexer multiplexer_122 (
    .in0(multiplexer_81_out[9]), .in1(multiplexer_81_out[10]), .out(multiplexer_113_out[9]),
    .sel(PLA_1_out[11]));
  Multiplexer multiplexer_123 (
    .in0(multiplexer_81_out[10]), .in1(multiplexer_81_out[11]), .out(multiplexer_113_out[10]),
    .sel(PLA_1_out[11]));
  Multiplexer multiplexer_124 (
    .in0(multiplexer_81_out[11]), .in1(multiplexer_81_out[12]), .out(multiplexer_113_out[11]),
    .sel(PLA_1_out[11]));
  Multiplexer multiplexer_125 (
    .in0(multiplexer_81_out[12]), .in1(multiplexer_81_out[13]), .out(multiplexer_113_out[12]),
    .sel(PLA_1_out[11]));
  Multiplexer multiplexer_126 (
    .in0(multiplexer_81_out[13]), .in1(multiplexer_81_out[14]), .out(multiplexer_113_out[13]),
    .sel(PLA_1_out[11]));
  Multiplexer multiplexer_127 (
    .in0(multiplexer_81_out[14]), .in1(multiplexer_81_out[15]), .out(multiplexer_113_out[14]),
    .sel(PLA_1_out[11]));
  Multiplexer multiplexer_128 (
    .in0(multiplexer_81_out[15]), .in1(1'b0), .out(multiplexer_113_out[15]), .sel(PLA_1_out[11]));
  and and_9 (and_9_out, multiplexer_97_out[0], PLA_1_out[4]);
  Multiplexer multiplexer_129 (
    .in0(multiplexer_97_out[0]), .in1(multiplexer_97_out[1]), .out(multiplexer_129_out[0]), .sel(PLA_1_out[4]));
  Multiplexer multiplexer_130 (
    .in0(multiplexer_97_out[1]), .in1(multiplexer_97_out[2]), .out(multiplexer_129_out[1]), .sel(PLA_1_out[4]));
  Multiplexer multiplexer_131 (
    .in0(multiplexer_97_out[2]), .in1(multiplexer_97_out[3]), .out(multiplexer_129_out[2]), .sel(PLA_1_out[4]));
  Multiplexer multiplexer_132 (
    .in0(multiplexer_97_out[3]), .in1(multiplexer_97_out[4]), .out(multiplexer_129_out[3]), .sel(PLA_1_out[4]));
  Multiplexer multiplexer_133 (
    .in0(multiplexer_97_out[4]), .in1(multiplexer_97_out[5]), .out(multiplexer_129_out[4]), .sel(PLA_1_out[4]));
  Multiplexer multiplexer_134 (
    .in0(multiplexer_97_out[5]), .in1(multiplexer_97_out[6]), .out(multiplexer_129_out[5]), .sel(PLA_1_out[4]));
  Multiplexer multiplexer_135 (
    .in0(multiplexer_97_out[6]), .in1(multiplexer_97_out[7]), .out(multiplexer_129_out[6]), .sel(PLA_1_out[4]));
  Multiplexer multiplexer_136 (
    .in0(multiplexer_97_out[7]), .in1(multiplexer_97_out[8]), .out(multiplexer_129_out[7]), .sel(PLA_1_out[4]));
  Multiplexer multiplexer_137 (
    .in0(multiplexer_97_out[8]), .in1(multiplexer_97_out[9]), .out(multiplexer_129_out[8]), .sel(PLA_1_out[4]));
  Multiplexer multiplexer_138 (
    .in0(multiplexer_97_out[9]), .in1(multiplexer_97_out[10]), .out(multiplexer_129_out[9]),
    .sel(PLA_1_out[4]));
  Multiplexer multiplexer_139 (
    .in0(multiplexer_97_out[10]), .in1(multiplexer_97_out[11]), .out(multiplexer_129_out[10]),
    .sel(PLA_1_out[4]));
  Multiplexer multiplexer_140 (
    .in0(multiplexer_97_out[11]), .in1(multiplexer_97_out[12]), .out(multiplexer_129_out[11]),
    .sel(PLA_1_out[4]));
  Multiplexer multiplexer_141 (
    .in0(multiplexer_97_out[12]), .in1(multiplexer_97_out[13]), .out(multiplexer_129_out[12]),
    .sel(PLA_1_out[4]));
  Multiplexer multiplexer_142 (
    .in0(multiplexer_97_out[13]), .in1(multiplexer_97_out[14]), .out(multiplexer_129_out[13]),
    .sel(PLA_1_out[4]));
  Multiplexer multiplexer_143 (
    .in0(multiplexer_97_out[14]), .in1(multiplexer_97_out[15]), .out(multiplexer_129_out[14]),
    .sel(PLA_1_out[4]));
  Multiplexer multiplexer_144 (
    .in0(multiplexer_97_out[15]), .in1(1'b0), .out(multiplexer_129_out[15]), .sel(PLA_1_out[4]));
  and and_10 (and_10_out, multiplexer_113_out[0], PLA_1_out[12]);
  Multiplexer multiplexer_145 (
    .in0(multiplexer_113_out[0]), .in1(multiplexer_113_out[1]), .out(multiplexer_145_out[0]),
    .sel(PLA_1_out[12]));
  Multiplexer multiplexer_146 (
    .in0(multiplexer_113_out[1]), .in1(multiplexer_113_out[2]), .out(multiplexer_145_out[1]),
    .sel(PLA_1_out[12]));
  Multiplexer multiplexer_147 (
    .in0(multiplexer_113_out[2]), .in1(multiplexer_113_out[3]), .out(multiplexer_145_out[2]),
    .sel(PLA_1_out[12]));
  Multiplexer multiplexer_148 (
    .in0(multiplexer_113_out[3]), .in1(multiplexer_113_out[4]), .out(multiplexer_145_out[3]),
    .sel(PLA_1_out[12]));
  Multiplexer multiplexer_149 (
    .in0(multiplexer_113_out[4]), .in1(multiplexer_113_out[5]), .out(multiplexer_145_out[4]),
    .sel(PLA_1_out[12]));
  Multiplexer multiplexer_150 (
    .in0(multiplexer_113_out[5]), .in1(multiplexer_113_out[6]), .out(multiplexer_145_out[5]),
    .sel(PLA_1_out[12]));
  Multiplexer multiplexer_151 (
    .in0(multiplexer_113_out[6]), .in1(multiplexer_113_out[7]), .out(multiplexer_145_out[6]),
    .sel(PLA_1_out[12]));
  Multiplexer multiplexer_152 (
    .in0(multiplexer_113_out[7]), .in1(multiplexer_113_out[8]), .out(multiplexer_145_out[7]),
    .sel(PLA_1_out[12]));
  Multiplexer multiplexer_153 (
    .in0(multiplexer_113_out[8]), .in1(multiplexer_113_out[9]), .out(multiplexer_145_out[8]),
    .sel(PLA_1_out[12]));
  Multiplexer multiplexer_154 (
    .in0(multiplexer_113_out[9]), .in1(multiplexer_113_out[10]), .out(multiplexer_145_out[9]),
    .sel(PLA_1_out[12]));
  Multiplexer multiplexer_155 (
    .in0(multiplexer_113_out[10]), .in1(multiplexer_113_out[11]), .out(multiplexer_145_out[10]),
    .sel(PLA_1_out[12]));
  Multiplexer multiplexer_156 (
    .in0(multiplexer_113_out[11]), .in1(multiplexer_113_out[12]), .out(multiplexer_145_out[11]),
    .sel(PLA_1_out[12]));
  Multiplexer multiplexer_157 (
    .in0(multiplexer_113_out[12]), .in1(multiplexer_113_out[13]), .out(multiplexer_145_out[12]),
    .sel(PLA_1_out[12]));
  Multiplexer multiplexer_158 (
    .in0(multiplexer_113_out[13]), .in1(multiplexer_113_out[14]), .out(multiplexer_145_out[13]),
    .sel(PLA_1_out[12]));
  Multiplexer multiplexer_159 (
    .in0(multiplexer_113_out[14]), .in1(multiplexer_113_out[15]), .out(multiplexer_145_out[14]),
    .sel(PLA_1_out[12]));
  Multiplexer multiplexer_160 (
    .in0(multiplexer_113_out[15]), .in1(1'b0), .out(multiplexer_145_out[15]), .sel(PLA_1_out[12]));
  and and_11 (and_11_out, multiplexer_129_out[0], PLA_1_out[5]);
  Multiplexer multiplexer_161 (
    .in0(multiplexer_129_out[0]), .in1(multiplexer_129_out[1]), .out(multiplexer_161_out[0]),
    .sel(PLA_1_out[5]));
  Multiplexer multiplexer_162 (
    .in0(multiplexer_129_out[1]), .in1(multiplexer_129_out[2]), .out(multiplexer_161_out[1]),
    .sel(PLA_1_out[5]));
  Multiplexer multiplexer_163 (
    .in0(multiplexer_129_out[2]), .in1(multiplexer_129_out[3]), .out(multiplexer_161_out[2]),
    .sel(PLA_1_out[5]));
  Multiplexer multiplexer_164 (
    .in0(multiplexer_129_out[3]), .in1(multiplexer_129_out[4]), .out(multiplexer_161_out[3]),
    .sel(PLA_1_out[5]));
  Multiplexer multiplexer_165 (
    .in0(multiplexer_129_out[4]), .in1(multiplexer_129_out[5]), .out(multiplexer_161_out[4]),
    .sel(PLA_1_out[5]));
  Multiplexer multiplexer_166 (
    .in0(multiplexer_129_out[5]), .in1(multiplexer_129_out[6]), .out(multiplexer_161_out[5]),
    .sel(PLA_1_out[5]));
  Multiplexer multiplexer_167 (
    .in0(multiplexer_129_out[6]), .in1(multiplexer_129_out[7]), .out(multiplexer_161_out[6]),
    .sel(PLA_1_out[5]));
  Multiplexer multiplexer_168 (
    .in0(multiplexer_129_out[7]), .in1(multiplexer_129_out[8]), .out(multiplexer_161_out[7]),
    .sel(PLA_1_out[5]));
  Multiplexer multiplexer_169 (
    .in0(multiplexer_129_out[8]), .in1(multiplexer_129_out[9]), .out(multiplexer_161_out[8]),
    .sel(PLA_1_out[5]));
  Multiplexer multiplexer_170 (
    .in0(multiplexer_129_out[9]), .in1(multiplexer_129_out[10]), .out(multiplexer_161_out[9]),
    .sel(PLA_1_out[5]));
  Multiplexer multiplexer_171 (
    .in0(multiplexer_129_out[10]), .in1(multiplexer_129_out[11]), .out(multiplexer_161_out[10]),
    .sel(PLA_1_out[5]));
  Multiplexer multiplexer_172 (
    .in0(multiplexer_129_out[11]), .in1(multiplexer_129_out[12]), .out(multiplexer_161_out[11]),
    .sel(PLA_1_out[5]));
  Multiplexer multiplexer_173 (
    .in0(multiplexer_129_out[12]), .in1(multiplexer_129_out[13]), .out(multiplexer_161_out[12]),
    .sel(PLA_1_out[5]));
  Multiplexer multiplexer_174 (
    .in0(multiplexer_129_out[13]), .in1(multiplexer_129_out[14]), .out(multiplexer_161_out[13]),
    .sel(PLA_1_out[5]));
  Multiplexer multiplexer_175 (
    .in0(multiplexer_129_out[14]), .in1(multiplexer_129_out[15]), .out(multiplexer_161_out[14]),
    .sel(PLA_1_out[5]));
  Multiplexer multiplexer_176 (
    .in0(multiplexer_129_out[15]), .in1(1'b0), .out(multiplexer_161_out[15]), .sel(PLA_1_out[5]));
  and and_12 (and_12_out, multiplexer_145_out[0], PLA_1_out[13]);
  Multiplexer multiplexer_177 (
    .in0(multiplexer_145_out[0]), .in1(multiplexer_145_out[1]), .out(multiplexer_177_out[0]),
    .sel(PLA_1_out[13]));
  Multiplexer multiplexer_178 (
    .in0(multiplexer_145_out[1]), .in1(multiplexer_145_out[2]), .out(multiplexer_177_out[1]),
    .sel(PLA_1_out[13]));
  Multiplexer multiplexer_179 (
    .in0(multiplexer_145_out[2]), .in1(multiplexer_145_out[3]), .out(multiplexer_177_out[2]),
    .sel(PLA_1_out[13]));
  Multiplexer multiplexer_180 (
    .in0(multiplexer_145_out[3]), .in1(multiplexer_145_out[4]), .out(multiplexer_177_out[3]),
    .sel(PLA_1_out[13]));
  Multiplexer multiplexer_181 (
    .in0(multiplexer_145_out[4]), .in1(multiplexer_145_out[5]), .out(multiplexer_177_out[4]),
    .sel(PLA_1_out[13]));
  Multiplexer multiplexer_182 (
    .in0(multiplexer_145_out[5]), .in1(multiplexer_145_out[6]), .out(multiplexer_177_out[5]),
    .sel(PLA_1_out[13]));
  Multiplexer multiplexer_183 (
    .in0(multiplexer_145_out[6]), .in1(multiplexer_145_out[7]), .out(multiplexer_177_out[6]),
    .sel(PLA_1_out[13]));
  Multiplexer multiplexer_184 (
    .in0(multiplexer_145_out[7]), .in1(multiplexer_145_out[8]), .out(multiplexer_177_out[7]),
    .sel(PLA_1_out[13]));
  Multiplexer multiplexer_185 (
    .in0(multiplexer_145_out[8]), .in1(multiplexer_145_out[9]), .out(multiplexer_177_out[8]),
    .sel(PLA_1_out[13]));
  Multiplexer multiplexer_186 (
    .in0(multiplexer_145_out[9]), .in1(multiplexer_145_out[10]), .out(multiplexer_177_out[9]),
    .sel(PLA_1_out[13]));
  Multiplexer multiplexer_187 (
    .in0(multiplexer_145_out[10]), .in1(multiplexer_145_out[11]), .out(multiplexer_177_out[10]),
    .sel(PLA_1_out[13]));
  Multiplexer multiplexer_188 (
    .in0(multiplexer_145_out[11]), .in1(multiplexer_145_out[12]), .out(multiplexer_177_out[11]),
    .sel(PLA_1_out[13]));
  Multiplexer multiplexer_189 (
    .in0(multiplexer_145_out[12]), .in1(multiplexer_145_out[13]), .out(multiplexer_177_out[12]),
    .sel(PLA_1_out[13]));
  Multiplexer multiplexer_190 (
    .in0(multiplexer_145_out[13]), .in1(multiplexer_145_out[14]), .out(multiplexer_177_out[13]),
    .sel(PLA_1_out[13]));
  Multiplexer multiplexer_191 (
    .in0(multiplexer_145_out[14]), .in1(multiplexer_145_out[15]), .out(multiplexer_177_out[14]),
    .sel(PLA_1_out[13]));
  Multiplexer multiplexer_192 (
    .in0(multiplexer_145_out[15]), .in1(1'b0), .out(multiplexer_177_out[15]), .sel(PLA_1_out[13]));
  and and_13 (and_13_out, multiplexer_161_out[0], PLA_1_out[6]);
  and and_14 (and_14_out, multiplexer_177_out[0], PLA_1_out[14]);
  Multiplexer multiplexer_193 (
    .in0(multiplexer_161_out[0]), .in1(multiplexer_161_out[1]), .out(multiplexer_193_out[0]),
    .sel(PLA_1_out[6]));
  Multiplexer multiplexer_194 (
    .in0(multiplexer_161_out[1]), .in1(multiplexer_161_out[2]), .out(multiplexer_193_out[1]),
    .sel(PLA_1_out[6]));
  Multiplexer multiplexer_195 (
    .in0(multiplexer_161_out[2]), .in1(multiplexer_161_out[3]), .out(multiplexer_193_out[2]),
    .sel(PLA_1_out[6]));
  Multiplexer multiplexer_196 (
    .in0(multiplexer_161_out[3]), .in1(multiplexer_161_out[4]), .out(multiplexer_193_out[3]),
    .sel(PLA_1_out[6]));
  Multiplexer multiplexer_197 (
    .in0(multiplexer_161_out[4]), .in1(multiplexer_161_out[5]), .out(multiplexer_193_out[4]),
    .sel(PLA_1_out[6]));
  Multiplexer multiplexer_198 (
    .in0(multiplexer_161_out[5]), .in1(multiplexer_161_out[6]), .out(multiplexer_193_out[5]),
    .sel(PLA_1_out[6]));
  Multiplexer multiplexer_199 (
    .in0(multiplexer_161_out[6]), .in1(multiplexer_161_out[7]), .out(multiplexer_193_out[6]),
    .sel(PLA_1_out[6]));
  Multiplexer multiplexer_200 (
    .in0(multiplexer_161_out[7]), .in1(multiplexer_161_out[8]), .out(multiplexer_193_out[7]),
    .sel(PLA_1_out[6]));
  Multiplexer multiplexer_201 (
    .in0(multiplexer_161_out[8]), .in1(multiplexer_161_out[9]), .out(multiplexer_193_out[8]),
    .sel(PLA_1_out[6]));
  Multiplexer multiplexer_202 (
    .in0(multiplexer_161_out[9]), .in1(multiplexer_161_out[10]), .out(multiplexer_193_out[9]),
    .sel(PLA_1_out[6]));
  Multiplexer multiplexer_203 (
    .in0(multiplexer_161_out[10]), .in1(multiplexer_161_out[11]), .out(multiplexer_193_out[10]),
    .sel(PLA_1_out[6]));
  Multiplexer multiplexer_204 (
    .in0(multiplexer_161_out[11]), .in1(multiplexer_161_out[12]), .out(multiplexer_193_out[11]),
    .sel(PLA_1_out[6]));
  Multiplexer multiplexer_205 (
    .in0(multiplexer_161_out[12]), .in1(multiplexer_161_out[13]), .out(multiplexer_193_out[12]),
    .sel(PLA_1_out[6]));
  Multiplexer multiplexer_206 (
    .in0(multiplexer_161_out[13]), .in1(multiplexer_161_out[14]), .out(multiplexer_193_out[13]),
    .sel(PLA_1_out[6]));
  Multiplexer multiplexer_207 (
    .in0(multiplexer_161_out[14]), .in1(multiplexer_161_out[15]), .out(multiplexer_193_out[14]),
    .sel(PLA_1_out[6]));
  Multiplexer multiplexer_208 (
    .in0(multiplexer_161_out[15]), .in1(1'b0), .out(multiplexer_193_out[15]), .sel(PLA_1_out[6]));
  Multiplexer multiplexer_209 (
    .in0(multiplexer_177_out[0]), .in1(multiplexer_177_out[1]), .out(Output_bus_1[0]), .sel(PLA_1_out[14]));
  Multiplexer multiplexer_210 (
    .in0(multiplexer_177_out[1]), .in1(multiplexer_177_out[2]), .out(Output_bus_1[1]), .sel(PLA_1_out[14]));
  Multiplexer multiplexer_211 (
    .in0(multiplexer_177_out[2]), .in1(multiplexer_177_out[3]), .out(Output_bus_1[2]), .sel(PLA_1_out[14]));
  Multiplexer multiplexer_212 (
    .in0(multiplexer_177_out[3]), .in1(multiplexer_177_out[4]), .out(Output_bus_1[3]), .sel(PLA_1_out[14]));
  Multiplexer multiplexer_213 (
    .in0(multiplexer_177_out[4]), .in1(multiplexer_177_out[5]), .out(Output_bus_1[4]), .sel(PLA_1_out[14]));
  Multiplexer multiplexer_214 (
    .in0(multiplexer_177_out[5]), .in1(multiplexer_177_out[6]), .out(Output_bus_1[5]), .sel(PLA_1_out[14]));
  Multiplexer multiplexer_215 (
    .in0(multiplexer_177_out[6]), .in1(multiplexer_177_out[7]), .out(Output_bus_1[6]), .sel(PLA_1_out[14]));
  Multiplexer multiplexer_216 (
    .in0(multiplexer_177_out[7]), .in1(multiplexer_177_out[8]), .out(Output_bus_1[7]), .sel(PLA_1_out[14]));
  Multiplexer multiplexer_217 (
    .in0(multiplexer_177_out[8]), .in1(multiplexer_177_out[9]), .out(Output_bus_1[8]), .sel(PLA_1_out[14]));
  Multiplexer multiplexer_218 (
    .in0(multiplexer_177_out[9]), .in1(multiplexer_177_out[10]), .out(Output_bus_1[9]), .sel(PLA_1_out[14]));
  Multiplexer multiplexer_219 (
    .in0(multiplexer_177_out[10]), .in1(multiplexer_177_out[11]), .out(Output_bus_1[10]), .sel(PLA_1_out[14]));
  Multiplexer multiplexer_220 (
    .in0(multiplexer_177_out[11]), .in1(multiplexer_177_out[12]), .out(Output_bus_1[11]), .sel(PLA_1_out[14]));
  Multiplexer multiplexer_221 (
    .in0(multiplexer_177_out[12]), .in1(multiplexer_177_out[13]), .out(Output_bus_1[12]), .sel(PLA_1_out[14]));
  Multiplexer multiplexer_222 (
    .in0(multiplexer_177_out[13]), .in1(multiplexer_177_out[14]), .out(Output_bus_1[13]), .sel(PLA_1_out[14]));
  Multiplexer multiplexer_223 (
    .in0(multiplexer_177_out[14]), .in1(multiplexer_177_out[15]), .out(Output_bus_1[14]), .sel(PLA_1_out[14]));
  Multiplexer multiplexer_224 (.in0(multiplexer_177_out[15]), .in1(1'b0), .out(Output_bus_1[15]), .sel(PLA_1_out[14]));
  or or_1 (or_1_out, and_4_out, and_6_out, and_8_out, and_2_out, and_12_out, and_14_out, and_10_out);
  and and_15 (and_15_out, multiplexer_193_out[0], PLA_1_out[7]);
  Multiplexer multiplexer_225 (
    .in0(multiplexer_193_out[0]), .in1(multiplexer_193_out[1]), .out(multiplexer_225_out[0]),
    .sel(PLA_1_out[7]));
  Multiplexer multiplexer_226 (
    .in0(multiplexer_193_out[1]), .in1(multiplexer_193_out[2]), .out(multiplexer_225_out[1]),
    .sel(PLA_1_out[7]));
  Multiplexer multiplexer_227 (
    .in0(multiplexer_193_out[2]), .in1(multiplexer_193_out[3]), .out(multiplexer_225_out[2]),
    .sel(PLA_1_out[7]));
  Multiplexer multiplexer_228 (
    .in0(multiplexer_193_out[3]), .in1(multiplexer_193_out[4]), .out(multiplexer_225_out[3]),
    .sel(PLA_1_out[7]));
  Multiplexer multiplexer_229 (
    .in0(multiplexer_193_out[4]), .in1(multiplexer_193_out[5]), .out(multiplexer_225_out[4]),
    .sel(PLA_1_out[7]));
  Multiplexer multiplexer_230 (
    .in0(multiplexer_193_out[5]), .in1(multiplexer_193_out[6]), .out(multiplexer_225_out[5]),
    .sel(PLA_1_out[7]));
  Multiplexer multiplexer_231 (
    .in0(multiplexer_193_out[6]), .in1(multiplexer_193_out[7]), .out(multiplexer_225_out[6]),
    .sel(PLA_1_out[7]));
  Multiplexer multiplexer_232 (
    .in0(multiplexer_193_out[7]), .in1(multiplexer_193_out[8]), .out(multiplexer_225_out[7]),
    .sel(PLA_1_out[7]));
  Multiplexer multiplexer_233 (
    .in0(multiplexer_193_out[8]), .in1(multiplexer_193_out[9]), .out(multiplexer_225_out[8]),
    .sel(PLA_1_out[7]));
  Multiplexer multiplexer_234 (
    .in0(multiplexer_193_out[9]), .in1(multiplexer_193_out[10]), .out(multiplexer_225_out[9]),
    .sel(PLA_1_out[7]));
  Multiplexer multiplexer_235 (
    .in0(multiplexer_193_out[10]), .in1(multiplexer_193_out[11]), .out(multiplexer_225_out[10]),
    .sel(PLA_1_out[7]));
  Multiplexer multiplexer_236 (
    .in0(multiplexer_193_out[11]), .in1(multiplexer_193_out[12]), .out(multiplexer_225_out[11]),
    .sel(PLA_1_out[7]));
  Multiplexer multiplexer_237 (
    .in0(multiplexer_193_out[12]), .in1(multiplexer_193_out[13]), .out(multiplexer_225_out[12]),
    .sel(PLA_1_out[7]));
  Multiplexer multiplexer_238 (
    .in0(multiplexer_193_out[13]), .in1(multiplexer_193_out[14]), .out(multiplexer_225_out[13]),
    .sel(PLA_1_out[7]));
  Multiplexer multiplexer_239 (
    .in0(multiplexer_193_out[14]), .in1(multiplexer_193_out[15]), .out(multiplexer_225_out[14]),
    .sel(PLA_1_out[7]));
  Multiplexer multiplexer_240 (
    .in0(multiplexer_193_out[15]), .in1(1'b0), .out(multiplexer_225_out[15]), .sel(PLA_1_out[7]));
  or or_2 (or_2_out, and_1_out, and_3_out, and_5_out, and_7_out, and_11_out, and_13_out, and_15_out, and_9_out);
  or or_3 (carry_out, or_2_out, or_1_out);
endmodule
module Instruction_Control (
  input  [15:0] mem_data_in,
  input  [15:0] mem_addr_in,
  input  CLK,
  input  [15:0] pc_data_in,
  input  pc_write_enable,
  input  carry_flag,
  input  zero_flag,
  input  sign_flag,
  input  RESET,
  output [15:0] mem_data_out,
  output [15:0] operand,
  output [15:0] pc_data_out,
  output [18:0] CPU_Control_BUS
);

  wire and_1_out, and_2_out, and_3_out, and_4_out, comparator_1_eq, comparator_2_eq, comparator_2_gt,
       comparator_3_eq, comparator_4_eq, d_ff_1_q, multiplexer_1_out, nor_1_out, not_1_out, not_2_out,
       not_3_out, not_4_out, or_1_out, or_2_out, or_3_out, or_5_out;
  wire [7:0] IDSC_q, IIRND_out, ITSD_out, subtractor_1_out, TSR_q;
  wire [15:0] adder_1_out, adder_2_out, adder_3_out, bit_extender_1_out, IMBD_out, Instruction_Register_p5,
       Instruction_Register_p6, MOR_q, multiplexer_2_out, multiplexer_4_out, PC_q, sixteen_register_1_q;
  wire [16:16] or_4_out;
  wire [23:0] Microcode_ROM_data, multiplexer_6_out;

  not not_1 (not_1_out, multiplexer_6_out[22]);
  or or_1 (or_1_out, pc_write_enable, nor_1_out);
  and and_1 (and_1_out, CLK, not_3_out);
  and and_2 (and_2_out, not_2_out, nor_1_out);
  not not_2 (not_2_out, pc_write_enable);
  Multiplexer multiplexer_1 (.in0(and_1_out), .in1(CLK), .out(multiplexer_1_out), .sel(or_2_out));
  or or_2 (or_2_out, or_1_out, not_1_out);
  Multiplexer #(.width(16)) multiplexer_2 (
    .in0(pc_data_in), .in1(pc_data_out), .out(multiplexer_2_out), .sel(and_2_out));
  Counter #(.max('hffff), .width(16)) PC (
    .clr(RESET), .load(or_1_out), .up(not_1_out), .clk(multiplexer_1_out), .D(multiplexer_2_out), .Q(PC_q));  // open: count, carry
  not not_3 (not_3_out, or_4_out[16]);
  LedBar #(.matrixcols(16)) LedBar_4 (
    .led0(pc_data_out[15]), .led1(pc_data_out[14]), .led2(pc_data_out[13]), .led3(pc_data_out[12]),
    .led4(pc_data_out[11]), .led5(pc_data_out[10]), .led6(pc_data_out[9]), .led7(pc_data_out[8]),
    .led8(pc_data_out[7]), .led9(pc_data_out[6]), .led10(pc_data_out[5]), .led11(pc_data_out[4]),
    .led12(pc_data_out[3]), .led13(pc_data_out[2]), .led14(pc_data_out[1]), .led15(pc_data_out[0]));
  D_Flip_Flop d_ff_1 (.D(or_1_out), .clk(CLK), .Q(d_ff_1_q), .reset(RESET));  // open: Qn, preset
  Adder #(.width(16)) adder_1 (.a(sixteen_register_1_q), .b(16'h1), .out(adder_1_out));  // open: cin, cout
  sixteen_register sixteen_register_1 (.S(RESET), .CLK(CLK), .D(PC_q), .WE(1'b1), .Q(sixteen_register_1_q));
  Adder #(.width(16)) adder_2 (
    .a(mem_addr_in), .b(Instruction_Register_p5), .out(adder_2_out), .cin(1'b0));  // open: cout
  Comparator #(.mode("unsigned"), .width(16)) comparator_1 (
    .a(PC_q), .b(adder_1_out), .eq(comparator_1_eq));  // open: gt, lt
  nor nor_1 (nor_1_out, d_ff_1_q, comparator_1_eq);
  Multiplexer #(.width(16)) multiplexer_3 (.in0(PC_q), .in1(adder_1_out), .out(pc_data_out), .sel(nor_1_out));
  Multiplexer #(.select(2), .width(16)) multiplexer_4 (
    .in0(pc_data_out), .in1(adder_2_out), .in2(Instruction_Register_p5), .out(multiplexer_4_out),
    .sel(CPU_Control_BUS[1:0]));  // open: in3
  RAM #(.addrWidth(16), .dataWidth(16), .enables("line")) RAM_1 (
    .addr(multiplexer_4_out), .we(multiplexer_6_out[0]), .clk(CLK), .din(mem_data_in), .dout(mem_data_out));
  or or_3 (or_3_out, RESET, and_3_out);
  Clock clock_1 ();  // open: out
  // Shift_Register #(.length(2), .width(16)) Instruction_Register: pin names not known; wires that end beside it: RESET, 1'b1, and_1_out, mem_data_out, Instruction_Register_p5, Instruction_Register_p6
  Counter IDSC (.clr(RESET), .load(or_3_out), .up(1'b1), .clk(CLK), .D(IIRND_out), .Q(IDSC_q));  // open: count, carry
  and and_3 (and_3_out, or_5_out, comparator_4_eq);
  PLA #(.in_width(20), .out_width(8), .\table ("xxx0xxxxxxxxxxxxxxxx 00000010 # IE=0 (during fetch)\n0xx10000101111111111 00000010 # jnc opd (Taken)\n1xx10000101111111111 00000010 # jnc opd (Skip)\n1xx10000110011111111 00000010 # jc opd (Taken)\n0xx10000110011111111 00000010 # jc opd (Skip)\nx0x10000110111111111 00000010 # jnz opd (Taken)\nx1x10000110111111111 00000010 # jnz opd (Skip)\nx1x10000111011111111 00000010 # jz opd (Taken)\nx0x10000111011111111 00000010 # jz opd (Skip)\nxx010000111111111111 00000010 # jns opd (Taken)\nxx110000111111111111 00000010 # jns opd (Skip)\nxx110001000011111111 00000010 # js opd (Taken)\nxx010001000011111111 00000010 # js opd (Skip)\nxxx10001000111111111 00000010 # jmp opd\nx1x10001011011111111 00000010 # je opd (Taken)\nx0x10001011011111111 00000010 # je opd (Skip)\nx0x10001011111111111 00000010 # jne opd(Taken)\nx1x10001011111111111 00000010 # jne opd(Skip)\nx0010001100011111111 00000010 # ja opd (Taken)\nxxx10001100011111111 00000010 # ja opd (Skip)\nx0010001100111111111 00000010 # jae opd (Taken)\nx1010001100111111111 00000010 # jae opd (Taken)\nxxx10001100111111111 00000010 # jae opd (Skip)\nx0110001101011111111 00000010 # jl opd (Taken)\nxxx10001101011111111 00000010 # jl opd (Skip)\nx0110001101111111111 00000010 # jle opd (Taken)\nx1010001101111111111 00000010 # jle opd (Taken)\nxxx10001101111111111 00000010 # jle opd (Skip)\nxxx10001001111111111 00000010 # hlt\nxxx10001010011111111 00000010 # nop\nxxxx1111111111111111 00000010 # invaild\nxxx10001010111111111 00000010 # lpc\nxxx10000000000000000 00000010 # add a, a\nxxx10000000000000001 00000010 # add a, b\nxxx10000000000000010 00000010 # add a, c\nxxx10000000000000011 00000010 # add a, d\nxxx10000000000000100 00000010 # add a, e\nxxx10000000000000101 00000010 # add a, bp\nxxx10000000000000110 00000010 # add a, sp\nxxx10000000000010000 00000010 # add b, a\nxxx10000000000010001 00000010 # add b, b\nxxx10000000000010010 00000010 # add b, c\nxxx10000000000010011 00000010 # add b, d\nxxx10000000000010100 00000010 # add b, e\nxxx10000000000010101 00000010 # add b, bp\nxxx10000000000010110 00000010 # add b, sp\nxxx10000000000100000 00000010 # add c, a\nxxx10000000000100001 00000010 # add c, b\nxxx10000000000100010 00000010 # add c, c\nxxx10000000000100011 00000010 # add c, d\nxxx10000000000100100 00000010 # add c, e\nxxx10000000000100101 00000010 # add c, bp\nxxx10000000000100110 00000010 # add c, sp\nxxx10000000000110000 00000010 # add d, a\nxxx10000000000110001 00000010 # add d, b\nxxx10000000000110010 00000010 # add d, c\nxxx10000000000110011 00000010 # add d, d\nxxx10000000000110100 00000010 # add d, e\nxxx10000000000110101 00000010 # add d, bp\nxxx10000000000110110 00000010 # add d, sp\nxxx10000000001000000 00000010 # add e, a\nxxx10000000001000001 00000010 # add e, b\nxxx10000000001000010 00000010 # add e, c\nxxx10000000001000011 00000010 # add e, d\nxxx10000000001000100 00000010 # add e, e\nxxx10000000001000101 00000010 # add e, bp\nxxx10000000001000110 00000010 # add e, sp\nxxx10000000001010000 00000010 # add bp, a\nxxx10000000001010001 00000010 # add bp, b\nxxx10000000001010010 00000010 # add bp, c\nxxx10000000001010011 00000010 # add bp, d\nxxx10000000001010100 00000010 # add bp, e\nxxx10000000001010101 00000010 # add bp, bp\nxxx10000000001010110 00000010 # add bp, sp\nxxx10000000001100000 00000010 # add sp, a\nxxx10000000001100001 00000010 # add sp, b\nxxx10000000001100010 00000010 # add sp, c\nxxx10000000001100011 00000010 # add sp, d\nxxx10000000001100100 00000010 # add sp, e\nxxx10000000001100101 00000010 # add sp, bp\nxxx10000000001100110 00000010 # add sp, sp\nxxx10000000100000000 00000010 # sub a, a\nxxx10000000100000001 00000010 # sub a, b\nxxx10000000100000010 00000010 # sub a, c\nxxx10000000100000011 00000010 # sub a, d\nxxx10000000100000100 00000010 # sub a, e\nxxx10000000100000101 00000010 # sub a, bp\nxxx10000000100000110 00000010 # sub a, sp\nxxx10000000100010000 00000010 # sub b, a\nxxx10000000100010001 00000010 # sub b, b\nxxx10000000100010010 00000010 # sub b, c\nxxx10000000100010011 00000010 # sub b, d\nxxx10000000100010100 00000010 # sub b, e\nxxx10000000100010101 00000010 # sub b, bp\nxxx10000000100010110 00000010 # sub b, sp\nxxx10000000100100000 00000010 # sub c, a\nxxx10000000100100001 00000010 # sub c, b\nxxx10000000100100010 00000010 # sub c, c\nxxx10000000100100011 00000010 # sub c, d\nxxx10000000100100100 00000010 # sub c, e\nxxx10000000100100101 00000010 # sub c, bp\nxxx10000000100100110 00000010 # sub c, sp\nxxx10000000100110000 00000010 # sub d, a\nxxx10000000100110001 00000010 # sub d, b\nxxx10000000100110010 00000010 # sub d, c\nxxx10000000100110011 00000010 # sub d, d\nxxx10000000100110100 00000010 # sub d, e\nxxx10000000100110101 00000010 # sub d, bp\nxxx10000000100110110 00000010 # sub d, sp\nxxx10000000101000000 00000010 # sub e, a\nxxx10000000101000001 00000010 # sub e, b\nxxx10000000101000010 00000010 # sub e, c\nxxx10000000101000011 00000010 # sub e, d\nxxx10000000101000100 00000010 # sub e, e\nxxx10000000101000101 00000010 # sub e, bp\nxxx10000000101000110 00000010 # sub e, sp\nxxx10000000101010000 00000010 # sub bp, a\nxxx10000000101010001 00000010 # sub bp, b\nxxx10000000101010010 00000010 # sub bp, c\nxxx10000000101010011 00000010 # sub bp, d\nxxx10000000101010100 00000010 # sub bp, e\nxxx10000000101010101 00000010 # sub bp, bp\nxxx10000000101010110 00000010 # sub bp, sp\nxxx10000000101100000 00000010 # sub sp, a\nxxx10000000101100001 00000010 # sub sp, b\nxxx10000000101100010 00000010 # sub sp, c\nxxx10000000101100011 00000010 # sub sp, d\nxxx10000000101100100 00000010 # sub sp, e\nxxx10000000101100101 00000010 # sub sp, bp\nxxx10000000101100110 00000010 # sub sp, sp\nxxx10000001000000000 00000010 # mul a, a\nxxx10000001000000001 00000010 # mul a, b\nxxx10000001000000010 00000010 # mul a, c\nxxx10000001000000011 00000010 # mul a, d\nxxx10000001000000100 00000010 # mul a, e\nxxx10000001000000101 00000010 # mul a, bp\nxxx10000001000000110 00000010 # mul a, sp\nxxx10000001000010000 00000010 # mul b, a\nxxx10000001000010001 00000010 # mul b, b\nxxx10000001000010010 00000010 # mul b, c\nxxx10000001000010011 00000010 # mul b, d\nxxx10000001000010100 00000010 # mul b, e\nxxx10000001000010101 00000010 # mul b, bp\nxxx10000001000010110 00000010 # mul b, sp\nxxx10000001000100000 00000010 # mul c, a\nxxx10000001000100001 00000010 # mul c, b\nxxx10000001000100010 00000010 # mul c, c\nxxx10000001000100011 00000010 # mul c, d\nxxx10000001000100100 00000010 # mul c, e\nxxx10000001000100101 00000010 # mul c, bp\nxxx10000001000100110 00000010 # mul c, sp\nxxx10000001000110000 00000010 # mul d, a\nxxx10000001000110001 00000010 # mul d, b\nxxx10000001000110010 00000010 # mul d, c\nxxx10000001000110011 00000010 # mul d, d\nxxx10000001000110100 00000010 # mul d, e\nxxx10000001000110101 00000010 # mul d, bp\nxxx10000001000110110 00000010 # mul d, sp\nxxx10000001001000000 00000010 # mul e, a\nxxx10000001001000001 00000010 # mul e, b\nxxx10000001001000010 00000010 # mul e, c\nxxx10000001001000011 00000010 # mul e, d\nxxx10000001001000100 00000010 # mul e, e\nxxx10000001001000101 00000010 # mul e, bp\nxxx10000001001000110 00000010 # mul e, sp\nxxx10000001001010000 00000010 # mul bp, a\nxxx10000001001010001 00000010 # mul bp, b\nxxx10000001001010010 00000010 # mul bp, c\nxxx10000001001010011 00000010 # mul bp, d\nxxx10000001001010100 00000010 # mul bp, e\nxxx10000001001010101 00000010 # mul bp, bp\nxxx10000001001010110 00000010 # mul bp, sp\nxxx10000001001100000 00000010 # mul sp, a\nxxx10000001001100001 00000010 # mul sp, b\nxxx10000001001100010 00000010 # mul sp, c\nxxx10000001001100011 00000010 # mul sp, d\nxxx10000001001100100 00000010 # mul sp, e\nxxx10000001001100101 00000010 # mul sp, bp\nxxx10000001001100110 00000010 # mul sp, sp\nxxx10000001100000000 00000010 # and a, a\nxxx10000001100000001 00000010 # and a, b\nxxx10000001100000010 00000010 # and a, c\nxxx10000001100000011 00000010 # and a, d\nxxx10000001100000100 00000010 # and a, e\nxxx10000001100000101 00000010 # and a, bp\nxxx10000001100000110 00000010 # and a, sp\nxxx10000001100010000 00000010 # and b, a\nxxx10000001100010001 00000010 # and b, b\nxxx10000001100010010 00000010 # and b, c\nxxx10000001100010011 00000010 # and b, d\nxxx10000001100010100 00000010 # and b, e\nxxx10000001100010101 00000010 # and b, bp\nxxx10000001100010110 00000010 # and b, sp\nxxx10000001100100000 00000010 # and c, a\nxxx10000001100100001 00000010 # and c, b\nxxx10000001100100010 00000010 # and c, c\nxxx10000001100100011 00000010 # and c, d\nxxx10000001100100100 00000010 # and c, e\nxxx10000001100100101 00000010 # and c, bp\nxxx10000001100100110 00000010 # and c, sp\nxxx10000001100110000 00000010 # and d, a\nxxx10000001100110001 00000010 # and d, b\nxxx10000001100110010 00000010 # and d, c\nxxx10000001100110011 00000010 # and d, d\nxxx10000001100110100 00000010 # and d, e\nxxx10000001100110101 00000010 # and d, bp\nxxx10000001100110110 00000010 # and d, sp\nxxx10000001101000000 00000010 # and e, a\nxxx10000001101000001 00000010 # and e, b\nxxx10000001101000010 00000010 # and e, c\nxxx10000001101000011 00000010 # and e, d\nxxx10000001101000100 00000010 # and e, e\nxxx10000001101000101 00000010 # and e, bp\nxxx10000001101000110 00000010 # and e, sp\nxxx10000001101010000 00000010 # and bp, a\nxxx10000001101010001 00000010 # and bp, b\nxxx10000001101010010 00000010 # and bp, c\nxxx10000001101010011 00000010 # and bp, d\nxxx10000001101010100 00000010 # and bp, e\nxxx10000001101010101 00000010 # and bp, bp\nxxx10000001101010110 00000010 # and bp, sp\nxxx10000001101100000 00000010 # and sp, a\nxxx10000001101100001 00000010 # and sp, b\nxxx10000001101100010 00000010 # and sp, c\nxxx10000001101100011 00000010 # and sp, d\nxxx10000001101100100 00000010 # and sp, e\nxxx10000001101100101 00000010 # and sp, bp\nxxx10000001101100110 00000010 # and sp, sp\nxxx10000010000000000 00000010 # or a, a\nxxx10000010000000001 00000010 # or a, b\nxxx10000010000000010 00000010 # or a, c\nxxx10000010000000011 00000010 # or a, d\nxxx10000010000000100 00000010 # or a, e\nxxx10000010000000101 00000010 # or a, bp\nxxx10000010000000110 00000010 # or a, sp\nxxx10000010000010000 00000010 # or b, a\nxxx10000010000010001 00000010 # or b, b\nxxx10000010000010010 00000010 # or b, c\nxxx10000010000010011 00000010 # or b, d\nxxx10000010000010100 00000010 # or b, e\nxxx10000010000010101 00000010 # or b, bp\nxxx10000010000010110 00000010 # or b, sp\nxxx10000010000100000 00000010 # or c, a\nxxx10000010000100001 00000010 # or c, b\nxxx10000010000100010 00000010 # or c, c\nxxx10000010000100011 00000010 # or c, d\nxxx10000010000100100 00000010 # or c, e\nxxx10000010000100101 00000010 # or c, bp\nxxx10000010000100110 00000010 # or c, sp\nxxx10000010000110000 00000010 # or d, a\nxxx10000010000110001 00000010 # or d, b\nxxx10000010000110010 00000010 # or d, c\nxxx10000010000110011 00000010 # or d, d\nxxx10000010000110100 00000010 # or d, e\nxxx10000010000110101 00000010 # or d, bp\nxxx10000010000110110 00000010 # or d, sp\nxxx10000010001000000 00000010 # or e, a\nxxx10000010001000001 00000010 # or e, b\nxxx10000010001000010 00000010 # or e, c\nxxx10000010001000011 00000010 # or e, d\nxxx10000010001000100 00000010 # or e, e\nxxx10000010001000101 00000010 # or e, bp\nxxx10000010001000110 00000010 # or e, sp\nxxx10000010001010000 00000010 # or bp, a\nxxx10000010001010001 00000010 # or bp, b\nxxx10000010001010010 00000010 # or bp, c\nxxx10000010001010011 00000010 # or bp, d\nxxx10000010001010100 00000010 # or bp, e\nxxx10000010001010101 00000010 # or bp, bp\nxxx10000010001010110 00000010 # or bp, sp\nxxx10000010001100000 00000010 # or sp, a\nxxx10000010001100001 00000010 # or sp, b\nxxx10000010001100010 00000010 # or sp, c\nxxx10000010001100011 00000010 # or sp, d\nxxx10000010001100100 00000010 # or sp, e\nxxx10000010001100101 00000010 # or sp, bp\nxxx10000010001100110 00000010 # or sp, sp\nxxx10000011000000000 00000010 # xor a, a\nxxx10000011000000001 00000010 # xor a, b\nxxx10000011000000010 00000010 # xor a, c\nxxx10000011000000011 00000010 # xor a, d\nxxx10000011000000100 00000010 # xor a, e\nxxx10000011000000101 00000010 # xor a, bp\nxxx10000011000000110 00000010 # xor a, sp\nxxx10000011000010000 00000010 # xor b, a\nxxx10000011000010001 00000010 # xor b, b\nxxx10000011000010010 00000010 # xor b, c\nxxx10000011000010011 00000010 # xor b, d\nxxx10000011000010100 00000010 # xor b, e\nxxx10000011000010101 00000010 # xor b, bp\nxxx10000011000010110 00000010 # xor b, sp\nxxx10000011000100000 00000010 # xor c, a\nxxx10000011000100001 00000010 # xor c, b\nxxx10000011000100010 00000010 # xor c, c\nxxx10000011000100011 00000010 # xor c, d\nxxx10000011000100100 00000010 # xor c, e\nxxx10000011000100101 00000010 # xor c, bp\nxxx10000011000100110 00000010 # xor c, sp\nxxx10000011000110000 00000010 # xor d, a\nxxx10000011000110001 00000010 # xor d, b\nxxx10000011000110010 00000010 # xor d, c\nxxx10000011000110011 00000010 # xor d, d\nxxx10000011000110100 00000010 # xor d, e\nxxx10000011000110101 00000010 # xor d, bp\nxxx10000011000110110 00000010 # xor d, sp\nxxx10000011001000000 00000010 # xor e, a\nxxx10000011001000001 00000010 # xor e, b\nxxx10000011001000010 00000010 # xor e, c\nxxx10000011001000011 00000010 # xor e, d\nxxx10000011001000100 00000010 # xor e, e\nxxx10000011001000101 00000010 # xor e, bp\nxxx10000011001000110 00000010 # xor e, sp\nxxx10000011001010000 00000010 # xor bp, a\nxxx10000011001010001 00000010 # xor bp, b\nxxx10000011001010010 00000010 # xor bp, c\nxxx10000011001010011 00000010 # xor bp, d\nxxx10000011001010100 00000010 # xor bp, e\nxxx10000011001010101 00000010 # xor bp, bp\nxxx10000011001010110 00000010 # xor bp, sp\nxxx10000011001100000 00000010 # xor sp, a\nxxx10000011001100001 00000010 # xor sp, b\nxxx10000011001100010 00000010 # xor sp, c\nxxx10000011001100011 00000010 # xor sp, d\nxxx10000011001100100 00000010 # xor sp, e\nxxx10000011001100101 00000010 # xor sp, bp\nxxx10000011001100110 00000010 # xor sp, sp\nxxx10000011100000000 00000010 # shr a, a\nxxx10000011100000001 00000010 # shr a, b\nxxx10000011100000010 00000010 # shr a, c\nxxx10000011100000011 00000010 # shr a, d\nxxx10000011100000100 00000010 # shr a, e\nxxx10000011100000101 00000010 # shr a, bp\nxxx10000011100000110 00000010 # shr a, sp\nxxx10000011100010000 00000010 # shr b, a\nxxx10000011100010001 00000010 # shr b, b\nxxx10000011100010010 00000010 # shr b, c\nxxx10000011100010011 00000010 # shr b, d\nxxx10000011100010100 00000010 # shr b, e\nxxx10000011100010101 00000010 # shr b, bp\nxxx10000011100010110 00000010 # shr b, sp\nxxx10000011100100000 00000010 # shr c, a\nxxx10000011100100001 00000010 # shr c, b\nxxx10000011100100010 00000010 # shr c, c\nxxx10000011100100011 00000010 # shr c, d\nxxx10000011100100100 00000010 # shr c, e\nxxx10000011100100101 00000010 # shr c, bp\nxxx10000011100100110 00000010 # shr c, sp\nxxx10000011100110000 00000010 # shr d, a\nxxx10000011100110001 00000010 # shr d, b\nxxx10000011100110010 00000010 # shr d, c\nxxx10000011100110011 00000010 # shr d, d\nxxx10000011100110100 00000010 # shr d, e\nxxx10000011100110101 00000010 # shr d, bp\nxxx10000011100110110 00000010 # shr d, sp\nxxx10000011101000000 00000010 # shr e, a\nxxx10000011101000001 00000010 # shr e, b\nxxx10000011101000010 00000010 # shr e, c\nxxx10000011101000011 00000010 # shr e, d\nxxx10000011101000100 00000010 # shr e, e\nxxx10000011101000101 00000010 # shr e, bp\nxxx10000011101000110 00000010 # shr e, sp\nxxx10000011101010000 00000010 # shr bp, a\nxxx10000011101010001 00000010 # shr bp, b\nxxx10000011101010010 00000010 # shr bp, c\nxxx10000011101010011 00000010 # shr bp, d\nxxx10000011101010100 00000010 # shr bp, e\nxxx10000011101010101 00000010 # shr bp, bp\nxxx10000011101010110 00000010 # shr bp, sp\nxxx10000011101100000 00000010 # shr sp, a\nxxx10000011101100001 00000010 # shr sp, b\nxxx10000011101100010 00000010 # shr sp, c\nxxx10000011101100011 00000010 # shr sp, d\nxxx10000011101100100 00000010 # shr sp, e\nxxx10000011101100101 00000010 # shr sp, bp\nxxx10000011101100110 00000010 # shr sp, sp\nxxx10000000000001111 00000010 # add a, opd\nxxx10000000000011111 00000010 # add b, opd\nxxx10000000000101111 00000010 # add c, opd\nxxx10000000000111111 00000010 # add d, opd\nxxx10000000001001111 00000010 # add e, opd\nxxx10000000001011111 00000010 # add bp, opd\nxxx10000000001101111 00000010 # add sp, opd\nxxx10000000100001111 00000010 # sub a, opd\nxxx10000000100011111 00000010 # sub b, opd\nxxx10000000100101111 00000010 # sub c, opd\nxxx10000000100111111 00000010 # sub d, opd\nxxx10000000101001111 00000010 # sub e, opd\nxxx10000000101011111 00000010 # sub bp, opd\nxxx10000000101101111 00000010 # sub sp, opd\nxxx10000001000001111 00000010 # mul a, opd\nxxx10000001000011111 00000010 # mul b, opd\nxxx10000001000101111 00000010 # mul c, opd\nxxx10000001000111111 00000010 # mul d, opd\nxxx10000001001001111 00000010 # mul e, opd\nxxx10000001001011111 00000010 # mul bp, opd\nxxx10000001001101111 00000010 # mul sp, opd\nxxx10000001100001111 00000010 # and a, opd\nxxx10000001100011111 00000010 # and b, opd\nxxx10000001100101111 00000010 # and c, opd\nxxx10000001100111111 00000010 # and d, opd\nxxx10000001101001111 00000010 # and e, opd\nxxx10000001101011111 00000010 # and bp, opd\nxxx10000001101101111 00000010 # and sp, opd\nxxx10000010000001111 00000010 # or a, opd\nxxx10000010000011111 00000010 # or b, opd\nxxx10000010000101111 00000010 # or c, opd\nxxx10000010000111111 00000010 # or d, opd\nxxx10000010001001111 00000010 # or e, opd\nxxx10000010001011111 00000010 # or bp, opd\nxxx10000010001101111 00000010 # or sp, opd\nxxx10000011000001111 00000010 # xor a, opd\nxxx10000011000011111 00000010 # xor b, opd\nxxx10000011000101111 00000010 # xor c, opd\nxxx10000011000111111 00000010 # xor d, opd\nxxx10000011001001111 00000010 # xor e, opd\nxxx10000011001011111 00000010 # xor bp, opd\nxxx10000011001101111 00000010 # xor sp, opd\nxxx10000011100001111 00000010 # shr a, opd\nxxx10000011100011111 00000010 # shr b, opd\nxxx10000011100101111 00000010 # shr c, opd\nxxx10000011100111111 00000010 # shr d, opd\nxxx10000011101001111 00000010 # shr e, opd\nxxx10000011101011111 00000010 # shr bp, opd\nxxx10000011101101111 00000010 # shr sp, opd\nxxx10000000000001001 00000010 # add a, [memaddr+opd]\nxxx10000000000011001 00000010 # add b, [memaddr+opd]\nxxx10000000000101001 00000010 # add c, [memaddr+opd]\nxxx10000000000111001 00000010 # add d, [memaddr+opd]\nxxx10000000001001001 00000010 # add e, [memaddr+opd]\nxxx10000000001011001 00000010 # add bp, [memaddr+opd]\nxxx10000000001101001 00000010 # add sp, [memaddr+opd]\nxxx10000000000001001 00000010 # add a, [memaddr+opd]\nxxx10000000000011001 00000010 # add b, [memaddr+opd]\nxxx10000000000101001 00000010 # add c, [memaddr+opd]\nxxx10000000000111001 00000010 # add d, [memaddr+opd]\nxxx10000000001001001 00000010 # add e, [memaddr+opd]\nxxx10000000001011001 00000010 # add bp, [memaddr+opd]\nxxx10000000001101001 00000010 # add sp, [memaddr+opd]\nxxx10000000100001001 00000010 # sub a, [memaddr+opd]\nxxx10000000100011001 00000010 # sub b, [memaddr+opd]\nxxx10000000100101001 00000010 # sub c, [memaddr+opd]\nxxx10000000100111001 00000010 # sub d, [memaddr+opd]\nxxx10000000101001001 00000010 # sub e, [memaddr+opd]\nxxx10000000101011001 00000010 # sub bp, [memaddr+opd]\nxxx10000000101101001 00000010 # sub sp, [memaddr+opd]\nxxx10000000100001001 00000010 # sub a, [memaddr+opd]\nxxx10000000100011001 00000010 # sub b, [memaddr+opd]\nxxx10000000100101001 00000010 # sub c, [memaddr+opd]\nxxx10000000100111001 00000010 # sub d, [memaddr+opd]\nxxx10000000101001001 00000010 # sub e, [memaddr+opd]\nxxx10000000101011001 00000010 # sub bp, [memaddr+opd]\nxxx10000000101101001 00000010 # sub sp, [memaddr+opd]\nxxx10000001000001001 00000010 # mul a, [memaddr+opd]\nxxx10000001000011001 00000010 # mul b, [memaddr+opd]\nxxx10000001000101001 00000010 # mul c, [memaddr+opd]\nxxx10000001000111001 00000010 # mul d, [memaddr+opd]\nxxx10000001001001001 00000010 # mul e, [memaddr+opd]\nxxx10000001001011001 00000010 # mul bp, [memaddr+opd]\nxxx10000001001101001 00000010 # mul sp, [memaddr+opd]\nxxx10000001000001001 00000010 # mul a, [memaddr+opd]\nxxx10000001000011001 00000010 # mul b, [memaddr+opd]\nxxx10000001000101001 00000010 # mul c, [memaddr+opd]\nxxx10000001000111001 00000010 # mul d, [memaddr+opd]\nxxx10000001001001001 00000010 # mul e, [memaddr+opd]\nxxx10000001001011001 00000010 # mul bp, [memaddr+opd]\nxxx10000001001101001 00000010 # mul sp, [memaddr+opd]\nxxx10000001100001001 00000010 # and a, [memaddr+opd]\nxxx10000001100011001 00000010 # and b, [memaddr+opd]\nxxx10000001100101001 00000010 # and c, [memaddr+opd]\nxxx10000001100111001 00000010 # and d, [memaddr+opd]\nxxx10000001101001001 00000010 # and e, [memaddr+opd]\nxxx10000001101011001 00000010 # and bp, [memaddr+opd]\nxxx10000001101101001 00000010 # and sp, [memaddr+opd]\nxxx10000001100001001 00000010 # and a, [memaddr+opd]\nxxx10000001100011001 00000010 # and b, [memaddr+opd]\nxxx10000001100101001 00000010 # and c, [memaddr+opd]\nxxx10000001100111001 00000010 # and d, [memaddr+opd]\nxxx10000001101001001 00000010 # and e, [memaddr+opd]\nxxx10000001101011001 00000010 # and bp, [memaddr+opd]\nxxx10000001101101001 00000010 # and sp, [memaddr+opd]\nxxx10000010000001001 00000010 # or a, [memaddr+opd]\nxxx10000010000011001 00000010 # or b, [memaddr+opd]\nxxx10000010000101001 00000010 # or c, [memaddr+opd]\nxxx10000010000111001 00000010 # or d, [memaddr+opd]\nxxx10000010001001001 00000010 # or e, [memaddr+opd]\nxxx10000010001011001 00000010 # or bp, [memaddr+opd]\nxxx10000010001101001 00000010 # or sp, [memaddr+opd]\nxxx10000010000001001 00000010 # or a, [memaddr+opd]\nxxx10000010000011001 00000010 # or b, [memaddr+opd]\nxxx10000010000101001 00000010 # or c, [memaddr+opd]\nxxx10000010000111001 00000010 # or d, [memaddr+opd]\nxxx10000010001001001 00000010 # or e, [memaddr+opd]\nxxx10000010001011001 00000010 # or bp, [memaddr+opd]\nxxx10000010001101001 00000010 # or sp, [memaddr+opd]\nxxx10000011000001001 00000010 # xor a, [memaddr+opd]\nxxx10000011000011001 00000010 # xor b, [memaddr+opd]\nxxx10000011000101001 00000010 # xor c, [memaddr+opd]\nxxx10000011000111001 00000010 # xor d, [memaddr+opd]\nxxx10000011001001001 00000010 # xor e, [memaddr+opd]\nxxx10000011001011001 00000010 # xor bp, [memaddr+opd]\nxxx10000011001101001 00000010 # xor sp, [memaddr+opd]\nxxx10000011000001001 00000010 # xor a, [memaddr+opd]\nxxx10000011000011001 00000010 # xor b, [memaddr+opd]\nxxx10000011000101001 00000010 # xor c, [memaddr+opd]\nxxx10000011000111001 00000010 # xor d, [memaddr+opd]\nxxx10000011001001001 00000010 # xor e, [memaddr+opd]\nxxx10000011001011001 00000010 # xor bp, [memaddr+opd]\nxxx10000011001101001 00000010 # xor sp, [memaddr+opd]\nxxx10000011100001001 00000010 # shr a, [memaddr+opd]\nxxx10000011100011001 00000010 # shr b, [memaddr+opd]\nxxx10000011100101001 00000010 # shr c, [memaddr+opd]\nxxx10000011100111001 00000010 # shr d, [memaddr+opd]\nxxx10000011101001001 00000010 # shr e, [memaddr+opd]\nxxx10000011101011001 00000010 # shr bp, [memaddr+opd]\nxxx10000011101101001 00000010 # shr sp, [memaddr+opd]\nxxx10000011100001001 00000010 # shr a, [memaddr+opd]\nxxx10000011100011001 00000010 # shr b, [memaddr+opd]\nxxx10000011100101001 00000010 # shr c, [memaddr+opd]\nxxx10000011100111001 00000010 # shr d, [memaddr+opd]\nxxx10000011101001001 00000010 # shr e, [memaddr+opd]\nxxx10000011101011001 00000010 # shr bp, [memaddr+opd]\nxxx10000011101101001 00000010 # shr sp, [memaddr+opd]\nxxx10000000010111111 00000010 # add memval,opd\nxxx10000010100001111 00000010 # not a\nxxx10000010100011111 00000010 # not b\nxxx10000010100101111 00000010 # not c\nxxx10000010100111111 00000010 # not d\nxxx10000010101001111 00000010 # not e\nxxx10000010101011111 00000010 # not bp\nxxx10000010101101111 00000010 # not sp\nxxx10000100000000000 00000010 # mov a, a\nxxx10000100000000001 00000010 # mov a, b\nxxx10000100000000010 00000010 # mov a, c\nxxx10000100000000011 00000010 # mov a, d\nxxx10000100000000100 00000010 # mov a, e\nxxx10000100000000101 00000010 # mov a, bp\nxxx10000100000000110 00000010 # mov a, sp\nxxx10000100000010000 00000010 # mov b, a\nxxx10000100000010001 00000010 # mov b, b\nxxx10000100000010010 00000010 # mov b, c\nxxx10000100000010011 00000010 # mov b, d\nxxx10000100000010100 00000010 # mov b, e\nxxx10000100000010101 00000010 # mov b, bp\nxxx10000100000010110 00000010 # mov b, sp\nxxx10000100000100000 00000010 # mov c, a\nxxx10000100000100001 00000010 # mov c, b\nxxx10000100000100010 00000010 # mov c, c\nxxx10000100000100011 00000010 # mov c, d\nxxx10000100000100100 00000010 # mov c, e\nxxx10000100000100101 00000010 # mov c, bp\nxxx10000100000100110 00000010 # mov c, sp\nxxx10000100000110000 00000010 # mov d, a\nxxx10000100000110001 00000010 # mov d, b\nxxx10000100000110010 00000010 # mov d, c\nxxx10000100000110011 00000010 # mov d, d\nxxx10000100000110100 00000010 # mov d, e\nxxx10000100000110101 00000010 # mov d, bp\nxxx10000100000110110 00000010 # mov d, sp\nxxx10000100001000000 00000010 # mov e, a\nxxx10000100001000001 00000010 # mov e, b\nxxx10000100001000010 00000010 # mov e, c\nxxx10000100001000011 00000010 # mov e, d\nxxx10000100001000100 00000010 # mov e, e\nxxx10000100001000101 00000010 # mov e, bp\nxxx10000100001000110 00000010 # mov e, sp\nxxx10000100001010000 00000010 # mov bp, a\nxxx10000100001010001 00000010 # mov bp, b\nxxx10000100001010010 00000010 # mov bp, c\nxxx10000100001010011 00000010 # mov bp, d\nxxx10000100001010100 00000010 # mov bp, e\nxxx10000100001010101 00000010 # mov bp, bp\nxxx10000100001010110 00000010 # mov bp, sp\nxxx10000100001100000 00000010 # mov sp, a\nxxx10000100001100001 00000010 # mov sp, b\nxxx10000100001100010 00000010 # mov sp, c\nxxx10000100001100011 00000010 # mov sp, d\nxxx10000100001100100 00000010 # mov sp, e\nxxx10000100001100101 00000010 # mov sp, bp\nxxx10000100001100110 00000010 # mov sp, sp\nxxx10000100000001001 00000010 # mov a, [memaddr+opd]\nxxx10000100000011001 00000010 # mov b, [memaddr+opd]\nxxx10000100000101001 00000010 # mov c, [memaddr+opd]\nxxx10000100000111001 00000010 # mov d, [memaddr+opd]\nxxx10000100001001001 00000010 # mov e, [memaddr+opd]\nxxx10000100001011001 00000010 # mov bp, [memaddr+opd]\nxxx10000100001101001 00000010 # mov sp, [memaddr+opd]\nxxx10000100000001001 00000010 # mov a, [memaddr+opd]\nxxx10000100000011001 00000010 # mov b, [memaddr+opd]\nxxx10000100000101001 00000010 # mov c, [memaddr+opd]\nxxx10000100000111001 00000010 # mov d, [memaddr+opd]\nxxx10000100001001001 00000010 # mov e, [memaddr+opd]\nxxx10000100001011001 00000010 # mov bp, [memaddr+opd]\nxxx10000100001101001 00000010 # mov sp, [memaddr+opd]\nxxx10000100010111001 00000011 # mov memval, [memaddr+opd]\nxxx10000100010100000 00000010 # mov memaddr,a\nxxx10000100010100001 00000010 # mov memaddr,b\nxxx10000100010100010 00000010 # mov memaddr,c\nxxx10000100010100011 00000010 # mov memaddr,d\nxxx10000100010100100 00000010 # mov memaddr,e\nxxx10000100010100101 00000010 # mov memaddr,bp\nxxx10000100010100110 00000010 # mov memaddr,sp\nxxx10000100010110000 00000010 # mov memval,a\nxxx10000100010110001 00000010 # mov memval,b\nxxx10000100010110010 00000010 # mov memval,c\nxxx10000100010110011 00000010 # mov memval,d\nxxx10000100010110100 00000010 # mov memval,e\nxxx10000100010110101 00000010 # mov memval,bp\nxxx10000100010110110 00000010 # mov memval,sp\nxxx10000100010101010 00000011 # mov [memaddr+opd],memval\nxxx10000100010101111 00000010 # mov memaddr, opd\nxxx10000100010111111 00000010 # mov memval, opd\nxxx10000100000001111 00000010 # mov a, opd\nxxx10000100000011111 00000010 # mov b, opd\nxxx10000100000101111 00000010 # mov c, opd\nxxx10000100000111111 00000010 # mov d, opd\nxxx10000100001001111 00000010 # mov e, opd\nxxx10000100001011111 00000010 # mov bp, opd\nxxx10000100001101111 00000010 # mov sp, opd\nxxx10000100100001111 00000010 # in a\nxxx10000100100011111 00000010 # in b\nxxx10000100100101111 00000010 # in c\nxxx10000100100111111 00000010 # in d\nxxx10000100101001111 00000010 # in e\nxxx10000100101011111 00000010 # in bp\nxxx10000100101101111 00000010 # in sp\nxxx10000101000001111 00000010 # out a\nxxx10000101000011111 00000010 # out b\nxxx10000101000101111 00000010 # out c\nxxx10000101000111111 00000010 # out d\nxxx10000101001001111 00000010 # out e\nxxx10000101001011111 00000010 # out bp\nxxx10000101001101111 00000010 # out sp\nxxx10000101011111111 00000010 # out opd\nxxx10001001000000000 00000010 # cmp a, a\nxxx10001001000000001 00000010 # cmp a, b\nxxx10001001000000010 00000010 # cmp a, c\nxxx10001001000000011 00000010 # cmp a, d\nxxx10001001000000100 00000010 # cmp a, e\nxxx10001001000000101 00000010 # cmp a, bp\nxxx10001001000000110 00000010 # cmp a, sp\nxxx10001001000010000 00000010 # cmp b, a\nxxx10001001000010001 00000010 # cmp b, b\nxxx10001001000010010 00000010 # cmp b, c\nxxx10001001000010011 00000010 # cmp b, d\nxxx10001001000010100 00000010 # cmp b, e\nxxx10001001000010101 00000010 # cmp b, bp\nxxx10001001000010110 00000010 # cmp b, sp\nxxx10001001000100000 00000010 # cmp c, a\nxxx10001001000100001 00000010 # cmp c, b\nxxx10001001000100010 00000010 # cmp c, c\nxxx10001001000100011 00000010 # cmp c, d\nxxx10001001000100100 00000010 # cmp c, e\nxxx10001001000100101 00000010 # cmp c, bp\nxxx10001001000100110 00000010 # cmp c, sp\nxxx10001001000110000 00000010 # cmp d, a\nxxx10001001000110001 00000010 # cmp d, b\nxxx10001001000110010 00000010 # cmp d, c\nxxx10001001000110011 00000010 # cmp d, d\nxxx10001001000110100 00000010 # cmp d, e\nxxx10001001000110101 00000010 # cmp d, bp\nxxx10001001000110110 00000010 # cmp d, sp\nxxx10001001001000000 00000010 # cmp e, a\nxxx10001001001000001 00000010 # cmp e, b\nxxx10001001001000010 00000010 # cmp e, c\nxxx10001001001000011 00000010 # cmp e, d\nxxx10001001001000100 00000010 # cmp e, e\nxxx10001001001000101 00000010 # cmp e, bp\nxxx10001001001000110 00000010 # cmp e, sp\nxxx10001001001010000 00000010 # cmp bp, a\nxxx10001001001010001 00000010 # cmp bp, b\nxxx10001001001010010 00000010 # cmp bp, c\nxxx10001001001010011 00000010 # cmp bp, d\nxxx10001001001010100 00000010 # cmp bp, e\nxxx10001001001010101 00000010 # cmp bp, bp\nxxx10001001001010110 00000010 # cmp bp, sp\nxxx10001001001100000 00000010 # cmp sp, a\nxxx10001001001100001 00000010 # cmp sp, b\nxxx10001001001100010 00000010 # cmp sp, c\nxxx10001001001100011 00000010 # cmp sp, d\nxxx10001001001100100 00000010 # cmp sp, e\nxxx10001001001100101 00000010 # cmp sp, bp\nxxx10001001001100110 00000010 # cmp sp, sp\nxxx10001001000001111 00000010 # cmp a, opd\nxxx10001001000011111 00000010 # cmp b, opd\nxxx10001001000101111 00000010 # cmp c, opd\nxxx10001001000111111 00000010 # cmp d, opd\nxxx10001001001001111 00000010 # cmp e, opd\nxxx10001001001011111 00000010 # cmp bp, opd\nxxx10001001001101111 00000010 # cmp sp, opd\nxxx10001000110111111 00000010 # jmp memval\n0xx10000101100001111 00000010 # jnc a (Taken)\n0xx10000101100011111 00000010 # jnc b (Taken)\n0xx10000101100101111 00000010 # jnc c (Taken)\n0xx10000101100111111 00000010 # jnc d (Taken)\n0xx10000101101001111 00000010 # jnc e (Taken)\n0xx10000101101011111 00000010 # jnc bp (Taken)\n0xx10000101101101111 00000010 # jnc sp (Taken)\n1xx10000101100001111 00000010 # jnc a (Skip)\n1xx10000101100011111 00000010 # jnc b (Skip)\n1xx10000101100101111 00000010 # jnc c (Skip)\n1xx10000101100111111 00000010 # jnc d (Skip)\n1xx10000101101001111 00000010 # jnc e (Skip)\n1xx10000101101011111 00000010 # jnc bp (Skip)\n1xx10000101101101111 00000010 # jnc sp (Skip)\n1xx10000110000001111 00000010 # jc a (Taken)\n1xx10000110000011111 00000010 # jc b (Taken)\n1xx10000110000101111 00000010 # jc c (Taken)\n1xx10000110000111111 00000010 # jc d (Taken)\n1xx10000110001001111 00000010 # jc e (Taken)\n1xx10000110001011111 00000010 # jc bp (Taken)\n1xx10000110001101111 00000010 # jc sp (Taken)\n0xx10000110000001111 00000010 # jc a (Skip)\n0xx10000110000011111 00000010 # jc b (Skip)\n0xx10000110000101111 00000010 # jc c (Skip)\n0xx10000110000111111 00000010 # jc d (Skip)\n0xx10000110001001111 00000010 # jc e (Skip)\n0xx10000110001011111 00000010 # jc bp (Skip)\n0xx10000110001101111 00000010 # jc sp (Skip)\nx0x10000110100001111 00000010 # jnz a (Taken)\nx0x10000110100011111 00000010 # jnz b (Taken)\nx0x10000110100101111 00000010 # jnz c (Taken)\nx0x10000110100111111 00000010 # jnz d (Taken)\nx0x10000110101001111 00000010 # jnz e (Taken)\nx0x10000110101011111 00000010 # jnz bp (Taken)\nx0x10000110101101111 00000010 # jnz sp (Taken)\nx1x10000110100001111 00000010 # jnz a (Skip)\nx1x10000110100011111 00000010 # jnz b (Skip)\nx1x10000110100101111 00000010 # jnz c (Skip)\nx1x10000110100111111 00000010 # jnz d (Skip)\nx1x10000110101001111 00000010 # jnz e (Skip)\nx1x10000110101011111 00000010 # jnz bp (Skip)\nx1x10000110101101111 00000010 # jnz sp (Skip)\nx1x10000111000001111 00000010 # jz a (Taken)\nx1x10000111000011111 00000010 # jz b (Taken)\nx1x10000111000101111 00000010 # jz c (Taken)\nx1x10000111000111111 00000010 # jz d (Taken)\nx1x10000111001001111 00000010 # jz e (Taken)\nx1x10000111001011111 00000010 # jz bp (Taken)\nx1x10000111001101111 00000010 # jz sp (Taken)\nx0x10000111000001111 00000010 # jz a (Skip)\nx0x10000111000011111 00000010 # jz b (Skip)\nx0x10000111000101111 00000010 # jz c (Skip)\nx0x10000111000111111 00000010 # jz d (Skip)\nx0x10000111001001111 00000010 # jz e (Skip)\nx0x10000111001011111 00000010 # jz bp (Skip)\nx0x10000111001101111 00000010 # jz sp (Skip)\nxx010000111100001111 00000010 # jns a (Taken)\nxx010000111100011111 00000010 # jns b (Taken)\nxx010000111100101111 00000010 # jns c (Taken)\nxx010000111100111111 00000010 # jns d (Taken)\nxx010000111101001111 00000010 # jns e (Taken)\nxx010000111101011111 00000010 # jns bp (Taken)\nxx010000111101101111 00000010 # jns sp (Taken)\nxx110000111100001111 00000010 # jns a (Skip)\nxx110000111100011111 00000010 # jns b (Skip)\nxx110000111100101111 00000010 # jns c (Skip)\nxx110000111100111111 00000010 # jns d (Skip)\nxx110000111101001111 00000010 # jns e (Skip)\nxx110000111101011111 00000010 # jns bp (Skip)\nxx110000111101101111 00000010 # jns sp (Skip)\nxx110001000000001111 00000010 # js a (Taken)\nxx110001000000011111 00000010 # js b (Taken)\nxx110001000000101111 00000010 # js c (Taken)\nxx110001000000111111 00000010 # js d (Taken)\nxx110001000001001111 00000010 # js e (Taken)\nxx110001000001011111 00000010 # js bp (Taken)\nxx110001000001101111 00000010 # js sp (Taken)\nxx010001000000001111 00000010 # js a (Skip)\nxx010001000000011111 00000010 # js b (Skip)\nxx010001000000101111 00000010 # js c (Skip)\nxx010001000000111111 00000010 # js d (Skip)\nxx010001000001001111 00000010 # js e (Skip)\nxx010001000001011111 00000010 # js bp (Skip)\nxx010001000001101111 00000010 # js sp (Skip)\nxxx10001000100001111 00000010 # jmp a\nxxx10001000100011111 00000010 # jmp b\nxxx10001000100101111 00000010 # jmp c\nxxx10001000100111111 00000010 # jmp d\nxxx10001000101001111 00000010 # jmp e\nxxx10001000101011111 00000010 # jmp bp\nxxx10001000101101111 00000010 # jmp sp\nx1x10001011000001111 00000010 # je a (Taken)\nx1x10001011000011111 00000010 # je b (Taken)\nx1x10001011000101111 00000010 # je c (Taken)\nx1x10001011000111111 00000010 # je d (Taken)\nx1x10001011001001111 00000010 # je e (Taken)\nx1x10001011001011111 00000010 # je bp (Taken)\nx1x10001011001101111 00000010 # je sp (Taken)\nx0x10001011000001111 00000010 # je a (Skip)\nx0x10001011000011111 00000010 # je b (Skip)\nx0x10001011000101111 00000010 # je c (Skip)\nx0x10001011000111111 00000010 # je d (Skip)\nx0x10001011001001111 00000010 # je e (Skip)\nx0x10001011001011111 00000010 # je bp (Skip)\nx0x10001011001101111 00000010 # je sp (Skip)\nx0x10001011100001111 00000010 # jne a(Taken)\nx0x10001011100011111 00000010 # jne b(Taken)\nx0x10001011100101111 00000010 # jne c(Taken)\nx0x10001011100111111 00000010 # jne d(Taken)\nx0x10001011101001111 00000010 # jne e(Taken)\nx0x10001011101011111 00000010 # jne bp(Taken)\nx0x10001011101101111 00000010 # jne sp(Taken)\nx1x10001011100001111 00000010 # jne a(Skip)\nx1x10001011100011111 00000010 # jne b(Skip)\nx1x10001011100101111 00000010 # jne c(Skip)\nx1x10001011100111111 00000010 # jne d(Skip)\nx1x10001011101001111 00000010 # jne e(Skip)\nx1x10001011101011111 00000010 # jne bp(Skip)\nx1x10001011101101111 00000010 # jne sp(Skip)\nx0010001100000001111 00000010 # ja a (Taken)\nx0010001100000011111 00000010 # ja b (Taken)\nx0010001100000101111 00000010 # ja c (Taken)\nx0010001100000111111 00000010 # ja d (Taken)\nx0010001100001001111 00000010 # ja e (Taken)\nx0010001100001011111 00000010 # ja bp (Taken)\nx0010001100001101111 00000010 # ja sp (Taken)\nxxx10001100000001111 00000010 # ja a (Skip)\nxxx10001100000011111 00000010 # ja b (Skip)\nxxx10001100000101111 00000010 # ja c (Skip)\nxxx10001100000111111 00000010 # ja d (Skip)\nxxx10001100001001111 00000010 # ja e (Skip)\nxxx10001100001011111 00000010 # ja bp (Skip)\nxxx10001100001101111 00000010 # ja sp (Skip)\nx0010001100100001111 00000010 # jae a (Taken)\nx0010001100100011111 00000010 # jae b (Taken)\nx0010001100100101111 00000010 # jae c (Taken)\nx0010001100100111111 00000010 # jae d (Taken)\nx0010001100101001111 00000010 # jae e (Taken)\nx0010001100101011111 00000010 # jae bp (Taken)\nx0010001100101101111 00000010 # jae sp (Taken)\nx1010001100100001111 00000010 # jae a (Taken)\nx1010001100100011111 00000010 # jae b (Taken)\nx1010001100100101111 00000010 # jae c (Taken)\nx1010001100100111111 00000010 # jae d (Taken)\nx1010001100101001111 00000010 # jae e (Taken)\nx1010001100101011111 00000010 # jae bp (Taken)\nx1010001100101101111 00000010 # jae sp (Taken)\nxxx10001100100001111 00000010 # jae a (Skip)\nxxx10001100100011111 00000010 # jae b (Skip)\nxxx10001100100101111 00000010 # jae c (Skip)\nxxx10001100100111111 00000010 # jae d (Skip)\nxxx10001100101001111 00000010 # jae e (Skip)\nxxx10001100101011111 00000010 # jae bp (Skip)\nxxx10001100101101111 00000010 # jae sp (Skip)\nx0110001101000001111 00000010 # jl a (Taken)\nx0110001101000011111 00000010 # jl b (Taken)\nx0110001101000101111 00000010 # jl c (Taken)\nx0110001101000111111 00000010 # jl d (Taken)\nx0110001101001001111 00000010 # jl e (Taken)\nx0110001101001011111 00000010 # jl bp (Taken)\nx0110001101001101111 00000010 # jl sp (Taken)\nxxx10001101000001111 00000010 # jl a (Skip)\nxxx10001101000011111 00000010 # jl b (Skip)\nxxx10001101000101111 00000010 # jl c (Skip)\nxxx10001101000111111 00000010 # jl d (Skip)\nxxx10001101001001111 00000010 # jl e (Skip)\nxxx10001101001011111 00000010 # jl bp (Skip)\nxxx10001101001101111 00000010 # jl sp (Skip)\nx0110001101100001111 00000010 # jle a (Taken)\nx0110001101100011111 00000010 # jle b (Taken)\nx0110001101100101111 00000010 # jle c (Taken)\nx0110001101100111111 00000010 # jle d (Taken)\nx0110001101101001111 00000010 # jle e (Taken)\nx0110001101101011111 00000010 # jle bp (Taken)\nx0110001101101101111 00000010 # jle sp (Taken)\nx1010001101100001111 00000010 # jle a (Taken)\nx1010001101100011111 00000010 # jle b (Taken)\nx1010001101100101111 00000010 # jle c (Taken)\nx1010001101100111111 00000010 # jle d (Taken)\nx1010001101101001111 00000010 # jle e (Taken)\nx1010001101101011111 00000010 # jle bp (Taken)\nx1010001101101101111 00000010 # jle sp (Taken)\nxxx10001101100001111 00000010 # jle a (Skip)\nxxx10001101100011111 00000010 # jle b (Skip)\nxxx10001101100101111 00000010 # jle c (Skip)\nxxx10001101100111111 00000010 # jle d (Skip)\nxxx10001101101001111 00000010 # jle e (Skip)\nxxx10001101101011111 00000010 # jle bp (Skip)")) ITSD (
    .in({carry_flag, zero_flag, sign_flag, or_4_out[16], Instruction_Register_p6}), .out(ITSD_out));
  PLA #(.in_width(20), .out_width(8), .\table ("xxx0xxxxxxxxxxxxxxxx 00000000 # IE=0 (during fetch)\n0xx10000101111111111 00000000 # jnc opd (Taken)\n1xx10000101111111111 00000001 # jnc opd (Skip)\n1xx10000110011111111 00000000 # jc opd (Taken)\n0xx10000110011111111 00000001 # jc opd (Skip)\nx0x10000110111111111 00000000 # jnz opd (Taken)\nx1x10000110111111111 00000001 # jnz opd (Skip)\nx1x10000111011111111 00000000 # jz opd (Taken)\nx0x10000111011111111 00000001 # jz opd (Skip)\nxx010000111111111111 00000000 # jns opd (Taken)\nxx110000111111111111 00000001 # jns opd (Skip)\nxx110001000011111111 00000000 # js opd (Taken)\nxx010001000011111111 00000001 # js opd (Skip)\nxxx10001000111111111 00000000 # jmp opd\nx1x10001011011111111 00000000 # je opd (Taken)\nx0x10001011011111111 00000001 # je opd (Skip)\nx0x10001011111111111 00000000 # jne opd(Taken)\nx1x10001011111111111 00000001 # jne opd(Skip)\nx0010001100011111111 00000000 # ja opd (Taken)\nxxx10001100011111111 00000001 # ja opd (Skip)\nx0010001100111111111 00000000 # jae opd (Taken)\nx1010001100111111111 00000000 # jae opd (Taken)\nxxx10001100111111111 00000001 # jae opd (Skip)\nx0110001101011111111 00000000 # jl opd (Taken)\nxxx10001101011111111 00000001 # jl opd (Skip)\nx0110001101111111111 00000000 # jle opd (Taken)\nx1010001101111111111 00000000 # jle opd (Taken)\nxxx10001101111111111 00000001 # jle opd (Skip)\nxxx10001001111111111 00000001 # hlt\nxxx10001010011111111 00000001 # nop\nxxxx1111111111111111 00000001 # invaild\nxxx10001010111111111 00000001 # lpc\nxxx10000000000000000 00000001 # add a, a\nxxx10000000000000001 00000001 # add a, b\nxxx10000000000000010 00000001 # add a, c\nxxx10000000000000011 00000001 # add a, d\nxxx10000000000000100 00000001 # add a, e\nxxx10000000000000101 00000001 # add a, bp\nxxx10000000000000110 00000001 # add a, sp\nxxx10000000000010000 00000001 # add b, a\nxxx10000000000010001 00000001 # add b, b\nxxx10000000000010010 00000001 # add b, c\nxxx10000000000010011 00000001 # add b, d\nxxx10000000000010100 00000001 # add b, e\nxxx10000000000010101 00000001 # add b, bp\nxxx10000000000010110 00000001 # add b, sp\nxxx10000000000100000 00000001 # add c, a\nxxx10000000000100001 00000001 # add c, b\nxxx10000000000100010 00000001 # add c, c\nxxx10000000000100011 00000001 # add c, d\nxxx10000000000100100 00000001 # add c, e\nxxx10000000000100101 00000001 # add c, bp\nxxx10000000000100110 00000001 # add c, sp\nxxx10000000000110000 00000001 # add d, a\nxxx10000000000110001 00000001 # add d, b\nxxx10000000000110010 00000001 # add d, c\nxxx10000000000110011 00000001 # add d, d\nxxx10000000000110100 00000001 # add d, e\nxxx10000000000110101 00000001 # add d, bp\nxxx10000000000110110 00000001 # add d, sp\nxxx10000000001000000 00000001 # add e, a\nxxx10000000001000001 00000001 # add e, b\nxxx10000000001000010 00000001 # add e, c\nxxx10000000001000011 00000001 # add e, d\nxxx10000000001000100 00000001 # add e, e\nxxx10000000001000101 00000001 # add e, bp\nxxx10000000001000110 00000001 # add e, sp\nxxx10000000001010000 00000001 # add bp, a\nxxx10000000001010001 00000001 # add bp, b\nxxx10000000001010010 00000001 # add bp, c\nxxx10000000001010011 00000001 # add bp, d\nxxx10000000001010100 00000001 # add bp, e\nxxx10000000001010101 00000001 # add bp, bp\nxxx10000000001010110 00000001 # add bp, sp\nxxx10000000001100000 00000001 # add sp, a\nxxx10000000001100001 00000001 # add sp, b\nxxx10000000001100010 00000001 # add sp, c\nxxx10000000001100011 00000001 # add sp, d\nxxx10000000001100100 00000001 # add sp, e\nxxx10000000001100101 00000001 # add sp, bp\nxxx10000000001100110 00000001 # add sp, sp\nxxx10000000100000000 00000001 # sub a, a\nxxx10000000100000001 00000001 # sub a, b\nxxx10000000100000010 00000001 # sub a, c\nxxx10000000100000011 00000001 # sub a, d\nxxx10000000100000100 00000001 # sub a, e\nxxx10000000100000101 00000001 # sub a, bp\nxxx10000000100000110 00000001 # sub a, sp\nxxx10000000100010000 00000001 # sub b, a\nxxx10000000100010001 00000001 # sub b, b\nxxx10000000100010010 00000001 # sub b, c\nxxx10000000100010011 00000001 # sub b, d\nxxx10000000100010100 00000001 # sub b, e\nxxx10000000100010101 00000001 # sub b, bp\nxxx10000000100010110 00000001 # sub b, sp\nxxx10000000100100000 00000001 # sub c, a\nxxx10000000100100001 00000001 # sub c, b\nxxx10000000100100010 00000001 # sub c, c\nxxx10000000100100011 00000001 # sub c, d\nxxx10000000100100100 00000001 # sub c, e\nxxx10000000100100101 00000001 # sub c, bp\nxxx10000000100100110 00000001 # sub c, sp\nxxx10000000100110000 00000001 # sub d, a\nxxx10000000100110001 00000001 # sub d, b\nxxx10000000100110010 00000001 # sub d, c\nxxx10000000100110011 00000001 # sub d, d\nxxx10000000100110100 00000001 # sub d, e\nxxx10000000100110101 00000001 # sub d, bp\nxxx10000000100110110 00000001 # sub d, sp\nxxx10000000101000000 00000001 # sub e, a\nxxx10000000101000001 00000001 # sub e, b\nxxx10000000101000010 00000001 # sub e, c\nxxx10000000101000011 00000001 # sub e, d\nxxx10000000101000100 00000001 # sub e, e\nxxx10000000101000101 00000001 # sub e, bp\nxxx10000000101000110 00000001 # sub e, sp\nxxx10000000101010000 00000001 # sub bp, a\nxxx10000000101010001 00000001 # sub bp, b\nxxx10000000101010010 00000001 # sub bp, c\nxxx10000000101010011 00000001 # sub bp, d\nxxx10000000101010100 00000001 # sub bp, e\nxxx10000000101010101 00000001 # sub bp, bp\nxxx10000000101010110 00000001 # sub bp, sp\nxxx10000000101100000 00000001 # sub sp, a\nxxx10000000101100001 00000001 # sub sp, b\nxxx10000000101100010 00000001 # sub sp, c\nxxx10000000101100011 00000001 # sub sp, d\nxxx10000000101100100 00000001 # sub sp, e\nxxx10000000101100101 00000001 # sub sp, bp\nxxx10000000101100110 00000001 # sub sp, sp\nxxx10000001000000000 00000001 # mul a, a\nxxx10000001000000001 00000001 # mul a, b\nxxx10000001000000010 00000001 # mul a, c\nxxx10000001000000011 00000001 # mul a, d\nxxx10000001000000100 00000001 # mul a, e\nxxx10000001000000101 00000001 # mul a, bp\nxxx10000001000000110 00000001 # mul a, sp\nxxx10000001000010000 00000001 # mul b, a\nxxx10000001000010001 00000001 # mul b, b\nxxx10000001000010010 00000001 # mul b, c\nxxx10000001000010011 00000001 # mul b, d\nxxx10000001000010100 00000001 # mul b, e\nxxx10000001000010101 00000001 # mul b, bp\nxxx10000001000010110 00000001 # mul b, sp\nxxx10000001000100000 00000001 # mul c, a\nxxx10000001000100001 00000001 # mul c, b\nxxx10000001000100010 00000001 # mul c, c\nxxx10000001000100011 00000001 # mul c, d\nxxx10000001000100100 00000001 # mul c, e\nxxx10000001000100101 00000001 # mul c, bp\nxxx10000001000100110 00000001 # mul c, sp\nxxx10000001000110000 00000001 # mul d, a\nxxx10000001000110001 00000001 # mul d, b\nxxx10000001000110010 00000001 # mul d, c\nxxx10000001000110011 00000001 # mul d, d\nxxx10000001000110100 00000001 # mul d, e\nxxx10000001000110101 00000001 # mul d, bp\nxxx10000001000110110 00000001 # mul d, sp\nxxx10000001001000000 00000001 # mul e, a\nxxx10000001001000001 00000001 # mul e, b\nxxx10000001001000010 00000001 # mul e, c\nxxx10000001001000011 00000001 # mul e, d\nxxx10000001001000100 00000001 # mul e, e\nxxx10000001001000101 00000001 # mul e, bp\nxxx10000001001000110 00000001 # mul e, sp\nxxx10000001001010000 00000001 # mul bp, a\nxxx10000001001010001 00000001 # mul bp, b\nxxx10000001001010010 00000001 # mul bp, c\nxxx10000001001010011 00000001 # mul bp, d\nxxx10000001001010100 00000001 # mul bp, e\nxxx10000001001010101 00000001 # mul bp, bp\nxxx10000001001010110 00000001 # mul bp, sp\nxxx10000001001100000 00000001 # mul sp, a\nxxx10000001001100001 00000001 # mul sp, b\nxxx10000001001100010 00000001 # mul sp, c\nxxx10000001001100011 00000001 # mul sp, d\nxxx10000001001100100 00000001 # mul sp, e\nxxx10000001001100101 00000001 # mul sp, bp\nxxx10000001001100110 00000001 # mul sp, sp\nxxx10000001100000000 00000001 # and a, a\nxxx10000001100000001 00000001 # and a, b\nxxx10000001100000010 00000001 # and a, c\nxxx10000001100000011 00000001 # and a, d\nxxx10000001100000100 00000001 # and a, e\nxxx10000001100000101 00000001 # and a, bp\nxxx10000001100000110 00000001 # and a, sp\nxxx10000001100010000 00000001 # and b, a\nxxx10000001100010001 00000001 # and b, b\nxxx10000001100010010 00000001 # and b, c\nxxx10000001100010011 00000001 # and b, d\nxxx10000001100010100 00000001 # and b, e\nxxx10000001100010101 00000001 # and b, bp\nxxx10000001100010110 00000001 # and b, sp\nxxx10000001100100000 00000001 # and c, a\nxxx10000001100100001 00000001 # and c, b\nxxx10000001100100010 00000001 # and c, c\nxxx10000001100100011 00000001 # and c, d\nxxx10000001100100100 00000001 # and c, e\nxxx10000001100100101 00000001 # and c, bp\nxxx10000001100100110 00000001 # and c, sp\nxxx10000001100110000 00000001 # and d, a\nxxx10000001100110001 00000001 # and d, b\nxxx10000001100110010 00000001 # and d, c\nxxx10000001100110011 00000001 # and d, d\nxxx10000001100110100 00000001 # and d, e\nxxx10000001100110101 00000001 # and d, bp\nxxx10000001100110110 00000001 # and d, sp\nxxx10000001101000000 00000001 # and e, a\nxxx10000001101000001 00000001 # and e, b\nxxx10000001101000010 00000001 # and e, c\nxxx10000001101000011 00000001 # and e, d\nxxx10000001101000100 00000001 # and e, e\nxxx10000001101000101 00000001 # and e, bp\nxxx10000001101000110 00000001 # and e, sp\nxxx10000001101010000 00000001 # and bp, a\nxxx10000001101010001 00000001 # and bp, b\nxxx10000001101010010 00000001 # and bp, c\nxxx10000001101010011 00000001 # and bp, d\nxxx10000001101010100 00000001 # and bp, e\nxxx10000001101010101 00000001 # and bp, bp\nxxx10000001101010110 00000001 # and bp, sp\nxxx10000001101100000 00000001 # and sp, a\nxxx10000001101100001 00000001 # and sp, b\nxxx10000001101100010 00000001 # and sp, c\nxxx10000001101100011 00000001 # and sp, d\nxxx10000001101100100 00000001 # and sp, e\nxxx10000001101100101 00000001 # and sp, bp\nxxx10000001101100110 00000001 # and sp, sp\nxxx10000010000000000 00000001 # or a, a\nxxx10000010000000001 00000001 # or a, b\nxxx10000010000000010 00000001 # or a, c\nxxx10000010000000011 00000001 # or a, d\nxxx10000010000000100 00000001 # or a, e\nxxx10000010000000101 00000001 # or a, bp\nxxx10000010000000110 00000001 # or a, sp\nxxx10000010000010000 00000001 # or b, a\nxxx10000010000010001 00000001 # or b, b\nxxx10000010000010010 00000001 # or b, c\nxxx10000010000010011 00000001 # or b, d\nxxx10000010000010100 00000001 # or b, e\nxxx10000010000010101 00000001 # or b, bp\nxxx10000010000010110 00000001 # or b, sp\nxxx10000010000100000 00000001 # or c, a\nxxx10000010000100001 00000001 # or c, b\nxxx10000010000100010 00000001 # or c, c\nxxx10000010000100011 00000001 # or c, d\nxxx10000010000100100 00000001 # or c, e\nxxx10000010000100101 00000001 # or c, bp\nxxx10000010000100110 00000001 # or c, sp\nxxx10000010000110000 00000001 # or d, a\nxxx10000010000110001 00000001 # or d, b\nxxx10000010000110010 00000001 # or d, c\nxxx10000010000110011 00000001 # or d, d\nxxx10000010000110100 00000001 # or d, e\nxxx10000010000110101 00000001 # or d, bp\nxxx10000010000110110 00000001 # or d, sp\nxxx10000010001000000 00000001 # or e, a\nxxx10000010001000001 00000001 # or e, b\nxxx10000010001000010 00000001 # or e, c\nxxx10000010001000011 00000001 # or e, d\nxxx10000010001000100 00000001 # or e, e\nxxx10000010001000101 00000001 # or e, bp\nxxx10000010001000110 00000001 # or e, sp\nxxx10000010001010000 00000001 # or bp, a\nxxx10000010001010001 00000001 # or bp, b\nxxx10000010001010010 00000001 # or bp, c\nxxx10000010001010011 00000001 # or bp, d\nxxx10000010001010100 00000001 # or bp, e\nxxx10000010001010101 00000001 # or bp, bp\nxxx10000010001010110 00000001 # or bp, sp\nxxx10000010001100000 00000001 # or sp, a\nxxx10000010001100001 00000001 # or sp, b\nxxx10000010001100010 00000001 # or sp, c\nxxx10000010001100011 00000001 # or sp, d\nxxx10000010001100100 00000001 # or sp, e\nxxx10000010001100101 00000001 # or sp, bp\nxxx10000010001100110 00000001 # or sp, sp\nxxx10000011000000000 00000001 # xor a, a\nxxx10000011000000001 00000001 # xor a, b\nxxx10000011000000010 00000001 # xor a, c\nxxx10000011000000011 00000001 # xor a, d\nxxx10000011000000100 00000001 # xor a, e\nxxx10000011000000101 00000001 # xor a, bp\nxxx10000011000000110 00000001 # xor a, sp\nxxx10000011000010000 00000001 # xor b, a\nxxx10000011000010001 00000001 # xor b, b\nxxx10000011000010010 00000001 # xor b, c\nxxx10000011000010011 00000001 # xor b, d\nxxx10000011000010100 00000001 # xor b, e\nxxx10000011000010101 00000001 # xor b, bp\nxxx10000011000010110 00000001 # xor b, sp\nxxx10000011000100000 00000001 # xor c, a\nxxx10000011000100001 00000001 # xor c, b\nxxx10000011000100010 00000001 # xor c, c\nxxx10000011000100011 00000001 # xor c, d\nxxx10000011000100100 00000001 # xor c, e\nxxx10000011000100101 00000001 # xor c, bp\nxxx10000011000100110 00000001 # xor c, sp\nxxx10000011000110000 00000001 # xor d, a\nxxx10000011000110001 00000001 # xor d, b\nxxx10000011000110010 00000001 # xor d, c\nxxx10000011000110011 00000001 # xor d, d\nxxx10000011000110100 00000001 # xor d, e\nxxx10000011000110101 00000001 # xor d, bp\nxxx10000011000110110 00000001 # xor d, sp\nxxx10000011001000000 00000001 # xor e, a\nxxx10000011001000001 00000001 # xor e, b\nxxx10000011001000010 00000001 # xor e, c\nxxx10000011001000011 00000001 # xor e, d\nxxx10000011001000100 00000001 # xor e, e\nxxx10000011001000101 00000001 # xor e, bp\nxxx10000011001000110 00000001 # xor e, sp\nxxx10000011001010000 00000001 # xor bp, a\nxxx10000011001010001 00000001 # xor bp, b\nxxx10000011001010010 00000001 # xor bp, c\nxxx10000011001010011 00000001 # xor bp, d\nxxx10000011001010100 00000001 # xor bp, e\nxxx10000011001010101 00000001 # xor bp, bp\nxxx10000011001010110 00000001 # xor bp, sp\nxxx10000011001100000 00000001 # xor sp, a\nxxx10000011001100001 00000001 # xor sp, b\nxxx10000011001100010 00000001 # xor sp, c\nxxx10000011001100011 00000001 # xor sp, d\nxxx10000011001100100 00000001 # xor sp, e\nxxx10000011001100101 00000001 # xor sp, bp\nxxx10000011001100110 00000001 # xor sp, sp\nxxx10000011100000000 00000001 # shr a, a\nxxx10000011100000001 00000001 # shr a, b\nxxx10000011100000010 00000001 # shr a, c\nxxx10000011100000011 00000001 # shr a, d\nxxx10000011100000100 00000001 # shr a, e\nxxx10000011100000101 00000001 # shr a, bp\nxxx10000011100000110 00000001 # shr a, sp\nxxx10000011100010000 00000001 # shr b, a\nxxx10000011100010001 00000001 # shr b, b\nxxx10000011100010010 00000001 # shr b, c\nxxx10000011100010011 00000001 # shr b, d\nxxx10000011100010100 00000001 # shr b, e\nxxx10000011100010101 00000001 # shr b, bp\nxxx10000011100010110 00000001 # shr b, sp\nxxx10000011100100000 00000001 # shr c, a\nxxx10000011100100001 00000001 # shr c, b\nxxx10000011100100010 00000001 # shr c, c\nxxx10000011100100011 00000001 # shr c, d\nxxx10000011100100100 00000001 # shr c, e\nxxx10000011100100101 00000001 # shr c, bp\nxxx10000011100100110 00000001 # shr c, sp\nxxx10000011100110000 00000001 # shr d, a\nxxx10000011100110001 00000001 # shr d, b\nxxx10000011100110010 00000001 # shr d, c\nxxx10000011100110011 00000001 # shr d, d\nxxx10000011100110100 00000001 # shr d, e\nxxx10000011100110101 00000001 # shr d, bp\nxxx10000011100110110 00000001 # shr d, sp\nxxx10000011101000000 00000001 # shr e, a\nxxx10000011101000001 00000001 # shr e, b\nxxx10000011101000010 00000001 # shr e, c\nxxx10000011101000011 00000001 # shr e, d\nxxx10000011101000100 00000001 # shr e, e\nxxx10000011101000101 00000001 # shr e, bp\nxxx10000011101000110 00000001 # shr e, sp\nxxx10000011101010000 00000001 # shr bp, a\nxxx10000011101010001 00000001 # shr bp, b\nxxx10000011101010010 00000001 # shr bp, c\nxxx10000011101010011 00000001 # shr bp, d\nxxx10000011101010100 00000001 # shr bp, e\nxxx10000011101010101 00000001 # shr bp, bp\nxxx10000011101010110 00000001 # shr bp, sp\nxxx10000011101100000 00000001 # shr sp, a\nxxx10000011101100001 00000001 # shr sp, b\nxxx10000011101100010 00000001 # shr sp, c\nxxx10000011101100011 00000001 # shr sp, d\nxxx10000011101100100 00000001 # shr sp, e\nxxx10000011101100101 00000001 # shr sp, bp\nxxx10000011101100110 00000001 # shr sp, sp\nxxx10000000000001111 00000001 # add a, opd\nxxx10000000000011111 00000001 # add b, opd\nxxx10000000000101111 00000001 # add c, opd\nxxx10000000000111111 00000001 # add d, opd\nxxx10000000001001111 00000001 # add e, opd\nxxx10000000001011111 00000001 # add bp, opd\nxxx10000000001101111 00000001 # add sp, opd\nxxx10000000100001111 00000001 # sub a, opd\nxxx10000000100011111 00000001 # sub b, opd\nxxx10000000100101111 00000001 # sub c, opd\nxxx10000000100111111 00000001 # sub d, opd\nxxx10000000101001111 00000001 # sub e, opd\nxxx10000000101011111 00000001 # sub bp, opd\nxxx10000000101101111 00000001 # sub sp, opd\nxxx10000001000001111 00000001 # mul a, opd\nxxx10000001000011111 00000001 # mul b, opd\nxxx10000001000101111 00000001 # mul c, opd\nxxx10000001000111111 00000001 # mul d, opd\nxxx10000001001001111 00000001 # mul e, opd\nxxx10000001001011111 00000001 # mul bp, opd\nxxx10000001001101111 00000001 # mul sp, opd\nxxx10000001100001111 00000001 # and a, opd\nxxx10000001100011111 00000001 # and b, opd\nxxx10000001100101111 00000001 # and c, opd\nxxx10000001100111111 00000001 # and d, opd\nxxx10000001101001111 00000001 # and e, opd\nxxx10000001101011111 00000001 # and bp, opd\nxxx10000001101101111 00000001 # and sp, opd\nxxx10000010000001111 00000001 # or a, opd\nxxx10000010000011111 00000001 # or b, opd\nxxx10000010000101111 00000001 # or c, opd\nxxx10000010000111111 00000001 # or d, opd\nxxx10000010001001111 00000001 # or e, opd\nxxx10000010001011111 00000001 # or bp, opd\nxxx10000010001101111 00000001 # or sp, opd\nxxx10000011000001111 00000001 # xor a, opd\nxxx10000011000011111 00000001 # xor b, opd\nxxx10000011000101111 00000001 # xor c, opd\nxxx10000011000111111 00000001 # xor d, opd\nxxx10000011001001111 00000001 # xor e, opd\nxxx10000011001011111 00000001 # xor bp, opd\nxxx10000011001101111 00000001 # xor sp, opd\nxxx10000011100001111 00000001 # shr a, opd\nxxx10000011100011111 00000001 # shr b, opd\nxxx10000011100101111 00000001 # shr c, opd\nxxx10000011100111111 00000001 # shr d, opd\nxxx10000011101001111 00000001 # shr e, opd\nxxx10000011101011111 00000001 # shr bp, opd\nxxx10000011101101111 00000001 # shr sp, opd\nxxx10000000000001001 00000000 # add a, [memaddr+opd]\nxxx10000000000011001 00000000 # add b, [memaddr+opd]\nxxx10000000000101001 00000000 # add c, [memaddr+opd]\nxxx10000000000111001 00000000 # add d, [memaddr+opd]\nxxx10000000001001001 00000000 # add e, [memaddr+opd]\nxxx10000000001011001 00000000 # add bp, [memaddr+opd]\nxxx10000000001101001 00000000 # add sp, [memaddr+opd]\nxxx10000000000001001 00000000 # add a, [memaddr+opd]\nxxx10000000000011001 00000000 # add b, [memaddr+opd]\nxxx10000000000101001 00000000 # add c, [memaddr+opd]\nxxx10000000000111001 00000000 # add d, [memaddr+opd]\nxxx10000000001001001 00000000 # add e, [memaddr+opd]\nxxx10000000001011001 00000000 # add bp, [memaddr+opd]\nxxx10000000001101001 00000000 # add sp, [memaddr+opd]\nxxx10000000100001001 00000000 # sub a, [memaddr+opd]\nxxx10000000100011001 00000000 # sub b, [memaddr+opd]\nxxx10000000100101001 00000000 # sub c, [memaddr+opd]\nxxx10000000100111001 00000000 # sub d, [memaddr+opd]\nxxx10000000101001001 00000000 # sub e, [memaddr+opd]\nxxx10000000101011001 00000000 # sub bp, [memaddr+opd]\nxxx10000000101101001 00000000 # sub sp, [memaddr+opd]\nxxx10000000100001001 00000000 # sub a, [memaddr+opd]\nxxx10000000100011001 00000000 # sub b, [memaddr+opd]\nxxx10000000100101001 00000000 # sub c, [memaddr+opd]\nxxx10000000100111001 00000000 # sub d, [memaddr+opd]\nxxx10000000101001001 00000000 # sub e, [memaddr+opd]\nxxx10000000101011001 00000000 # sub bp, [memaddr+opd]\nxxx10000000101101001 00000000 # sub sp, [memaddr+opd]\nxxx10000001000001001 00000000 # mul a, [memaddr+opd]\nxxx10000001000011001 00000000 # mul b, [memaddr+opd]\nxxx10000001000101001 00000000 # mul c, [memaddr+opd]\nxxx10000001000111001 00000000 # mul d, [memaddr+opd]\nxxx10000001001001001 00000000 # mul e, [memaddr+opd]\nxxx10000001001011001 00000000 # mul bp, [memaddr+opd]\nxxx10000001001101001 00000000 # mul sp, [memaddr+opd]\nxxx10000001000001001 00000000 # mul a, [memaddr+opd]\nxxx10000001000011001 00000000 # mul b, [memaddr+opd]\nxxx10000001000101001 00000000 # mul c, [memaddr+opd]\nxxx10000001000111001 00000000 # mul d, [memaddr+opd]\nxxx10000001001001001 00000000 # mul e, [memaddr+opd]\nxxx10000001001011001 00000000 # mul bp, [memaddr+opd]\nxxx10000001001101001 00000000 # mul sp, [memaddr+opd]\nxxx10000001100001001 00000000 # and a, [memaddr+opd]\nxxx10000001100011001 00000000 # and b, [memaddr+opd]\nxxx10000001100101001 00000000 # and c, [memaddr+opd]\nxxx10000001100111001 00000000 # and d, [memaddr+opd]\nxxx10000001101001001 00000000 # and e, [memaddr+opd]\nxxx10000001101011001 00000000 # and bp, [memaddr+opd]\nxxx10000001101101001 00000000 # and sp, [memaddr+opd]\nxxx10000001100001001 00000000 # and a, [memaddr+opd]\nxxx10000001100011001 00000000 # and b, [memaddr+opd]\nxxx10000001100101001 00000000 # and c, [memaddr+opd]\nxxx10000001100111001 00000000 # and d, [memaddr+opd]\nxxx10000001101001001 00000000 # and e, [memaddr+opd]\nxxx10000001101011001 00000000 # and bp, [memaddr+opd]\nxxx10000001101101001 00000000 # and sp, [memaddr+opd]\nxxx10000010000001001 00000000 # or a, [memaddr+opd]\nxxx10000010000011001 00000000 # or b, [memaddr+opd]\nxxx10000010000101001 00000000 # or c, [memaddr+opd]\nxxx10000010000111001 00000000 # or d, [memaddr+opd]\nxxx10000010001001001 00000000 # or e, [memaddr+opd]\nxxx10000010001011001 00000000 # or bp, [memaddr+opd]\nxxx10000010001101001 00000000 # or sp, [memaddr+opd]\nxxx10000010000001001 00000000 # or a, [memaddr+opd]\nxxx10000010000011001 00000000 # or b, [memaddr+opd]\nxxx10000010000101001 00000000 # or c, [memaddr+opd]\nxxx10000010000111001 00000000 # or d, [memaddr+opd]\nxxx10000010001001001 00000000 # or e, [memaddr+opd]\nxxx10000010001011001 00000000 # or bp, [memaddr+opd]\nxxx10000010001101001 00000000 # or sp, [memaddr+opd]\nxxx10000011000001001 00000000 # xor a, [memaddr+opd]\nxxx10000011000011001 00000000 # xor b, [memaddr+opd]\nxxx10000011000101001 00000000 # xor c, [memaddr+opd]\nxxx10000011000111001 00000000 # xor d, [memaddr+opd]\nxxx10000011001001001 00000000 # xor e, [memaddr+opd]\nxxx10000011001011001 00000000 # xor bp, [memaddr+opd]\nxxx10000011001101001 00000000 # xor sp, [memaddr+opd]\nxxx10000011000001001 00000000 # xor a, [memaddr+opd]\nxxx10000011000011001 00000000 # xor b, [memaddr+opd]\nxxx10000011000101001 00000000 # xor c, [memaddr+opd]\nxxx10000011000111001 00000000 # xor d, [memaddr+opd]\nxxx10000011001001001 00000000 # xor e, [memaddr+opd]\nxxx10000011001011001 00000000 # xor bp, [memaddr+opd]\nxxx10000011001101001 00000000 # xor sp, [memaddr+opd]\nxxx10000011100001001 00000000 # shr a, [memaddr+opd]\nxxx10000011100011001 00000000 # shr b, [memaddr+opd]\nxxx10000011100101001 00000000 # shr c, [memaddr+opd]\nxxx10000011100111001 00000000 # shr d, [memaddr+opd]\nxxx10000011101001001 00000000 # shr e, [memaddr+opd]\nxxx10000011101011001 00000000 # shr bp, [memaddr+opd]\nxxx10000011101101001 00000000 # shr sp, [memaddr+opd]\nxxx10000011100001001 00000000 # shr a, [memaddr+opd]\nxxx10000011100011001 00000000 # shr b, [memaddr+opd]\nxxx10000011100101001 00000000 # shr c, [memaddr+opd]\nxxx10000011100111001 00000000 # shr d, [memaddr+opd]\nxxx10000011101001001 00000000 # shr e, [memaddr+opd]\nxxx10000011101011001 00000000 # shr bp, [memaddr+opd]\nxxx10000011101101001 00000000 # shr sp, [memaddr+opd]\nxxx10000000010111111 00000001 # add memval,opd\nxxx10000010100001111 00000001 # not a\nxxx10000010100011111 00000001 # not b\nxxx10000010100101111 00000001 # not c\nxxx10000010100111111 00000001 # not d\nxxx10000010101001111 00000001 # not e\nxxx10000010101011111 00000001 # not bp\nxxx10000010101101111 00000001 # not sp\nxxx10000100000000000 00000001 # mov a, a\nxxx10000100000000001 00000001 # mov a, b\nxxx10000100000000010 00000001 # mov a, c\nxxx10000100000000011 00000001 # mov a, d\nxxx10000100000000100 00000001 # mov a, e\nxxx10000100000000101 00000001 # mov a, bp\nxxx10000100000000110 00000001 # mov a, sp\nxxx10000100000010000 00000001 # mov b, a\nxxx10000100000010001 00000001 # mov b, b\nxxx10000100000010010 00000001 # mov b, c\nxxx10000100000010011 00000001 # mov b, d\nxxx10000100000010100 00000001 # mov b, e\nxxx10000100000010101 00000001 # mov b, bp\nxxx10000100000010110 00000001 # mov b, sp\nxxx10000100000100000 00000001 # mov c, a\nxxx10000100000100001 00000001 # mov c, b\nxxx10000100000100010 00000001 # mov c, c\nxxx10000100000100011 00000001 # mov c, d\nxxx10000100000100100 00000001 # mov c, e\nxxx10000100000100101 00000001 # mov c, bp\nxxx10000100000100110 00000001 # mov c, sp\nxxx10000100000110000 00000001 # mov d, a\nxxx10000100000110001 00000001 # mov d, b\nxxx10000100000110010 00000001 # mov d, c\nxxx10000100000110011 00000001 # mov d, d\nxxx10000100000110100 00000001 # mov d, e\nxxx10000100000110101 00000001 # mov d, bp\nxxx10000100000110110 00000001 # mov d, sp\nxxx10000100001000000 00000001 # mov e, a\nxxx10000100001000001 00000001 # mov e, b\nxxx10000100001000010 00000001 # mov e, c\nxxx10000100001000011 00000001 # mov e, d\nxxx10000100001000100 00000001 # mov e, e\nxxx10000100001000101 00000001 # mov e, bp\nxxx10000100001000110 00000001 # mov e, sp\nxxx10000100001010000 00000001 # mov bp, a\nxxx10000100001010001 00000001 # mov bp, b\nxxx10000100001010010 00000001 # mov bp, c\nxxx10000100001010011 00000001 # mov bp, d\nxxx10000100001010100 00000001 # mov bp, e\nxxx10000100001010101 00000001 # mov bp, bp\nxxx10000100001010110 00000001 # mov bp, sp\nxxx10000100001100000 00000001 # mov sp, a\nxxx10000100001100001 00000001 # mov sp, b\nxxx10000100001100010 00000001 # mov sp, c\nxxx10000100001100011 00000001 # mov sp, d\nxxx10000100001100100 00000001 # mov sp, e\nxxx10000100001100101 00000001 # mov sp, bp\nxxx10000100001100110 00000001 # mov sp, sp\nxxx10000100000001001 00000000 # mov a, [memaddr+opd]\nxxx10000100000011001 00000000 # mov b, [memaddr+opd]\nxxx10000100000101001 00000000 # mov c, [memaddr+opd]\nxxx10000100000111001 00000000 # mov d, [memaddr+opd]\nxxx10000100001001001 00000000 # mov e, [memaddr+opd]\nxxx10000100001011001 00000000 # mov bp, [memaddr+opd]\nxxx10000100001101001 00000000 # mov sp, [memaddr+opd]\nxxx10000100000001001 00000000 # mov a, [memaddr+opd]\nxxx10000100000011001 00000000 # mov b, [memaddr+opd]\nxxx10000100000101001 00000000 # mov c, [memaddr+opd]\nxxx10000100000111001 00000000 # mov d, [memaddr+opd]\nxxx10000100001001001 00000000 # mov e, [memaddr+opd]\nxxx10000100001011001 00000000 # mov bp, [memaddr+opd]\nxxx10000100001101001 00000000 # mov sp, [memaddr+opd]\nxxx10000100010111001 00000000 # mov memval, [memaddr+opd]\nxxx10000100010100000 00000001 # mov memaddr,a\nxxx10000100010100001 00000001 # mov memaddr,b\nxxx10000100010100010 00000001 # mov memaddr,c\nxxx10000100010100011 00000001 # mov memaddr,d\nxxx10000100010100100 00000001 # mov memaddr,e\nxxx10000100010100101 00000001 # mov memaddr,bp\nxxx10000100010100110 00000001 # mov memaddr,sp\nxxx10000100010110000 00000001 # mov memval,a\nxxx10000100010110001 00000001 # mov memval,b\nxxx10000100010110010 00000001 # mov memval,c\nxxx10000100010110011 00000001 # mov memval,d\nxxx10000100010110100 00000001 # mov memval,e\nxxx10000100010110101 00000001 # mov memval,bp\nxxx10000100010110110 00000001 # mov memval,sp\nxxx10000100010101010 00000000 # mov [memaddr+opd],memval\nxxx10000100010101111 00000001 # mov memaddr, opd\nxxx10000100010111111 00000001 # mov memval, opd\nxxx10000100000001111 00000001 # mov a, opd\nxxx10000100000011111 00000001 # mov b, opd\nxxx10000100000101111 00000001 # mov c, opd\nxxx10000100000111111 00000001 # mov d, opd\nxxx10000100001001111 00000001 # mov e, opd\nxxx10000100001011111 00000001 # mov bp, opd\nxxx10000100001101111 00000001 # mov sp, opd\nxxx10000100100001111 00000001 # in a\nxxx10000100100011111 00000001 # in b\nxxx10000100100101111 00000001 # in c\nxxx10000100100111111 00000001 # in d\nxxx10000100101001111 00000001 # in e\nxxx10000100101011111 00000001 # in bp\nxxx10000100101101111 00000001 # in sp\nxxx10000101000001111 00000001 # out a\nxxx10000101000011111 00000001 # out b\nxxx10000101000101111 00000001 # out c\nxxx10000101000111111 00000001 # out d\nxxx10000101001001111 00000001 # out e\nxxx10000101001011111 00000001 # out bp\nxxx10000101001101111 00000001 # out sp\nxxx10000101011111111 00000001 # out opd\nxxx10001001000000000 00000001 # cmp a, a\nxxx10001001000000001 00000001 # cmp a, b\nxxx10001001000000010 00000001 # cmp a, c\nxxx10001001000000011 00000001 # cmp a, d\nxxx10001001000000100 00000001 # cmp a, e\nxxx10001001000000101 00000001 # cmp a, bp\nxxx10001001000000110 00000001 # cmp a, sp\nxxx10001001000010000 00000001 # cmp b, a\nxxx10001001000010001 00000001 # cmp b, b\nxxx10001001000010010 00000001 # cmp b, c\nxxx10001001000010011 00000001 # cmp b, d\nxxx10001001000010100 00000001 # cmp b, e\nxxx10001001000010101 00000001 # cmp b, bp\nxxx10001001000010110 00000001 # cmp b, sp\nxxx10001001000100000 00000001 # cmp c, a\nxxx10001001000100001 00000001 # cmp c, b\nxxx10001001000100010 00000001 # cmp c, c\nxxx10001001000100011 00000001 # cmp c, d\nxxx10001001000100100 00000001 # cmp c, e\nxxx10001001000100101 00000001 # cmp c, bp\nxxx10001001000100110 00000001 # cmp c, sp\nxxx10001001000110000 00000001 # cmp d, a\nxxx10001001000110001 00000001 # cmp d, b\nxxx10001001000110010 00000001 # cmp d, c\nxxx10001001000110011 00000001 # cmp d, d\nxxx10001001000110100 00000001 # cmp d, e\nxxx10001001000110101 00000001 # cmp d, bp\nxxx10001001000110110 00000001 # cmp d, sp\nxxx10001001001000000 00000001 # cmp e, a\nxxx10001001001000001 00000001 # cmp e, b\nxxx10001001001000010 00000001 # cmp e, c\nxxx10001001001000011 00000001 # cmp e, d\nxxx10001001001000100 00000001 # cmp e, e\nxxx10001001001000101 00000001 # cmp e, bp\nxxx10001001001000110 00000001 # cmp e, sp\nxxx10001001001010000 00000001 # cmp bp, a\nxxx10001001001010001 00000001 # cmp bp, b\nxxx10001001001010010 00000001 # cmp bp, c\nxxx10001001001010011 00000001 # cmp bp, d\nxxx10001001001010100 00000001 # cmp bp, e\nxxx10001001001010101 00000001 # cmp bp, bp\nxxx10001001001010110 00000001 # cmp bp, sp\nxxx10001001001100000 00000001 # cmp sp, a\nxxx10001001001100001 00000001 # cmp sp, b\nxxx10001001001100010 00000001 # cmp sp, c\nxxx10001001001100011 00000001 # cmp sp, d\nxxx10001001001100100 00000001 # cmp sp, e\nxxx10001001001100101 00000001 # cmp sp, bp\nxxx10001001001100110 00000001 # cmp sp, sp\nxxx10001001000001111 00000001 # cmp a, opd\nxxx10001001000011111 00000001 # cmp b, opd\nxxx10001001000101111 00000001 # cmp c, opd\nxxx10001001000111111 00000001 # cmp d, opd\nxxx10001001001001111 00000001 # cmp e, opd\nxxx10001001001011111 00000001 # cmp bp, opd\nxxx10001001001101111 00000001 # cmp sp, opd\nxxx10001000110111111 00000000 # jmp memval\n0xx10000101100001111 00000000 # jnc a (Taken)\n0xx10000101100011111 00000000 # jnc b (Taken)\n0xx10000101100101111 00000000 # jnc c (Taken)\n0xx10000101100111111 00000000 # jnc d (Taken)\n0xx10000101101001111 00000000 # jnc e (Taken)\n0xx10000101101011111 00000000 # jnc bp (Taken)\n0xx10000101101101111 00000000 # jnc sp (Taken)\n1xx10000101100001111 00000001 # jnc a (Skip)\n1xx10000101100011111 00000001 # jnc b (Skip)\n1xx10000101100101111 00000001 # jnc c (Skip)\n1xx10000101100111111 00000001 # jnc d (Skip)\n1xx10000101101001111 00000001 # jnc e (Skip)\n1xx10000101101011111 00000001 # jnc bp (Skip)\n1xx10000101101101111 00000001 # jnc sp (Skip)\n1xx10000110000001111 00000000 # jc a (Taken)\n1xx10000110000011111 00000000 # jc b (Taken)\n1xx10000110000101111 00000000 # jc c (Taken)\n1xx10000110000111111 00000000 # jc d (Taken)\n1xx10000110001001111 00000000 # jc e (Taken)\n1xx10000110001011111 00000000 # jc bp (Taken)\n1xx10000110001101111 00000000 # jc sp (Taken)\n0xx10000110000001111 00000001 # jc a (Skip)\n0xx10000110000011111 00000001 # jc b (Skip)\n0xx10000110000101111 00000001 # jc c (Skip)\n0xx10000110000111111 00000001 # jc d (Skip)\n0xx10000110001001111 00000001 # jc e (Skip)\n0xx10000110001011111 00000001 # jc bp (Skip)\n0xx10000110001101111 00000001 # jc sp (Skip)\nx0x10000110100001111 00000000 # jnz a (Taken)\nx0x10000110100011111 00000000 # jnz b (Taken)\nx0x10000110100101111 00000000 # jnz c (Taken)\nx0x10000110100111111 00000000 # jnz d (Taken)\nx0x10000110101001111 00000000 # jnz e (Taken)\nx0x10000110101011111 00000000 # jnz bp (Taken)\nx0x10000110101101111 00000000 # jnz sp (Taken)\nx1x10000110100001111 00000001 # jnz a (Skip)\nx1x10000110100011111 00000001 # jnz b (Skip)\nx1x10000110100101111 00000001 # jnz c (Skip)\nx1x10000110100111111 00000001 # jnz d (Skip)\nx1x10000110101001111 00000001 # jnz e (Skip)\nx1x10000110101011111 00000001 # jnz bp (Skip)\nx1x10000110101101111 00000001 # jnz sp (Skip)\nx1x10000111000001111 00000000 # jz a (Taken)\nx1x10000111000011111 00000000 # jz b (Taken)\nx1x10000111000101111 00000000 # jz c (Taken)\nx1x10000111000111111 00000000 # jz d (Taken)\nx1x10000111001001111 00000000 # jz e (Taken)\nx1x10000111001011111 00000000 # jz bp (Taken)\nx1x10000111001101111 00000000 # jz sp (Taken)\nx0x10000111000001111 00000001 # jz a (Skip)\nx0x10000111000011111 00000001 # jz b (Skip)\nx0x10000111000101111 00000001 # jz c (Skip)\nx0x10000111000111111 00000001 # jz d (Skip)\nx0x10000111001001111 00000001 # jz e (Skip)\nx0x10000111001011111 00000001 # jz bp (Skip)\nx0x10000111001101111 00000001 # jz sp (Skip)\nxx010000111100001111 00000000 # jns a (Taken)\nxx010000111100011111 00000000 # jns b (Taken)\nxx010000111100101111 00000000 # jns c (Taken)\nxx010000111100111111 00000000 # jns d (Taken)\nxx010000111101001111 00000000 # jns e (Taken)\nxx010000111101011111 00000000 # jns bp (Taken)\nxx010000111101101111 00000000 # jns sp (Taken)\nxx110000111100001111 00000001 # jns a (Skip)\nxx110000111100011111 00000001 # jns b (Skip)\nxx110000111100101111 00000001 # jns c (Skip)\nxx110000111100111111 00000001 # jns d (Skip)\nxx110000111101001111 00000001 # jns e (Skip)\nxx110000111101011111 00000001 # jns bp (Skip)\nxx110000111101101111 00000001 # jns sp (Skip)\nxx110001000000001111 00000000 # js a (Taken)\nxx110001000000011111 00000000 # js b (Taken)\nxx110001000000101111 00000000 # js c (Taken)\nxx110001000000111111 00000000 # js d (Taken)\nxx110001000001001111 00000000 # js e (Taken)\nxx110001000001011111 00000000 # js bp (Taken)\nxx110001000001101111 00000000 # js sp (Taken)\nxx010001000000001111 00000001 # js a (Skip)\nxx010001000000011111 00000001 # js b (Skip)\nxx010001000000101111 00000001 # js c (Skip)\nxx010001000000111111 00000001 # js d (Skip)\nxx010001000001001111 00000001 # js e (Skip)\nxx010001000001011111 00000001 # js bp (Skip)\nxx010001000001101111 00000001 # js sp (Skip)\nxxx10001000100001111 00000000 # jmp a\nxxx10001000100011111 00000000 # jmp b\nxxx10001000100101111 00000000 # jmp c\nxxx10001000100111111 00000000 # jmp d\nxxx10001000101001111 00000000 # jmp e\nxxx10001000101011111 00000000 # jmp bp\nxxx10001000101101111 00000000 # jmp sp\nx1x10001011000001111 00000000 # je a (Taken)\nx1x10001011000011111 00000000 # je b (Taken)\nx1x10001011000101111 00000000 # je c (Taken)\nx1x10001011000111111 00000000 # je d (Taken)\nx1x10001011001001111 00000000 # je e (Taken)\nx1x10001011001011111 00000000 # je bp (Taken)\nx1x10001011001101111 00000000 # je sp (Taken)\nx0x10001011000001111 00000001 # je a (Skip)\nx0x10001011000011111 00000001 # je b (Skip)\nx0x10001011000101111 00000001 # je c (Skip)\nx0x10001011000111111 00000001 # je d (Skip)\nx0x10001011001001111 00000001 # je e (Skip)\nx0x10001011001011111 00000001 # je bp (Skip)\nx0x10001011001101111 00000001 # je sp (Skip)\nx0x10001011100001111 00000000 # jne a(Taken)\nx0x10001011100011111 00000000 # jne b(Taken)\nx0x10001011100101111 00000000 # jne c(Taken)\nx0x10001011100111111 00000000 # jne d(Taken)\nx0x10001011101001111 00000000 # jne e(Taken)\nx0x10001011101011111 00000000 # jne bp(Taken)\nx0x10001011101101111 00000000 # jne sp(Taken)\nx1x10001011100001111 00000001 # jne a(Skip)\nx1x10001011100011111 00000001 # jne b(Skip)\nx1x10001011100101111 00000001 # jne c(Skip)\nx1x10001011100111111 00000001 # jne d(Skip)\nx1x10001011101001111 00000001 # jne e(Skip)\nx1x10001011101011111 00000001 # jne bp(Skip)\nx1x10001011101101111 00000001 # jne sp(Skip)\nx0010001100000001111 00000000 # ja a (Taken)\nx0010001100000011111 00000000 # ja b (Taken)\nx0010001100000101111 00000000 # ja c (Taken)\nx0010001100000111111 00000000 # ja d (Taken)\nx0010001100001001111 00000000 # ja e (Taken)\nx0010001100001011111 00000000 # ja bp (Taken)\nx0010001100001101111 00000000 # ja sp (Taken)\nxxx10001100000001111 00000001 # ja a (Skip)\nxxx10001100000011111 00000001 # ja b (Skip)\nxxx10001100000101111 00000001 # ja c (Skip)\nxxx10001100000111111 00000001 # ja d (Skip)\nxxx10001100001001111 00000001 # ja e (Skip)\nxxx10001100001011111 00000001 # ja bp (Skip)\nxxx10001100001101111 00000001 # ja sp (Skip)\nx0010001100100001111 00000000 # jae a (Taken)\nx0010001100100011111 00000000 # jae b (Taken)\nx0010001100100101111 00000000 # jae c (Taken)\nx0010001100100111111 00000000 # jae d (Taken)\nx0010001100101001111 00000000 # jae e (Taken)\nx0010001100101011111 00000000 # jae bp (Taken)\nx0010001100101101111 00000000 # jae sp (Taken)\nx1010001100100001111 00000000 # jae a (Taken)\nx1010001100100011111 00000000 # jae b (Taken)\nx1010001100100101111 00000000 # jae c (Taken)\nx1010001100100111111 00000000 # jae d (Taken)\nx1010001100101001111 00000000 # jae e (Taken)\nx1010001100101011111 00000000 # jae bp (Taken)\nx1010001100101101111 00000000 # jae sp (Taken)\nxxx10001100100001111 00000001 # jae a (Skip)\nxxx10001100100011111 00000001 # jae b (Skip)\nxxx10001100100101111 00000001 # jae c (Skip)\nxxx10001100100111111 00000001 # jae d (Skip)\nxxx10001100101001111 00000001 # jae e (Skip)\nxxx10001100101011111 00000001 # jae bp (Skip)\nxxx10001100101101111 00000001 # jae sp (Skip)\nx0110001101000001111 00000000 # jl a (Taken)\nx0110001101000011111 00000000 # jl b (Taken)\nx0110001101000101111 00000000 # jl c (Taken)\nx0110001101000111111 00000000 # jl d (Taken)\nx0110001101001001111 00000000 # jl e (Taken)\nx0110001101001011111 00000000 # jl bp (Taken)\nx0110001101001101111 00000000 # jl sp (Taken)\nxxx10001101000001111 00000001 # jl a (Skip)\nxxx10001101000011111 00000001 # jl b (Skip)\nxxx10001101000101111 00000001 # jl c (Skip)\nxxx10001101000111111 00000001 # jl d (Skip)\nxxx10001101001001111 00000001 # jl e (Skip)\nxxx10001101001011111 00000001 # jl bp (Skip)\nxxx10001101001101111 00000001 # jl sp (Skip)\nx0110001101100001111 00000000 # jle a (Taken)\nx0110001101100011111 00000000 # jle b (Taken)\nx0110001101100101111 00000000 # jle c (Taken)\nx0110001101100111111 00000000 # jle d (Taken)\nx0110001101101001111 00000000 # jle e (Taken)\nx0110001101101011111 00000000 # jle bp (Taken)\nx0110001101101101111 00000000 # jle sp (Taken)\nx1010001101100001111 00000000 # jle a (Taken)\nx1010001101100011111 00000000 # jle b (Taken)\nx1010001101100101111 00000000 # jle c (Taken)\nx1010001101100111111 00000000 # jle d (Taken)\nx1010001101101001111 00000000 # jle e (Taken)\nx1010001101101011111 00000000 # jle bp (Taken)\nx1010001101101101111 00000000 # jle sp (Taken)\nxxx10001101100001111 00000001 # jle a (Skip)\nxxx10001101100011111 00000001 # jle b (Skip)\nxxx10001101100101111 00000001 # jle c (Skip)\nxxx10001101100111111 00000001 # jle d (Skip)\nxxx10001101101001111 00000001 # jle e (Skip)\nxxx10001101101011111 00000001 # jle bp (Skip)")) IIRND (
    .in({carry_flag, zero_flag, sign_flag, or_4_out[16], Instruction_Register_p6}), .out(IIRND_out));
  Comparator #(.mode("unsigned")) comparator_2 (
    .a(IDSC_q), .b(8'h2), .gt(comparator_2_gt), .eq(comparator_2_eq));  // open: lt
  or or_4 (or_4_out[16], comparator_2_gt, comparator_2_eq);
  Comparator #(.mode("unsigned")) comparator_3 (.a(8'h1), .b(IDSC_q), .eq(comparator_3_eq));  // open: gt, lt
  or or_5 (or_5_out, IDSC_q[0], IDSC_q[1], IDSC_q[2], IDSC_q[3], IDSC_q[4], IDSC_q[5], IDSC_q[6], IDSC_q[7]);
  Subtractor subtractor_1 (.a(IDSC_q), .b(8'h2), .out(subtractor_1_out));  // open: bin, bout
  Multiplexer #(.width(16)) multiplexer_5 (
    .in0(Instruction_Register_p5), .in1(MOR_q), .out(operand), .sel(multiplexer_6_out[20]));
  PLA #(.in_width(20), .out_width(16), .\table ("xxx0xxxxxxxxxxxxxxxx 0000000000000000 # IE=0 (during fetch)\n0xx10000101111111111 0000000000000001 # jnc opd (Taken)\n1xx10000101111111111 0000000000000010 # jnc opd (Skip)\n1xx10000110011111111 0000000000000011 # jc opd (Taken)\n0xx10000110011111111 0000000000000100 # jc opd (Skip)\nx0x10000110111111111 0000000000000101 # jnz opd (Taken)\nx1x10000110111111111 0000000000000110 # jnz opd (Skip)\nx1x10000111011111111 0000000000000111 # jz opd (Taken)\nx0x10000111011111111 0000000000001000 # jz opd (Skip)\nxx010000111111111111 0000000000001001 # jns opd (Taken)\nxx110000111111111111 0000000000001010 # jns opd (Skip)\nxx110001000011111111 0000000000001011 # js opd (Taken)\nxx010001000011111111 0000000000001100 # js opd (Skip)\nxxx10001000111111111 0000000000001101 # jmp opd\nx1x10001011011111111 0000000000001110 # je opd (Taken)\nx0x10001011011111111 0000000000001111 # je opd (Skip)\nx0x10001011111111111 0000000000010000 # jne opd(Taken)\nx1x10001011111111111 0000000000010001 # jne opd(Skip)\nx0010001100011111111 0000000000010010 # ja opd (Taken)\nxxx10001100011111111 0000000000010011 # ja opd (Skip)\nx0010001100111111111 0000000000010100 # jae opd (Taken)\nx1010001100111111111 0000000000010101 # jae opd (Taken)\nxxx10001100111111111 0000000000010110 # jae opd (Skip)\nx0110001101011111111 0000000000010111 # jl opd (Taken)\nxxx10001101011111111 0000000000011000 # jl opd (Skip)\nx0110001101111111111 0000000000011001 # jle opd (Taken)\nx1010001101111111111 0000000000011010 # jle opd (Taken)\nxxx10001101111111111 0000000000011011 # jle opd (Skip)\nxxx10001001111111111 0000000000011100 # hlt\nxxx10001010011111111 0000000000011101 # nop\nxxxx1111111111111111 0000000000011110 # invaild\nxxx10001010111111111 0000000000011111 # lpc\nxxx10000000000000000 0000000000100000 # add a, a\nxxx10000000000000001 0000000000100001 # add a, b\nxxx10000000000000010 0000000000100010 # add a, c\nxxx10000000000000011 0000000000100011 # add a, d\nxxx10000000000000100 0000000000100100 # add a, e\nxxx10000000000000101 0000000000100101 # add a, bp\nxxx10000000000000110 0000000000100110 # add a, sp\nxxx10000000000010000 0000000000100111 # add b, a\nxxx10000000000010001 0000000000101000 # add b, b\nxxx10000000000010010 0000000000101001 # add b, c\nxxx10000000000010011 0000000000101010 # add b, d\nxxx10000000000010100 0000000000101011 # add b, e\nxxx10000000000010101 0000000000101100 # add b, bp\nxxx10000000000010110 0000000000101101 # add b, sp\nxxx10000000000100000 0000000000101110 # add c, a\nxxx10000000000100001 0000000000101111 # add c, b\nxxx10000000000100010 0000000000110000 # add c, c\nxxx10000000000100011 0000000000110001 # add c, d\nxxx10000000000100100 0000000000110010 # add c, e\nxxx10000000000100101 0000000000110011 # add c, bp\nxxx10000000000100110 0000000000110100 # add c, sp\nxxx10000000000110000 0000000000110101 # add d, a\nxxx10000000000110001 0000000000110110 # add d, b\nxxx10000000000110010 0000000000110111 # add d, c\nxxx10000000000110011 0000000000111000 # add d, d\nxxx10000000000110100 0000000000111001 # add d, e\nxxx10000000000110101 0000000000111010 # add d, bp\nxxx10000000000110110 0000000000111011 # add d, sp\nxxx10000000001000000 0000000000111100 # add e, a\nxxx10000000001000001 0000000000111101 # add e, b\nxxx10000000001000010 0000000000111110 # add e, c\nxxx10000000001000011 0000000000111111 # add e, d\nxxx10000000001000100 0000000001000000 # add e, e\nxxx10000000001000101 0000000001000001 # add e, bp\nxxx10000000001000110 0000000001000010 # add e, sp\nxxx10000000001010000 0000000001000011 # add bp, a\nxxx10000000001010001 0000000001000100 # add bp, b\nxxx10000000001010010 0000000001000101 # add bp, c\nxxx10000000001010011 0000000001000110 # add bp, d\nxxx10000000001010100 0000000001000111 # add bp, e\nxxx10000000001010101 0000000001001000 # add bp, bp\nxxx10000000001010110 0000000001001001 # add bp, sp\nxxx10000000001100000 0000000001001010 # add sp, a\nxxx10000000001100001 0000000001001011 # add sp, b\nxxx10000000001100010 0000000001001100 # add sp, c\nxxx10000000001100011 0000000001001101 # add sp, d\nxxx10000000001100100 0000000001001110 # add sp, e\nxxx10000000001100101 0000000001001111 # add sp, bp\nxxx10000000001100110 0000000001010000 # add sp, sp\nxxx10000000100000000 0000000001010001 # sub a, a\nxxx10000000100000001 0000000001010010 # sub a, b\nxxx10000000100000010 0000000001010011 # sub a, c\nxxx10000000100000011 0000000001010100 # sub a, d\nxxx10000000100000100 0000000001010101 # sub a, e\nxxx10000000100000101 0000000001010110 # sub a, bp\nxxx10000000100000110 0000000001010111 # sub a, sp\nxxx10000000100010000 0000000001011000 # sub b, a\nxxx10000000100010001 0000000001011001 # sub b, b\nxxx10000000100010010 0000000001011010 # sub b, c\nxxx10000000100010011 0000000001011011 # sub b, d\nxxx10000000100010100 0000000001011100 # sub b, e\nxxx10000000100010101 0000000001011101 # sub b, bp\nxxx10000000100010110 0000000001011110 # sub b, sp\nxxx10000000100100000 0000000001011111 # sub c, a\nxxx10000000100100001 0000000001100000 # sub c, b\nxxx10000000100100010 0000000001100001 # sub c, c\nxxx10000000100100011 0000000001100010 # sub c, d\nxxx10000000100100100 0000000001100011 # sub c, e\nxxx10000000100100101 0000000001100100 # sub c, bp\nxxx10000000100100110 0000000001100101 # sub c, sp\nxxx10000000100110000 0000000001100110 # sub d, a\nxxx10000000100110001 0000000001100111 # sub d, b\nxxx10000000100110010 0000000001101000 # sub d, c\nxxx10000000100110011 0000000001101001 # sub d, d\nxxx10000000100110100 0000000001101010 # sub d, e\nxxx10000000100110101 0000000001101011 # sub d, bp\nxxx10000000100110110 0000000001101100 # sub d, sp\nxxx10000000101000000 0000000001101101 # sub e, a\nxxx10000000101000001 0000000001101110 # sub e, b\nxxx10000000101000010 0000000001101111 # sub e, c\nxxx10000000101000011 0000000001110000 # sub e, d\nxxx10000000101000100 0000000001110001 # sub e, e\nxxx10000000101000101 0000000001110010 # sub e, bp\nxxx10000000101000110 0000000001110011 # sub e, sp\nxxx10000000101010000 0000000001110100 # sub bp, a\nxxx10000000101010001 0000000001110101 # sub bp, b\nxxx10000000101010010 0000000001110110 # sub bp, c\nxxx10000000101010011 0000000001110111 # sub bp, d\nxxx10000000101010100 0000000001111000 # sub bp, e\nxxx10000000101010101 0000000001111001 # sub bp, bp\nxxx10000000101010110 0000000001111010 # sub bp, sp\nxxx10000000101100000 0000000001111011 # sub sp, a\nxxx10000000101100001 0000000001111100 # sub sp, b\nxxx10000000101100010 0000000001111101 # sub sp, c\nxxx10000000101100011 0000000001111110 # sub sp, d\nxxx10000000101100100 0000000001111111 # sub sp, e\nxxx10000000101100101 0000000010000000 # sub sp, bp\nxxx10000000101100110 0000000010000001 # sub sp, sp\nxxx10000001000000000 0000000010000010 # mul a, a\nxxx10000001000000001 0000000010000011 # mul a, b\nxxx10000001000000010 0000000010000100 # mul a, c\nxxx10000001000000011 0000000010000101 # mul a, d\nxxx10000001000000100 0000000010000110 # mul a, e\nxxx10000001000000101 0000000010000111 # mul a, bp\nxxx10000001000000110 0000000010001000 # mul a, sp\nxxx10000001000010000 0000000010001001 # mul b, a\nxxx10000001000010001 0000000010001010 # mul b, b\nxxx10000001000010010 0000000010001011 # mul b, c\nxxx10000001000010011 0000000010001100 # mul b, d\nxxx10000001000010100 0000000010001101 # mul b, e\nxxx10000001000010101 0000000010001110 # mul b, bp\nxxx10000001000010110 0000000010001111 # mul b, sp\nxxx10000001000100000 0000000010010000 # mul c, a\nxxx10000001000100001 0000000010010001 # mul c, b\nxxx10000001000100010 0000000010010010 # mul c, c\nxxx10000001000100011 0000000010010011 # mul c, d\nxxx10000001000100100 0000000010010100 # mul c, e\nxxx10000001000100101 0000000010010101 # mul c, bp\nxxx10000001000100110 0000000010010110 # mul c, sp\nxxx10000001000110000 0000000010010111 # mul d, a\nxxx10000001000110001 0000000010011000 # mul d, b\nxxx10000001000110010 0000000010011001 # mul d, c\nxxx10000001000110011 0000000010011010 # mul d, d\nxxx10000001000110100 0000000010011011 # mul d, e\nxxx10000001000110101 0000000010011100 # mul d, bp\nxxx10000001000110110 0000000010011101 # mul d, sp\nxxx10000001001000000 0000000010011110 # mul e, a\nxxx10000001001000001 0000000010011111 # mul e, b\nxxx10000001001000010 0000000010100000 # mul e, c\nxxx10000001001000011 0000000010100001 # mul e, d\nxxx10000001001000100 0000000010100010 # mul e, e\nxxx10000001001000101 0000000010100011 # mul e, bp\nxxx10000001001000110 0000000010100100 # mul e, sp\nxxx10000001001010000 0000000010100101 # mul bp, a\nxxx10000001001010001 0000000010100110 # mul bp, b\nxxx10000001001010010 0000000010100111 # mul bp, c\nxxx10000001001010011 0000000010101000 # mul bp, d\nxxx10000001001010100 0000000010101001 # mul bp, e\nxxx10000001001010101 0000000010101010 # mul bp, bp\nxxx10000001001010110 0000000010101011 # mul bp, sp\nxxx10000001001100000 0000000010101100 # mul sp, a\nxxx10000001001100001 0000000010101101 # mul sp, b\nxxx10000001001100010 0000000010101110 # mul sp, c\nxxx10000001001100011 0000000010101111 # mul sp, d\nxxx10000001001100100 0000000010110000 # mul sp, e\nxxx10000001001100101 0000000010110001 # mul sp, bp\nxxx10000001001100110 0000000010110010 # mul sp, sp\nxxx10000001100000000 0000000010110011 # and a, a\nxxx10000001100000001 0000000010110100 # and a, b\nxxx10000001100000010 0000000010110101 # and a, c\nxxx10000001100000011 0000000010110110 # and a, d\nxxx10000001100000100 0000000010110111 # and a, e\nxxx10000001100000101 0000000010111000 # and a, bp\nxxx10000001100000110 0000000010111001 # and a, sp\nxxx10000001100010000 0000000010111010 # and b, a\nxxx10000001100010001 0000000010111011 # and b, b\nxxx10000001100010010 0000000010111100 # and b, c\nxxx10000001100010011 0000000010111101 # and b, d\nxxx10000001100010100 0000000010111110 # and b, e\nxxx10000001100010101 0000000010111111 # and b, bp\nxxx10000001100010110 0000000011000000 # and b, sp\nxxx10000001100100000 0000000011000001 # and c, a\nxxx10000001100100001 0000000011000010 # and c, b\nxxx10000001100100010 0000000011000011 # and c, c\nxxx10000001100100011 0000000011000100 # and c, d\nxxx10000001100100100 0000000011000101 # and c, e\nxxx10000001100100101 0000000011000110 # and c, bp\nxxx10000001100100110 0000000011000111 # and c, sp\nxxx10000001100110000 0000000011001000 # and d, a\nxxx10000001100110001 0000000011001001 # and d, b\nxxx10000001100110010 0000000011001010 # and d, c\nxxx10000001100110011 0000000011001011 # and d, d\nxxx10000001100110100 0000000011001100 # and d, e\nxxx10000001100110101 0000000011001101 # and d, bp\nxxx10000001100110110 0000000011001110 # and d, sp\nxxx10000001101000000 0000000011001111 # and e, a\nxxx10000001101000001 0000000011010000 # and e, b\nxxx10000001101000010 0000000011010001 # and e, c\nxxx10000001101000011 0000000011010010 # and e, d\nxxx10000001101000100 0000000011010011 # and e, e\nxxx10000001101000101 0000000011010100 # and e, bp\nxxx10000001101000110 0000000011010101 # and e, sp\nxxx10000001101010000 0000000011010110 # and bp, a\nxxx10000001101010001 0000000011010111 # and bp, b\nxxx10000001101010010 0000000011011000 # and bp, c\nxxx10000001101010011 0000000011011001 # and bp, d\nxxx10000001101010100 0000000011011010 # and bp, e\nxxx10000001101010101 0000000011011011 # and bp, bp\nxxx10000001101010110 0000000011011100 # and bp, sp\nxxx10000001101100000 0000000011011101 # and sp, a\nxxx10000001101100001 0000000011011110 # and sp, b\nxxx10000001101100010 0000000011011111 # and sp, c\nxxx10000001101100011 0000000011100000 # and sp, d\nxxx10000001101100100 0000000011100001 # and sp, e\nxxx10000001101100101 0000000011100010 # and sp, bp\nxxx10000001101100110 0000000011100011 # and sp, sp\nxxx10000010000000000 0000000011100100 # or a, a\nxxx10000010000000001 0000000011100101 # or a, b\nxxx10000010000000010 0000000011100110 # or a, c\nxxx10000010000000011 0000000011100111 # or a, d\nxxx10000010000000100 0000000011101000 # or a, e\nxxx10000010000000101 0000000011101001 # or a, bp\nxxx10000010000000110 0000000011101010 # or a, sp\nxxx10000010000010000 0000000011101011 # or b, a\nxxx10000010000010001 0000000011101100 # or b, b\nxxx10000010000010010 0000000011101101 # or b, c\nxxx10000010000010011 0000000011101110 # or b, d\nxxx10000010000010100 0000000011101111 # or b, e\nxxx10000010000010101 0000000011110000 # or b, bp\nxxx10000010000010110 0000000011110001 # or b, sp\nxxx10000010000100000 0000000011110010 # or c, a\nxxx10000010000100001 0000000011110011 # or c, b\nxxx10000010000100010 0000000011110100 # or c, c\nxxx10000010000100011 0000000011110101 # or c, d\nxxx10000010000100100 0000000011110110 # or c, e\nxxx10000010000100101 0000000011110111 # or c, bp\nxxx10000010000100110 0000000011111000 # or c, sp\nxxx10000010000110000 0000000011111001 # or d, a\nxxx10000010000110001 0000000011111010 # or d, b\nxxx10000010000110010 0000000011111011 # or d, c\nxxx10000010000110011 0000000011111100 # or d, d\nxxx10000010000110100 0000000011111101 # or d, e\nxxx10000010000110101 0000000011111110 # or d, bp\nxxx10000010000110110 0000000011111111 # or d, sp\nxxx10000010001000000 0000000100000000 # or e, a\nxxx10000010001000001 0000000100000001 # or e, b\nxxx10000010001000010 0000000100000010 # or e, c\nxxx10000010001000011 0000000100000011 # or e, d\nxxx10000010001000100 0000000100000100 # or e, e\nxxx10000010001000101 0000000100000101 # or e, bp\nxxx10000010001000110 0000000100000110 # or e, sp\nxxx10000010001010000 0000000100000111 # or bp, a\nxxx10000010001010001 0000000100001000 # or bp, b\nxxx10000010001010010 0000000100001001 # or bp, c\nxxx10000010001010011 0000000100001010 # or bp, d\nxxx10000010001010100 0000000100001011 # or bp, e\nxxx10000010001010101 0000000100001100 # or bp, bp\nxxx10000010001010110 0000000100001101 # or bp, sp\nxxx10000010001100000 0000000100001110 # or sp, a\nxxx10000010001100001 0000000100001111 # or sp, b\nxxx10000010001100010 0000000100010000 # or sp, c\nxxx10000010001100011 0000000100010001 # or sp, d\nxxx10000010001100100 0000000100010010 # or sp, e\nxxx10000010001100101 0000000100010011 # or sp, bp\nxxx10000010001100110 0000000100010100 # or sp, sp\nxxx10000011000000000 0000000100010101 # xor a, a\nxxx10000011000000001 0000000100010110 # xor a, b\nxxx10000011000000010 0000000100010111 # xor a, c\nxxx10000011000000011 0000000100011000 # xor a, d\nxxx10000011000000100 0000000100011001 # xor a, e\nxxx10000011000000101 0000000100011010 # xor a, bp\nxxx10000011000000110 0000000100011011 # xor a, sp\nxxx10000011000010000 0000000100011100 # xor b, a\nxxx10000011000010001 0000000100011101 # xor b, b\nxxx10000011000010010 0000000100011110 # xor b, c\nxxx10000011000010011 0000000100011111 # xor b, d\nxxx10000011000010100 0000000100100000 # xor b, e\nxxx10000011000010101 0000000100100001 # xor b, bp\nxxx10000011000010110 0000000100100010 # xor b, sp\nxxx10000011000100000 0000000100100011 # xor c, a\nxxx10000011000100001 0000000100100100 # xor c, b\nxxx10000011000100010 0000000100100101 # xor c, c\nxxx10000011000100011 0000000100100110 # xor c, d\nxxx10000011000100100 0000000100100111 # xor c, e\nxxx10000011000100101 0000000100101000 # xor c, bp\nxxx10000011000100110 0000000100101001 # xor c, sp\nxxx10000011000110000 0000000100101010 # xor d, a\nxxx10000011000110001 0000000100101011 # xor d, b\nxxx10000011000110010 0000000100101100 # xor d, c\nxxx10000011000110011 0000000100101101 # xor d, d\nxxx10000011000110100 0000000100101110 # xor d, e\nxxx10000011000110101 0000000100101111 # xor d, bp\nxxx10000011000110110 0000000100110000 # xor d, sp\nxxx10000011001000000 0000000100110001 # xor e, a\nxxx10000011001000001 0000000100110010 # xor e, b\nxxx10000011001000010 0000000100110011 # xor e, c\nxxx10000011001000011 0000000100110100 # xor e, d\nxxx10000011001000100 0000000100110101 # xor e, e\nxxx10000011001000101 0000000100110110 # xor e, bp\nxxx10000011001000110 0000000100110111 # xor e, sp\nxxx10000011001010000 0000000100111000 # xor bp, a\nxxx10000011001010001 0000000100111001 # xor bp, b\nxxx10000011001010010 0000000100111010 # xor bp, c\nxxx10000011001010011 0000000100111011 # xor bp, d\nxxx10000011001010100 0000000100111100 # xor bp, e\nxxx10000011001010101 0000000100111101 # xor bp, bp\nxxx10000011001010110 0000000100111110 # xor bp, sp\nxxx10000011001100000 0000000100111111 # xor sp, a\nxxx10000011001100001 0000000101000000 # xor sp, b\nxxx10000011001100010 0000000101000001 # xor sp, c\nxxx10000011001100011 0000000101000010 # xor sp, d\nxxx10000011001100100 0000000101000011 # xor sp, e\nxxx10000011001100101 0000000101000100 # xor sp, bp\nxxx10000011001100110 0000000101000101 # xor sp, sp\nxxx10000011100000000 0000000101000110 # shr a, a\nxxx10000011100000001 0000000101000111 # shr a, b\nxxx10000011100000010 0000000101001000 # shr a, c\nxxx10000011100000011 0000000101001001 # shr a, d\nxxx10000011100000100 0000000101001010 # shr a, e\nxxx10000011100000101 0000000101001011 # shr a, bp\nxxx10000011100000110 0000000101001100 # shr a, sp\nxxx10000011100010000 0000000101001101 # shr b, a\nxxx10000011100010001 0000000101001110 # shr b, b\nxxx10000011100010010 0000000101001111 # shr b, c\nxxx10000011100010011 0000000101010000 # shr b, d\nxxx10000011100010100 0000000101010001 # shr b, e\nxxx10000011100010101 0000000101010010 # shr b, bp\nxxx10000011100010110 0000000101010011 # shr b, sp\nxxx10000011100100000 0000000101010100 # shr c, a\nxxx10000011100100001 0000000101010101 # shr c, b\nxxx10000011100100010 0000000101010110 # shr c, c\nxxx10000011100100011 0000000101010111 # shr c, d\nxxx10000011100100100 0000000101011000 # shr c, e\nxxx10000011100100101 0000000101011001 # shr c, bp\nxxx10000011100100110 0000000101011010 # shr c, sp\nxxx10000011100110000 0000000101011011 # shr d, a\nxxx10000011100110001 0000000101011100 # shr d, b\nxxx10000011100110010 0000000101011101 # shr d, c\nxxx10000011100110011 0000000101011110 # shr d, d\nxxx10000011100110100 0000000101011111 # shr d, e\nxxx10000011100110101 0000000101100000 # shr d, bp\nxxx10000011100110110 0000000101100001 # shr d, sp\nxxx10000011101000000 0000000101100010 # shr e, a\nxxx10000011101000001 0000000101100011 # shr e, b\nxxx10000011101000010 0000000101100100 # shr e, c\nxxx10000011101000011 0000000101100101 # shr e, d\nxxx10000011101000100 0000000101100110 # shr e, e\nxxx10000011101000101 0000000101100111 # shr e, bp\nxxx10000011101000110 0000000101101000 # shr e, sp\nxxx10000011101010000 0000000101101001 # shr bp, a\nxxx10000011101010001 0000000101101010 # shr bp, b\nxxx10000011101010010 0000000101101011 # shr bp, c\nxxx10000011101010011 0000000101101100 # shr bp, d\nxxx10000011101010100 0000000101101101 # shr bp, e\nxxx10000011101010101 0000000101101110 # shr bp, bp\nxxx10000011101010110 0000000101101111 # shr bp, sp\nxxx10000011101100000 0000000101110000 # shr sp, a\nxxx10000011101100001 0000000101110001 # shr sp, b\nxxx10000011101100010 0000000101110010 # shr sp, c\nxxx10000011101100011 0000000101110011 # shr sp, d\nxxx10000011101100100 0000000101110100 # shr sp, e\nxxx10000011101100101 0000000101110101 # shr sp, bp\nxxx10000011101100110 0000000101110110 # shr sp, sp\nxxx10000000000001111 0000000101110111 # add a, opd\nxxx10000000000011111 0000000101111000 # add b, opd\nxxx10000000000101111 0000000101111001 # add c, opd\nxxx10000000000111111 0000000101111010 # add d, opd\nxxx10000000001001111 0000000101111011 # add e, opd\nxxx10000000001011111 0000000101111100 # add bp, opd\nxxx10000000001101111 0000000101111101 # add sp, opd\nxxx10000000100001111 0000000101111110 # sub a, opd\nxxx10000000100011111 0000000101111111 # sub b, opd\nxxx10000000100101111 0000000110000000 # sub c, opd\nxxx10000000100111111 0000000110000001 # sub d, opd\nxxx10000000101001111 0000000110000010 # sub e, opd\nxxx10000000101011111 0000000110000011 # sub bp, opd\nxxx10000000101101111 0000000110000100 # sub sp, opd\nxxx10000001000001111 0000000110000101 # mul a, opd\nxxx10000001000011111 0000000110000110 # mul b, opd\nxxx10000001000101111 0000000110000111 # mul c, opd\nxxx10000001000111111 0000000110001000 # mul d, opd\nxxx10000001001001111 0000000110001001 # mul e, opd\nxxx10000001001011111 0000000110001010 # mul bp, opd\nxxx10000001001101111 0000000110001011 # mul sp, opd\nxxx10000001100001111 0000000110001100 # and a, opd\nxxx10000001100011111 0000000110001101 # and b, opd\nxxx10000001100101111 0000000110001110 # and c, opd\nxxx10000001100111111 0000000110001111 # and d, opd\nxxx10000001101001111 0000000110010000 # and e, opd\nxxx10000001101011111 0000000110010001 # and bp, opd\nxxx10000001101101111 0000000110010010 # and sp, opd\nxxx10000010000001111 0000000110010011 # or a, opd\nxxx10000010000011111 0000000110010100 # or b, opd\nxxx10000010000101111 0000000110010101 # or c, opd\nxxx10000010000111111 0000000110010110 # or d, opd\nxxx10000010001001111 0000000110010111 # or e, opd\nxxx10000010001011111 0000000110011000 # or bp, opd\nxxx10000010001101111 0000000110011001 # or sp, opd\nxxx10000011000001111 0000000110011010 # xor a, opd\nxxx10000011000011111 0000000110011011 # xor b, opd\nxxx10000011000101111 0000000110011100 # xor c, opd\nxxx10000011000111111 0000000110011101 # xor d, opd\nxxx10000011001001111 0000000110011110 # xor e, opd\nxxx10000011001011111 0000000110011111 # xor bp, opd\nxxx10000011001101111 0000000110100000 # xor sp, opd\nxxx10000011100001111 0000000110100001 # shr a, opd\nxxx10000011100011111 0000000110100010 # shr b, opd\nxxx10000011100101111 0000000110100011 # shr c, opd\nxxx10000011100111111 0000000110100100 # shr d, opd\nxxx10000011101001111 0000000110100101 # shr e, opd\nxxx10000011101011111 0000000110100110 # shr bp, opd\nxxx10000011101101111 0000000110100111 # shr sp, opd\nxxx10000000000001001 0000000110101000 # add a, [memaddr+opd]\nxxx10000000000011001 0000000110101001 # add b, [memaddr+opd]\nxxx10000000000101001 0000000110101010 # add c, [memaddr+opd]\nxxx10000000000111001 0000000110101011 # add d, [memaddr+opd]\nxxx10000000001001001 0000000110101100 # add e, [memaddr+opd]\nxxx10000000001011001 0000000110101101 # add bp, [memaddr+opd]\nxxx10000000001101001 0000000110101110 # add sp, [memaddr+opd]\nxxx10000000000001001 0000000110101111 # add a, [memaddr+opd]\nxxx10000000000011001 0000000110110000 # add b, [memaddr+opd]\nxxx10000000000101001 0000000110110001 # add c, [memaddr+opd]\nxxx10000000000111001 0000000110110010 # add d, [memaddr+opd]\nxxx10000000001001001 0000000110110011 # add e, [memaddr+opd]\nxxx10000000001011001 0000000110110100 # add bp, [memaddr+opd]\nxxx10000000001101001 0000000110110101 # add sp, [memaddr+opd]\nxxx10000000100001001 0000000110110110 # sub a, [memaddr+opd]\nxxx10000000100011001 0000000110110111 # sub b, [memaddr+opd]\nxxx10000000100101001 0000000110111000 # sub c, [memaddr+opd]\nxxx10000000100111001 0000000110111001 # sub d, [memaddr+opd]\nxxx10000000101001001 0000000110111010 # sub e, [memaddr+opd]\nxxx10000000101011001 0000000110111011 # sub bp, [memaddr+opd]\nxxx10000000101101001 0000000110111100 # sub sp, [memaddr+opd]\nxxx10000000100001001 0000000110111101 # sub a, [memaddr+opd]\nxxx10000000100011001 0000000110111110 # sub b, [memaddr+opd]\nxxx10000000100101001 0000000110111111 # sub c, [memaddr+opd]\nxxx10000000100111001 0000000111000000 # sub d, [memaddr+opd]\nxxx10000000101001001 0000000111000001 # sub e, [memaddr+opd]\nxxx10000000101011001 0000000111000010 # sub bp, [memaddr+opd]\nxxx10000000101101001 0000000111000011 # sub sp, [memaddr+opd]\nxxx10000001000001001 0000000111000100 # mul a, [memaddr+opd]\nxxx10000001000011001 0000000111000101 # mul b, [memaddr+opd]\nxxx10000001000101001 0000000111000110 # mul c, [memaddr+opd]\nxxx10000001000111001 0000000111000111 # mul d, [memaddr+opd]\nxxx10000001001001001 0000000111001000 # mul e, [memaddr+opd]\nxxx10000001001011001 0000000111001001 # mul bp, [memaddr+opd]\nxxx10000001001101001 0000000111001010 # mul sp, [memaddr+opd]\nxxx10000001000001001 0000000111001011 # mul a, [memaddr+opd]\nxxx10000001000011001 0000000111001100 # mul b, [memaddr+opd]\nxxx10000001000101001 0000000111001101 # mul c, [memaddr+opd]\nxxx10000001000111001 0000000111001110 # mul d, [memaddr+opd]\nxxx10000001001001001 0000000111001111 # mul e, [memaddr+opd]\nxxx10000001001011001 0000000111010000 # mul bp, [memaddr+opd]\nxxx10000001001101001 0000000111010001 # mul sp, [memaddr+opd]\nxxx10000001100001001 0000000111010010 # and a, [memaddr+opd]\nxxx10000001100011001 0000000111010011 # and b, [memaddr+opd]\nxxx10000001100101001 0000000111010100 # and c, [memaddr+opd]\nxxx10000001100111001 0000000111010101 # and d, [memaddr+opd]\nxxx10000001101001001 0000000111010110 # and e, [memaddr+opd]\nxxx10000001101011001 0000000111010111 # and bp, [memaddr+opd]\nxxx10000001101101001 0000000111011000 # and sp, [memaddr+opd]\nxxx10000001100001001 0000000111011001 # and a, [memaddr+opd]\nxxx10000001100011001 0000000111011010 # and b, [memaddr+opd]\nxxx10000001100101001 0000000111011011 # and c, [memaddr+opd]\nxxx10000001100111001 0000000111011100 # and d, [memaddr+opd]\nxxx10000001101001001 0000000111011101 # and e, [memaddr+opd]\nxxx10000001101011001 0000000111011110 # and bp, [memaddr+opd]\nxxx10000001101101001 0000000111011111 # and sp, [memaddr+opd]\nxxx10000010000001001 0000000111100000 # or a, [memaddr+opd]\nxxx10000010000011001 0000000111100001 # or b, [memaddr+opd]\nxxx10000010000101001 0000000111100010 # or c, [memaddr+opd]\nxxx10000010000111001 0000000111100011 # or d, [memaddr+opd]\nxxx10000010001001001 0000000111100100 # or e, [memaddr+opd]\nxxx10000010001011001 0000000111100101 # or bp, [memaddr+opd]\nxxx10000010001101001 0000000111100110 # or sp, [memaddr+opd]\nxxx10000010000001001 0000000111100111 # or a, [memaddr+opd]\nxxx10000010000011001 0000000111101000 # or b, [memaddr+opd]\nxxx10000010000101001 0000000111101001 # or c, [memaddr+opd]\nxxx10000010000111001 0000000111101010 # or d, [memaddr+opd]\nxxx10000010001001001 0000000111101011 # or e, [memaddr+opd]\nxxx10000010001011001 0000000111101100 # or bp, [memaddr+opd]\nxxx10000010001101001 0000000111101101 # or sp, [memaddr+opd]\nxxx10000011000001001 0000000111101110 # xor a, [memaddr+opd]\nxxx10000011000011001 0000000111101111 # xor b, [memaddr+opd]\nxxx10000011000101001 0000000111110000 # xor c, [memaddr+opd]\nxxx10000011000111001 0000000111110001 # xor d, [memaddr+opd]\nxxx10000011001001001 0000000111110010 # xor e, [memaddr+opd]\nxxx10000011001011001 0000000111110011 # xor bp, [memaddr+opd]\nxxx10000011001101001 0000000111110100 # xor sp, [memaddr+opd]\nxxx10000011000001001 0000000111110101 # xor a, [memaddr+opd]\nxxx10000011000011001 0000000111110110 # xor b, [memaddr+opd]\nxxx10000011000101001 0000000111110111 # xor c, [memaddr+opd]\nxxx10000011000111001 0000000111111000 # xor d, [memaddr+opd]\nxxx10000011001001001 0000000111111001 # xor e, [memaddr+opd]\nxxx10000011001011001 0000000111111010 # xor bp, [memaddr+opd]\nxxx10000011001101001 0000000111111011 # xor sp, [memaddr+opd]\nxxx10000011100001001 0000000111111100 # shr a, [memaddr+opd]\nxxx10000011100011001 0000000111111101 # shr b, [memaddr+opd]\nxxx10000011100101001 0000000111111110 # shr c, [memaddr+opd]\nxxx10000011100111001 0000000111111111 # shr d, [memaddr+opd]\nxxx10000011101001001 0000001000000000 # shr e, [memaddr+opd]\nxxx10000011101011001 0000001000000001 # shr bp, [memaddr+opd]\nxxx10000011101101001 0000001000000010 # shr sp, [memaddr+opd]\nxxx10000011100001001 0000001000000011 # shr a, [memaddr+opd]\nxxx10000011100011001 0000001000000100 # shr b, [memaddr+opd]\nxxx10000011100101001 0000001000000101 # shr c, [memaddr+opd]\nxxx10000011100111001 0000001000000110 # shr d, [memaddr+opd]\nxxx10000011101001001 0000001000000111 # shr e, [memaddr+opd]\nxxx10000011101011001 0000001000001000 # shr bp, [memaddr+opd]\nxxx10000011101101001 0000001000001001 # shr sp, [memaddr+opd]\nxxx10000000010111111 0000001000001010 # add memval,opd\nxxx10000010100001111 0000001000001011 # not a\nxxx10000010100011111 0000001000001100 # not b\nxxx10000010100101111 0000001000001101 # not c\nxxx10000010100111111 0000001000001110 # not d\nxxx10000010101001111 0000001000001111 # not e\nxxx10000010101011111 0000001000010000 # not bp\nxxx10000010101101111 0000001000010001 # not sp\nxxx10000100000000000 0000001000010010 # mov a, a\nxxx10000100000000001 0000001000010011 # mov a, b\nxxx10000100000000010 0000001000010100 # mov a, c\nxxx10000100000000011 0000001000010101 # mov a, d\nxxx10000100000000100 0000001000010110 # mov a, e\nxxx10000100000000101 0000001000010111 # mov a, bp\nxxx10000100000000110 0000001000011000 # mov a, sp\nxxx10000100000010000 0000001000011001 # mov b, a\nxxx10000100000010001 0000001000011010 # mov b, b\nxxx10000100000010010 0000001000011011 # mov b, c\nxxx10000100000010011 0000001000011100 # mov b, d\nxxx10000100000010100 0000001000011101 # mov b, e\nxxx10000100000010101 0000001000011110 # mov b, bp\nxxx10000100000010110 0000001000011111 # mov b, sp\nxxx10000100000100000 0000001000100000 # mov c, a\nxxx10000100000100001 0000001000100001 # mov c, b\nxxx10000100000100010 0000001000100010 # mov c, c\nxxx10000100000100011 0000001000100011 # mov c, d\nxxx10000100000100100 0000001000100100 # mov c, e\nxxx10000100000100101 0000001000100101 # mov c, bp\nxxx10000100000100110 0000001000100110 # mov c, sp\nxxx10000100000110000 0000001000100111 # mov d, a\nxxx10000100000110001 0000001000101000 # mov d, b\nxxx10000100000110010 0000001000101001 # mov d, c\nxxx10000100000110011 0000001000101010 # mov d, d\nxxx10000100000110100 0000001000101011 # mov d, e\nxxx10000100000110101 0000001000101100 # mov d, bp\nxxx10000100000110110 0000001000101101 # mov d, sp\nxxx10000100001000000 0000001000101110 # mov e, a\nxxx10000100001000001 0000001000101111 # mov e, b\nxxx10000100001000010 0000001000110000 # mov e, c\nxxx10000100001000011 0000001000110001 # mov e, d\nxxx10000100001000100 0000001000110010 # mov e, e\nxxx10000100001000101 0000001000110011 # mov e, bp\nxxx10000100001000110 0000001000110100 # mov e, sp\nxxx10000100001010000 0000001000110101 # mov bp, a\nxxx10000100001010001 0000001000110110 # mov bp, b\nxxx10000100001010010 0000001000110111 # mov bp, c\nxxx10000100001010011 0000001000111000 # mov bp, d\nxxx10000100001010100 0000001000111001 # mov bp, e\nxxx10000100001010101 0000001000111010 # mov bp, bp\nxxx10000100001010110 0000001000111011 # mov bp, sp\nxxx10000100001100000 0000001000111100 # mov sp, a\nxxx10000100001100001 0000001000111101 # mov sp, b\nxxx10000100001100010 0000001000111110 # mov sp, c\nxxx10000100001100011 0000001000111111 # mov sp, d\nxxx10000100001100100 0000001001000000 # mov sp, e\nxxx10000100001100101 0000001001000001 # mov sp, bp\nxxx10000100001100110 0000001001000010 # mov sp, sp\nxxx10000100000001001 0000001001000011 # mov a, [memaddr+opd]\nxxx10000100000011001 0000001001000100 # mov b, [memaddr+opd]\nxxx10000100000101001 0000001001000101 # mov c, [memaddr+opd]\nxxx10000100000111001 0000001001000110 # mov d, [memaddr+opd]\nxxx10000100001001001 0000001001000111 # mov e, [memaddr+opd]\nxxx10000100001011001 0000001001001000 # mov bp, [memaddr+opd]\nxxx10000100001101001 0000001001001001 # mov sp, [memaddr+opd]\nxxx10000100000001001 0000001001001010 # mov a, [memaddr+opd]\nxxx10000100000011001 0000001001001011 # mov b, [memaddr+opd]\nxxx10000100000101001 0000001001001100 # mov c, [memaddr+opd]\nxxx10000100000111001 0000001001001101 # mov d, [memaddr+opd]\nxxx10000100001001001 0000001001001110 # mov e, [memaddr+opd]\nxxx10000100001011001 0000001001001111 # mov bp, [memaddr+opd]\nxxx10000100001101001 0000001001010000 # mov sp, [memaddr+opd]\nxxx10000100010111001 0000001001010001 # mov memval, [memaddr+opd]\nxxx10000100010100000 0000001001010011 # mov memaddr,a\nxxx10000100010100001 0000001001010100 # mov memaddr,b\nxxx10000100010100010 0000001001010101 # mov memaddr,c\nxxx10000100010100011 0000001001010110 # mov memaddr,d\nxxx10000100010100100 0000001001010111 # mov memaddr,e\nxxx10000100010100101 0000001001011000 # mov memaddr,bp\nxxx10000100010100110 0000001001011001 # mov memaddr,sp\nxxx10000100010110000 0000001001011010 # mov memval,a\nxxx10000100010110001 0000001001011011 # mov memval,b\nxxx10000100010110010 0000001001011100 # mov memval,c\nxxx10000100010110011 0000001001011101 # mov memval,d\nxxx10000100010110100 0000001001011110 # mov memval,e\nxxx10000100010110101 0000001001011111 # mov memval,bp\nxxx10000100010110110 0000001001100000 # mov memval,sp\nxxx10000100010101010 0000001001100001 # mov [memaddr+opd],memval\nxxx10000100010101111 0000001001100011 # mov memaddr, opd\nxxx10000100010111111 0000001001100100 # mov memval, opd\nxxx10000100000001111 0000001001100101 # mov a, opd\nxxx10000100000011111 0000001001100110 # mov b, opd\nxxx10000100000101111 0000001001100111 # mov c, opd\nxxx10000100000111111 0000001001101000 # mov d, opd\nxxx10000100001001111 0000001001101001 # mov e, opd\nxxx10000100001011111 0000001001101010 # mov bp, opd\nxxx10000100001101111 0000001001101011 # mov sp, opd\nxxx10000100100001111 0000001001101100 # in a\nxxx10000100100011111 0000001001101101 # in b\nxxx10000100100101111 0000001001101110 # in c\nxxx10000100100111111 0000001001101111 # in d\nxxx10000100101001111 0000001001110000 # in e\nxxx10000100101011111 0000001001110001 # in bp\nxxx10000100101101111 0000001001110010 # in sp\nxxx10000101000001111 0000001001110011 # out a\nxxx10000101000011111 0000001001110100 # out b\nxxx10000101000101111 0000001001110101 # out c\nxxx10000101000111111 0000001001110110 # out d\nxxx10000101001001111 0000001001110111 # out e\nxxx10000101001011111 0000001001111000 # out bp\nxxx10000101001101111 0000001001111001 # out sp\nxxx10000101011111111 0000001001111010 # out opd\nxxx10001001000000000 0000001001111011 # cmp a, a\nxxx10001001000000001 0000001001111100 # cmp a, b\nxxx10001001000000010 0000001001111101 # cmp a, c\nxxx10001001000000011 0000001001111110 # cmp a, d\nxxx10001001000000100 0000001001111111 # cmp a, e\nxxx10001001000000101 0000001010000000 # cmp a, bp\nxxx10001001000000110 0000001010000001 # cmp a, sp\nxxx10001001000010000 0000001010000010 # cmp b, a\nxxx10001001000010001 0000001010000011 # cmp b, b\nxxx10001001000010010 0000001010000100 # cmp b, c\nxxx10001001000010011 0000001010000101 # cmp b, d\nxxx10001001000010100 0000001010000110 # cmp b, e\nxxx10001001000010101 0000001010000111 # cmp b, bp\nxxx10001001000010110 0000001010001000 # cmp b, sp\nxxx10001001000100000 0000001010001001 # cmp c, a\nxxx10001001000100001 0000001010001010 # cmp c, b\nxxx10001001000100010 0000001010001011 # cmp c, c\nxxx10001001000100011 0000001010001100 # cmp c, d\nxxx10001001000100100 0000001010001101 # cmp c, e\nxxx10001001000100101 0000001010001110 # cmp c, bp\nxxx10001001000100110 0000001010001111 # cmp c, sp\nxxx10001001000110000 0000001010010000 # cmp d, a\nxxx10001001000110001 0000001010010001 # cmp d, b\nxxx10001001000110010 0000001010010010 # cmp d, c\nxxx10001001000110011 0000001010010011 # cmp d, d\nxxx10001001000110100 0000001010010100 # cmp d, e\nxxx10001001000110101 0000001010010101 # cmp d, bp\nxxx10001001000110110 0000001010010110 # cmp d, sp\nxxx10001001001000000 0000001010010111 # cmp e, a\nxxx10001001001000001 0000001010011000 # cmp e, b\nxxx10001001001000010 0000001010011001 # cmp e, c\nxxx10001001001000011 0000001010011010 # cmp e, d\nxxx10001001001000100 0000001010011011 # cmp e, e\nxxx10001001001000101 0000001010011100 # cmp e, bp\nxxx10001001001000110 0000001010011101 # cmp e, sp\nxxx10001001001010000 0000001010011110 # cmp bp, a\nxxx10001001001010001 0000001010011111 # cmp bp, b\nxxx10001001001010010 0000001010100000 # cmp bp, c\nxxx10001001001010011 0000001010100001 # cmp bp, d\nxxx10001001001010100 0000001010100010 # cmp bp, e\nxxx10001001001010101 0000001010100011 # cmp bp, bp\nxxx10001001001010110 0000001010100100 # cmp bp, sp\nxxx10001001001100000 0000001010100101 # cmp sp, a\nxxx10001001001100001 0000001010100110 # cmp sp, b\nxxx10001001001100010 0000001010100111 # cmp sp, c\nxxx10001001001100011 0000001010101000 # cmp sp, d\nxxx10001001001100100 0000001010101001 # cmp sp, e\nxxx10001001001100101 0000001010101010 # cmp sp, bp\nxxx10001001001100110 0000001010101011 # cmp sp, sp\nxxx10001001000001111 0000001010101100 # cmp a, opd\nxxx10001001000011111 0000001010101101 # cmp b, opd\nxxx10001001000101111 0000001010101110 # cmp c, opd\nxxx10001001000111111 0000001010101111 # cmp d, opd\nxxx10001001001001111 0000001010110000 # cmp e, opd\nxxx10001001001011111 0000001010110001 # cmp bp, opd\nxxx10001001001101111 0000001010110010 # cmp sp, opd\nxxx10001000110111111 0000001010110011 # jmp memval\n0xx10000101100001111 0000001010110100 # jnc a (Taken)\n0xx10000101100011111 0000001010110101 # jnc b (Taken)\n0xx10000101100101111 0000001010110110 # jnc c (Taken)\n0xx10000101100111111 0000001010110111 # jnc d (Taken)\n0xx10000101101001111 0000001010111000 # jnc e (Taken)\n0xx10000101101011111 0000001010111001 # jnc bp (Taken)\n0xx10000101101101111 0000001010111010 # jnc sp (Taken)\n1xx10000101100001111 0000001010111011 # jnc a (Skip)\n1xx10000101100011111 0000001010111100 # jnc b (Skip)\n1xx10000101100101111 0000001010111101 # jnc c (Skip)\n1xx10000101100111111 0000001010111110 # jnc d (Skip)\n1xx10000101101001111 0000001010111111 # jnc e (Skip)\n1xx10000101101011111 0000001011000000 # jnc bp (Skip)\n1xx10000101101101111 0000001011000001 # jnc sp (Skip)\n1xx10000110000001111 0000001011000010 # jc a (Taken)\n1xx10000110000011111 0000001011000011 # jc b (Taken)\n1xx10000110000101111 0000001011000100 # jc c (Taken)\n1xx10000110000111111 0000001011000101 # jc d (Taken)\n1xx10000110001001111 0000001011000110 # jc e (Taken)\n1xx10000110001011111 0000001011000111 # jc bp (Taken)\n1xx10000110001101111 0000001011001000 # jc sp (Taken)\n0xx10000110000001111 0000001011001001 # jc a (Skip)\n0xx10000110000011111 0000001011001010 # jc b (Skip)\n0xx10000110000101111 0000001011001011 # jc c (Skip)\n0xx10000110000111111 0000001011001100 # jc d (Skip)\n0xx10000110001001111 0000001011001101 # jc e (Skip)\n0xx10000110001011111 0000001011001110 # jc bp (Skip)\n0xx10000110001101111 0000001011001111 # jc sp (Skip)\nx0x10000110100001111 0000001011010000 # jnz a (Taken)\nx0x10000110100011111 0000001011010001 # jnz b (Taken)\nx0x10000110100101111 0000001011010010 # jnz c (Taken)\nx0x10000110100111111 0000001011010011 # jnz d (Taken)\nx0x10000110101001111 0000001011010100 # jnz e (Taken)\nx0x10000110101011111 0000001011010101 # jnz bp (Taken)\nx0x10000110101101111 0000001011010110 # jnz sp (Taken)\nx1x10000110100001111 0000001011010111 # jnz a (Skip)\nx1x10000110100011111 0000001011011000 # jnz b (Skip)\nx1x10000110100101111 0000001011011001 # jnz c (Skip)\nx1x10000110100111111 0000001011011010 # jnz d (Skip)\nx1x10000110101001111 0000001011011011 # jnz e (Skip)\nx1x10000110101011111 0000001011011100 # jnz bp (Skip)\nx1x10000110101101111 0000001011011101 # jnz sp (Skip)\nx1x10000111000001111 0000001011011110 # jz a (Taken)\nx1x10000111000011111 0000001011011111 # jz b (Taken)\nx1x10000111000101111 0000001011100000 # jz c (Taken)\nx1x10000111000111111 0000001011100001 # jz d (Taken)\nx1x10000111001001111 0000001011100010 # jz e (Taken)\nx1x10000111001011111 0000001011100011 # jz bp (Taken)\nx1x10000111001101111 0000001011100100 # jz sp (Taken)\nx0x10000111000001111 0000001011100101 # jz a (Skip)\nx0x10000111000011111 0000001011100110 # jz b (Skip)\nx0x10000111000101111 0000001011100111 # jz c (Skip)\nx0x10000111000111111 0000001011101000 # jz d (Skip)\nx0x10000111001001111 0000001011101001 # jz e (Skip)\nx0x10000111001011111 0000001011101010 # jz bp (Skip)\nx0x10000111001101111 0000001011101011 # jz sp (Skip)\nxx010000111100001111 0000001011101100 # jns a (Taken)\nxx010000111100011111 0000001011101101 # jns b (Taken)\nxx010000111100101111 0000001011101110 # jns c (Taken)\nxx010000111100111111 0000001011101111 # jns d (Taken)\nxx010000111101001111 0000001011110000 # jns e (Taken)\nxx010000111101011111 0000001011110001 # jns bp (Taken)\nxx010000111101101111 0000001011110010 # jns sp (Taken)\nxx110000111100001111 0000001011110011 # jns a (Skip)\nxx110000111100011111 0000001011110100 # jns b (Skip)\nxx110000111100101111 0000001011110101 # jns c (Skip)\nxx110000111100111111 0000001011110110 # jns d (Skip)\nxx110000111101001111 0000001011110111 # jns e (Skip)\nxx110000111101011111 0000001011111000 # jns bp (Skip)\nxx110000111101101111 0000001011111001 # jns sp (Skip)\nxx110001000000001111 0000001011111010 # js a (Taken)\nxx110001000000011111 0000001011111011 # js b (Taken)\nxx110001000000101111 0000001011111100 # js c (Taken)\nxx110001000000111111 0000001011111101 # js d (Taken)\nxx110001000001001111 0000001011111110 # js e (Taken)\nxx110001000001011111 0000001011111111 # js bp (Taken)\nxx110001000001101111 0000001100000000 # js sp (Taken)\nxx010001000000001111 0000001100000001 # js a (Skip)\nxx010001000000011111 0000001100000010 # js b (Skip)\nxx010001000000101111 0000001100000011 # js c (Skip)\nxx010001000000111111 0000001100000100 # js d (Skip)\nxx010001000001001111 0000001100000101 # js e (Skip)\nxx010001000001011111 0000001100000110 # js bp (Skip)\nxx010001000001101111 0000001100000111 # js sp (Skip)\nxxx10001000100001111 0000001100001000 # jmp a\nxxx10001000100011111 0000001100001001 # jmp b\nxxx10001000100101111 0000001100001010 # jmp c\nxxx10001000100111111 0000001100001011 # jmp d\nxxx10001000101001111 0000001100001100 # jmp e\nxxx10001000101011111 0000001100001101 # jmp bp\nxxx10001000101101111 0000001100001110 # jmp sp\nx1x10001011000001111 0000001100001111 # je a (Taken)\nx1x10001011000011111 0000001100010000 # je b (Taken)\nx1x10001011000101111 0000001100010001 # je c (Taken)\nx1x10001011000111111 0000001100010010 # je d (Taken)\nx1x10001011001001111 0000001100010011 # je e (Taken)\nx1x10001011001011111 0000001100010100 # je bp (Taken)\nx1x10001011001101111 0000001100010101 # je sp (Taken)\nx0x10001011000001111 0000001100010110 # je a (Skip)\nx0x10001011000011111 0000001100010111 # je b (Skip)\nx0x10001011000101111 0000001100011000 # je c (Skip)\nx0x10001011000111111 0000001100011001 # je d (Skip)\nx0x10001011001001111 0000001100011010 # je e (Skip)\nx0x10001011001011111 0000001100011011 # je bp (Skip)\nx0x10001011001101111 0000001100011100 # je sp (Skip)\nx0x10001011100001111 0000001100011101 # jne a(Taken)\nx0x10001011100011111 0000001100011110 # jne b(Taken)\nx0x10001011100101111 0000001100011111 # jne c(Taken)\nx0x10001011100111111 0000001100100000 # jne d(Taken)\nx0x10001011101001111 0000001100100001 # jne e(Taken)\nx0x10001011101011111 0000001100100010 # jne bp(Taken)\nx0x10001011101101111 0000001100100011 # jne sp(Taken)\nx1x10001011100001111 0000001100100100 # jne a(Skip)\nx1x10001011100011111 0000001100100101 # jne b(Skip)\nx1x10001011100101111 0000001100100110 # jne c(Skip)\nx1x10001011100111111 0000001100100111 # jne d(Skip)\nx1x10001011101001111 0000001100101000 # jne e(Skip)\nx1x10001011101011111 0000001100101001 # jne bp(Skip)\nx1x10001011101101111 0000001100101010 # jne sp(Skip)\nx0010001100000001111 0000001100101011 # ja a (Taken)\nx0010001100000011111 0000001100101100 # ja b (Taken)\nx0010001100000101111 0000001100101101 # ja c (Taken)\nx0010001100000111111 0000001100101110 # ja d (Taken)\nx0010001100001001111 0000001100101111 # ja e (Taken)\nx0010001100001011111 0000001100110000 # ja bp (Taken)\nx0010001100001101111 0000001100110001 # ja sp (Taken)\nxxx10001100000001111 0000001100110010 # ja a (Skip)\nxxx10001100000011111 0000001100110011 # ja b (Skip)\nxxx10001100000101111 0000001100110100 # ja c (Skip)\nxxx10001100000111111 0000001100110101 # ja d (Skip)\nxxx10001100001001111 0000001100110110 # ja e (Skip)\nxxx10001100001011111 0000001100110111 # ja bp (Skip)\nxxx10001100001101111 0000001100111000 # ja sp (Skip)\nx0010001100100001111 0000001100111001 # jae a (Taken)\nx0010001100100011111 0000001100111010 # jae b (Taken)\nx0010001100100101111 0000001100111011 # jae c (Taken)\nx0010001100100111111 0000001100111100 # jae d (Taken)\nx0010001100101001111 0000001100111101 # jae e (Taken)\nx0010001100101011111 0000001100111110 # jae bp (Taken)\nx0010001100101101111 0000001100111111 # jae sp (Taken)\nx1010001100100001111 0000001101000000 # jae a (Taken)\nx1010001100100011111 0000001101000001 # jae b (Taken)\nx1010001100100101111 0000001101000010 # jae c (Taken)\nx1010001100100111111 0000001101000011 # jae d (Taken)\nx1010001100101001111 0000001101000100 # jae e (Taken)\nx1010001100101011111 0000001101000101 # jae bp (Taken)\nx1010001100101101111 0000001101000110 # jae sp (Taken)\nxxx10001100100001111 0000001101000111 # jae a (Skip)\nxxx10001100100011111 0000001101001000 # jae b (Skip)\nxxx10001100100101111 0000001101001001 # jae c (Skip)\nxxx10001100100111111 0000001101001010 # jae d (Skip)\nxxx10001100101001111 0000001101001011 # jae e (Skip)\nxxx10001100101011111 0000001101001100 # jae bp (Skip)\nxxx10001100101101111 0000001101001101 # jae sp (Skip)\nx0110001101000001111 0000001101001110 # jl a (Taken)\nx0110001101000011111 0000001101001111 # jl b (Taken)\nx0110001101000101111 0000001101010000 # jl c (Taken)\nx0110001101000111111 0000001101010001 # jl d (Taken)\nx0110001101001001111 0000001101010010 # jl e (Taken)\nx0110001101001011111 0000001101010011 # jl bp (Taken)\nx0110001101001101111 0000001101010100 # jl sp (Taken)\nxxx10001101000001111 0000001101010101 # jl a (Skip)\nxxx10001101000011111 0000001101010110 # jl b (Skip)\nxxx10001101000101111 0000001101010111 # jl c (Skip)\nxxx10001101000111111 0000001101011000 # jl d (Skip)\nxxx10001101001001111 0000001101011001 # jl e (Skip)\nxxx10001101001011111 0000001101011010 # jl bp (Skip)\nxxx10001101001101111 0000001101011011 # jl sp (Skip)\nx0110001101100001111 0000001101011100 # jle a (Taken)\nx0110001101100011111 0000001101011101 # jle b (Taken)\nx0110001101100101111 0000001101011110 # jle c (Taken)\nx0110001101100111111 0000001101011111 # jle d (Taken)\nx0110001101101001111 0000001101100000 # jle e (Taken)\nx0110001101101011111 0000001101100001 # jle bp (Taken)\nx0110001101101101111 0000001101100010 # jle sp (Taken)\nx1010001101100001111 0000001101100011 # jle a (Taken)\nx1010001101100011111 0000001101100100 # jle b (Taken)\nx1010001101100101111 0000001101100101 # jle c (Taken)\nx1010001101100111111 0000001101100110 # jle d (Taken)\nx1010001101101001111 0000001101100111 # jle e (Taken)\nx1010001101101011111 0000001101101000 # jle bp (Taken)\nx1010001101101101111 0000001101101001 # jle sp (Taken)\nxxx10001101100001111 0000001101101010 # jle a (Skip)\nxxx10001101100011111 0000001101101011 # jle b (Skip)\nxxx10001101100101111 0000001101101100 # jle c (Skip)\nxxx10001101100111111 0000001101101101 # jle d (Skip)\nxxx10001101101001111 0000001101101110 # jle e (Skip)\nxxx10001101101011111 0000001101101111 # jle bp (Skip)")) IMBD (
    .in({carry_flag, zero_flag, sign_flag, or_4_out[16], Instruction_Register_p6}), .out(IMBD_out));
  Register TSR (.D(ITSD_out), .en(comparator_3_eq), .clk(CLK), .Q(TSR_q), .clr(RESET));
  Comparator #(.mode("unsigned")) comparator_4 (.a(TSR_q), .b(IDSC_q), .eq(comparator_4_eq));  // open: gt, lt
  Adder #(.width(16)) adder_3 (.a(IMBD_out), .b(bit_extender_1_out), .out(adder_3_out));  // open: cin, cout
  assign bit_extender_1_out = {{8{1'b0}}, subtractor_1_out};  // Bit_Extender bit_extender_1
  ROM #(.addrWidth(16), .dataWidth(24)) Microcode_ROM (.addr(adder_3_out), .data(Microcode_ROM_data));
  Multiplexer #(.width(24)) multiplexer_6 (
    .in0(24'h78), .in1(Microcode_ROM_data),
    .out({multiplexer_6_out[23:20], CPU_Control_BUS, multiplexer_6_out[0]}), .sel(and_4_out));
  and and_4 (and_4_out, or_4_out[16], not_4_out);
  not not_4 (not_4_out, multiplexer_6_out[21]);
  Register #(.width(16)) MOR (
    .D({CPU_Control_BUS[14:0], multiplexer_6_out[0]}), .en(multiplexer_6_out[21]), .clk(CLK), .Q(MOR_q),
    .clr(RESET));

  // Notes on the sheet:
  //   contents of Microcode_ROM (hex, n*v repeats v):
  //   78 1c038 78 1c038 78 1c038 78 1c038 78 1c038 78 1c038 78 1c038 1c038 78 1c038 78 1c038 78 1c038
  //   1c038 78 1c038 78 1c038 1c038 78 40078 78 78 28050 82000 82400 82800 82c00 83000 83400 83800 86008
  //   86408 86808 86c08 87008 87408 87808 8a010 8a410 8a810 8ac10 8b010 8b410 8b810 8e018 8e418 8e818
  //   8ec18 8f018 8f418 8f818 92020 92420 92820 92c20 93020 93420 93820 96028 96428 96828 96c28 97028
  //   97428 97828 9a030 9a430 9a830 9ac30 9b030 9b430 9b830 82080 82480 82880 82c80 83080 83480 83880
  //   86088 86488 86888 86c88 87088 87488 87888 8a090 8a490 8a890 8ac90 8b090 8b490 8b890 8e098 8e498
  //   8e898 8ec98 8f098 8f498 8f898 920a0 924a0 928a0 92ca0 930a0 934a0 938a0 960a8 964a8 968a8 96ca8
  //   970a8 974a8 978a8 9a0b0 9a4b0 9a8b0 9acb0 9b0b0 9b4b0 9b8b0 82100 82500 82900 82d00 83100 83500
  //   83900 86108 86508 86908 86d08 87108 87508 87908 8a110 8a510 8a910 8ad10 8b110 8b510 8b910 8e118
  //   8e518 8e918 8ed18 8f118 8f518 8f918 92120 92520 92920 92d20 93120 93520 93920 96128 96528 96928
  //   96d28 97128 97528 97928 9a130 9a530 9a930 9ad30 9b130 9b530 9b930 82180 82580 82980 82d80 83180
  //   83580 83980 86188 86588 86988 86d88 87188 87588 87988 8a190 8a590 8a990 8ad90 8b190 8b590 8b990
  //   8e198 8e598 8e998 8ed98 8f198 8f598 8f998 921a0 925a0 929a0 92da0 931a0 935a0 939a0 961a8 965a8
  //   969a8 96da8 971a8 975a8 979a8 9a1b0 9a5b0 9a9b0 9adb0 9b1b0 9b5b0 9b9b0 82200 82600 82a00 82e00
  //   83200 83600 83a00 86208 86608 86a08 86e08 87208 87608 87a08 8a210 8a610 8aa10 8ae10 8b210 8b610
  //   8ba10 8e218 8e618 8ea18 8ee18 8f218 8f618 8fa18 92220 92620 92a20 92e20 93220 93620 93a20 96228
  //   96628 96a28 96e28 97228 97628 97a28 9a230 9a630 9aa30 9ae30 9b230 9b630 9ba30 82300 82700 82b00
  //   82f00 83300 83700 83b00 86308 86708 86b08 86f08 87308 87708 87b08 8a310 8a710 8ab10 8af10 8b310
  //   8b710 8bb10 8e318 8e718 8eb18 8ef18 8f318 8f718 8fb18 92320 92720 92b20 92f20 93320 93720 93b20
  //   96328 96728 96b28 96f28 97328 97728 97b28 9a330 9a730 9ab30 9af30 9b330 9b730 9bb30 82380 82780
  //   82b80 82f80 83380 83780 83b80 86388 86788 86b88 86f88 87388 87788 87b88 8a390 8a790 8ab90 8af90
  //   8b390 8b790 8bb90 8e398 8e798 8eb98 8ef98 8f398 8f798 8fb98 923a0 927a0 92ba0 92fa0 933a0 937a0
  //   93ba0 963a8 967a8 96ba8 96fa8 973a8 977a8 97ba8 9a3b0 9a7b0 9abb0 9afb0 9b3b0 9b7b0 9bbb0 83c00
  //   87c08 8bc10 8fc18 93c20 97c28 9bc30 83c80 87c88 8bc90 8fc98 93ca0 97ca8 9bcb0 83d00 87d08 8bd10
  //   8fd18 93d20 97d28 9bd30 83d80 87d88 8bd90 8fd98 93da0 97da8 9bdb0 83e00 87e08 8be10 8fe18 93e20
  //   97e28 9be30 83f00 87f08 8bf10 8ff18 93f20 97f28 9bf30 83f80 87f88 8bf90 8ff98 93fa0 97fa8 9bfb0
  //   a6002 a640a a6812 a6c1a a7022 a742a a7832 7*400078 a6082 a648a a6892 a6c9a a70a2 a74aa a78b2
  //   7*400078 a6102 a650a a6912 a6d1a a7122 a752a a7932 7*400078 a6182 a658a a6992 a6d9a a71a2 a75aa
  //   a79b2 7*400078 a6202 a660a a6a12 a6e1a a7222 a762a a7a32 7*400078 a6302 a670a a6b12 a6f1a a7322
  //   a772a a7b32 7*400078 a6382 a678a a6b92 a6f9a a73a2 a77aa a7bb2 7*400078 afc50 82280 86288 8a290
  //   8e298 922a0 962a8 9a2b0 0 4000 8000 c000 10000 14000 18000 8 4008 8008 c008 10008 14008 18008 10
  //   4010 8010 c010 10010 14010 18010 18 4018 8018 c018 10018 14018 18018 20 4020 8020 c020 10020 14020
  //   18020 28 4028 8028 c028 10028 14028 18028 30 4030 8030 c030 10030 14030 18030 24002 2400a 24012
  //   2401a 24022 2402a 24032 7*400078 24052 400078 48 4048 8048 c048 10048 14048 18048 50 4050 8050 c050
  //   10050 14050 18050 7b 400078 1c048 1c050 1c000 1c008 1c010 1c018 1c020 1c028 1c030 20000 20008 20010
  //   20018 20020 20028 20030 40 4040 8040 c040 10040 14040 18040 1c040 820f8 824f8 828f8 82cf8 830f8
  //   834f8 838f8 860f8 864f8 868f8 86cf8 870f8 874f8 878f8 8a0f8 8a4f8 8a8f8 8acf8 8b0f8 8b4f8 8b8f8
  //   8e0f8 8e4f8 8e8f8 8ecf8 8f0f8 8f4f8 8f8f8 920f8 924f8 928f8 92cf8 930f8 934f8 938f8 960f8 964f8
  //   968f8 96cf8 970f8 974f8 978f8 9a0f8 9a4f8 9a8f8 9acf8 9b0f8 9b4f8 9b8f8 83cf8 87cf8 8bcf8 8fcf8
  //   93cf8 97cf8 9bcf8 2c038 38 4038 8038 c038 10038 14038 18038 7*78 38 4038 8038 c038 10038 14038 18038
  //   7*78 38 4038 8038 c038 10038 14038 18038 7*78 38 4038 8038 c038 10038 14038 18038 7*78 38 4038 8038
  //   c038 10038 14038 18038 7*78 38 4038 8038 c0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
endmodule

module registers (
  input  [15:0] reg_data_in,
  input  CLK,
  input  RESET,
  input  [15:0] write_reg_select,
  input  carry_flag,
  input  zero_flag,
  input  sign_flag,
  input  flag_write_sw,
  output [15:0] memval_out,
  output [15:0] memaddr_out,
  output [15:0] a_out,
  output [15:0] b_out,
  output [15:0] c_out,
  output [15:0] d_out,
  output [15:0] e_out,
  output [15:0] bp_out,
  output [15:0] sp_out,
  output [15:0] output_out,
  output [15:0] flag_output
);

  wire or_1_out;
  wire [15:0] multiplexer_1_out;

  Register #(.width(16)) MEMVAL (.D(reg_data_in), .en(write_reg_select[10]), .clk(CLK), .Q(memval_out), .clr(RESET));
  Register #(.width(16)) MEMADDR (.D(reg_data_in), .en(write_reg_select[9]), .clk(CLK), .Q(memaddr_out), .clr(RESET));
  Register #(.width(16)) A (.D(reg_data_in), .en(write_reg_select[0]), .clk(CLK), .Q(a_out), .clr(RESET));
  Register #(.width(16)) B (.D(reg_data_in), .en(write_reg_select[1]), .clk(CLK), .Q(b_out), .clr(RESET));
  Register #(.width(16)) C (.D(reg_data_in), .en(write_reg_select[2]), .clk(CLK), .Q(c_out), .clr(RESET));
  Register #(.width(16)) D (.D(reg_data_in), .en(write_reg_select[3]), .clk(CLK), .Q(d_out), .clr(RESET));
  Register #(.width(16)) E (.D(reg_data_in), .en(write_reg_select[4]), .clk(CLK), .Q(e_out), .clr(RESET));
  Register #(.width(16)) BP (.D(reg_data_in), .en(write_reg_select[5]), .clk(CLK), .Q(bp_out), .clr(RESET));
  Register #(.width(16)) SP (.D(reg_data_in), .en(write_reg_select[6]), .clk(CLK), .Q(sp_out), .clr(RESET));
  Register #(.width(16)) Output_port (
    .D(reg_data_in), .en(write_reg_select[8]), .clk(CLK), .Q(output_out), .clr(RESET));
  Multiplexer #(.width(16)) multiplexer_1 (
    .in0(reg_data_in), .in1({flag_output[15:3], sign_flag, zero_flag, carry_flag}), .out(multiplexer_1_out),
    .sel(flag_write_sw));
  or or_1 (or_1_out, write_reg_select[11], flag_write_sw);
  Register #(.width(16)) FLAGS (.D(multiplexer_1_out), .en(or_1_out), .clk(CLK), .Q(flag_output), .clr(RESET));
endmodule

module ALU (
  input  [15:0] in1_data_in,
  input  [15:0] in2_data_in,
  input  [2:0] ALU_function_select,
  output [15:0] ALU_Out,
  output sign_flag,
  output zero_flag,
  output carry_flag
);

  wire adder_1_cout, not_2_out, not_3_out, not_4_out, not_5_out, not_6_out, not_7_out, not_8_out, not_9_out,
       not_10_out, not_11_out, not_12_out, not_13_out, not_14_out, not_15_out, not_16_out, not_17_out,
       right_shifter_1_carry_out;
  wire [15:0] adder_1_out, and_1_out, demultiplexer_1_out0, demultiplexer_1_out1, demultiplexer_1_out2,
       demultiplexer_1_out3, demultiplexer_1_out4, demultiplexer_1_out5, demultiplexer_1_out6,
       demultiplexer_1_out7, demultiplexer_2_out0, demultiplexer_2_out1, demultiplexer_2_out2,
       demultiplexer_2_out3, demultiplexer_2_out4, demultiplexer_2_out6, demultiplexer_2_out7,
       multiplier_1_cout, multiplier_1_out, not_1_out, or_1_out, right_shifter_1_output_bus_1,
       subtractor_1_out, xor_1_out;

  Demultiplexer #(.select(3), .width(16)) demultiplexer_1 (
    .out0(demultiplexer_1_out0), .out1(demultiplexer_1_out1), .out2(demultiplexer_1_out2),
    .out3(demultiplexer_1_out3), .out4(demultiplexer_1_out4), .out5(demultiplexer_1_out5),
    .out6(demultiplexer_1_out6), .out7(demultiplexer_1_out7), .in(in1_data_in), .sel(ALU_function_select));
  Demultiplexer #(.select(3), .width(16)) demultiplexer_2 (
    .out0(demultiplexer_2_out0), .out1(demultiplexer_2_out1), .out2(demultiplexer_2_out2),
    .out3(demultiplexer_2_out3), .out4(demultiplexer_2_out4), .out6(demultiplexer_2_out6),
    .out7(demultiplexer_2_out7), .in(in2_data_in), .sel(ALU_function_select));  // open: out5
  Adder #(.width(16)) adder_1 (
    .a(demultiplexer_1_out0), .b(demultiplexer_2_out0), .out(adder_1_out), .cin(1'b0), .cout(adder_1_cout));
  Subtractor #(.width(16)) subtractor_1 (
    .a(demultiplexer_1_out1), .b(demultiplexer_2_out1), .out(subtractor_1_out), .bin(1'b0), .bout(sign_flag));
  Multiplier #(.width(16)) multiplier_1 (
    .a(demultiplexer_1_out2), .b(demultiplexer_2_out2), .out(multiplier_1_out), .cin({16{1'b0}}),
    .cout(multiplier_1_cout));
  assign and_1_out = demultiplexer_1_out3 & demultiplexer_2_out3;  // AND_Gate and_1, 16 bits wide
  assign or_1_out = demultiplexer_1_out4 | demultiplexer_2_out4;  // OR_Gate or_1, 16 bits wide
  assign not_1_out = ~demultiplexer_1_out5;  // NOT_Gate not_1, 16 bits wide
  assign xor_1_out = demultiplexer_1_out6 ^ demultiplexer_2_out6;  // XOR_Gate xor_1, 16 bits wide
  right_shifter right_shifter_1 (
    .Input_bus_1(demultiplexer_2_out7), .Input_bus_2(demultiplexer_1_out7),
    .carry_out(right_shifter_1_carry_out), .Output_bus_1(right_shifter_1_output_bus_1));
  Multiplexer #(.select(3), .width(16)) multiplexer_1 (
    .in0(adder_1_out), .in1(subtractor_1_out), .in2(multiplier_1_out), .in3(and_1_out), .in4(or_1_out),
    .in5(not_1_out), .in6(xor_1_out), .in7(right_shifter_1_output_bus_1), .out(ALU_Out),
    .sel(ALU_function_select));
  or or_2 (carry_flag, adder_1_cout, multiplier_1_cout[7], multiplier_1_cout[0], multiplier_1_cout[1], multiplier_1_cout[2], multiplier_1_cout[3], multiplier_1_cout[4], multiplier_1_cout[5], multiplier_1_cout[6], multiplier_1_cout[8], multiplier_1_cout[9], multiplier_1_cout[10], multiplier_1_cout[11], multiplier_1_cout[12], multiplier_1_cout[13], multiplier_1_cout[14], multiplier_1_cout[15], right_shifter_1_carry_out);
  not not_2 (not_2_out, ALU_Out[0]);
  not not_3 (not_3_out, ALU_Out[1]);
  not not_4 (not_4_out, ALU_Out[2]);
  not not_5 (not_5_out, ALU_Out[3]);
  not not_6 (not_6_out, ALU_Out[4]);
  not not_7 (not_7_out, ALU_Out[5]);
  not not_8 (not_8_out, ALU_Out[6]);
  not not_9 (not_9_out, ALU_Out[7]);
  not not_10 (not_10_out, ALU_Out[8]);
  not not_11 (not_11_out, ALU_Out[9]);
  not not_12 (not_12_out, ALU_Out[10]);
  not not_13 (not_13_out, ALU_Out[11]);
  not not_14 (not_14_out, ALU_Out[12]);
  not not_15 (not_15_out, ALU_Out[13]);
  not not_16 (not_16_out, ALU_Out[14]);
  not not_17 (not_17_out, ALU_Out[15]);
  and and_2 (zero_flag, not_9_out, not_2_out, not_3_out, not_4_out, not_5_out, not_6_out, not_7_out, not_8_out, not_10_out, not_11_out, not_12_out, not_13_out, not_14_out, not_15_out, not_16_out, not_17_out);
endmodule

module sixteen_register (
  input  S,
  input  CLK,
  input  [15:0] D,
  input  WE,
  output [15:0] Q
);

  wire [15:0] multiplexer_1_out;

  Multiplexer #(.width(16)) multiplexer_1 (.in0(Q), .in1(D), .out(multiplexer_1_out), .sel(WE));
  D_Flip_Flop d_ff_1 (.D(multiplexer_1_out[0]), .clk(CLK), .Q(Q[0]), .preset(S));  // open: Qn, reset
  D_Flip_Flop d_ff_2 (.D(multiplexer_1_out[1]), .clk(CLK), .Q(Q[1]), .preset(S));  // open: Qn, reset
  D_Flip_Flop d_ff_3 (.D(multiplexer_1_out[2]), .clk(CLK), .Q(Q[2]), .preset(S));  // open: Qn, reset
  D_Flip_Flop d_ff_4 (.D(multiplexer_1_out[3]), .clk(CLK), .Q(Q[3]), .preset(S));  // open: Qn, reset
  D_Flip_Flop d_ff_5 (.D(multiplexer_1_out[4]), .clk(CLK), .Q(Q[4]), .preset(S));  // open: Qn, reset
  D_Flip_Flop d_ff_6 (.D(multiplexer_1_out[5]), .clk(CLK), .Q(Q[5]), .preset(S));  // open: Qn, reset
  D_Flip_Flop d_ff_7 (.D(multiplexer_1_out[6]), .clk(CLK), .Q(Q[6]), .preset(S));  // open: Qn, reset
  D_Flip_Flop d_ff_8 (.D(multiplexer_1_out[7]), .clk(CLK), .Q(Q[7]), .preset(S));  // open: Qn, reset
  D_Flip_Flop d_ff_9 (.D(multiplexer_1_out[8]), .clk(CLK), .Q(Q[8]), .preset(S));  // open: Qn, reset
  D_Flip_Flop d_ff_10 (.D(multiplexer_1_out[9]), .clk(CLK), .Q(Q[9]), .preset(S));  // open: Qn, reset
  D_Flip_Flop d_ff_11 (.D(multiplexer_1_out[10]), .clk(CLK), .Q(Q[10]), .preset(S));  // open: Qn, reset
  D_Flip_Flop d_ff_12 (.D(multiplexer_1_out[11]), .clk(CLK), .Q(Q[11]), .preset(S));  // open: Qn, reset
  D_Flip_Flop d_ff_13 (.D(multiplexer_1_out[12]), .clk(CLK), .Q(Q[12]), .preset(S));  // open: Qn, reset
  D_Flip_Flop d_ff_14 (.D(multiplexer_1_out[13]), .clk(CLK), .Q(Q[13]), .preset(S));  // open: Qn, reset
  D_Flip_Flop d_ff_15 (.D(multiplexer_1_out[14]), .clk(CLK), .Q(Q[14]), .preset(S));  // open: Qn, reset
  D_Flip_Flop d_ff_16 (.D(multiplexer_1_out[15]), .clk(CLK), .Q(Q[15]), .preset(S));  // open: Qn, reset
endmodule
